// Digital circuit ALU Adder.dig as structural Verilog
// Four 4-bit adders with carry look-ahead chained to make 16-bit adder
module ALU_Adder (
  input  [15:0] A,
  input  [15:0] B,
  input  C_in,
  output [15:0] S,
  output E,
  output C_out
);

  wire _8b_fa_board_1_c_out;

  _8b_FA_board _8b_fa_board_1 (
    .C_in(C_in), .A(A[7:0]), .B(B[7:0]), .S(S[7:0]), .C_out(_8b_fa_board_1_c_out));  // open: C3_of
  _8b_FA_board _8b_fa_board_2 (
    .C_in(_8b_fa_board_1_c_out), .A(A[15:8]), .B(B[15:8]), .S(S[15:8]), .C_out(C_out), .C3_of(E));

  // Notes on the sheet:
  //   E: Overflow
  //   16 bit Fast adder
endmodule
