// Digital circuit Barrel Rotator.dig as structural Verilog
module Barrel_Rotator (
  input  [15:0] D_in,
  input  [3:0] shift,
  output [15:0] Output
);

  wire _74157_1_pin4, _74157_1_pin7, _74157_1_pin9, _74157_1_pin12, _74157_2_pin3, _74157_2_pin4,
       _74157_2_pin6, _74157_2_pin7, _74157_2_pin9, _74157_2_pin12, _74157_3_pin3, _74157_3_pin4,
       _74157_3_pin6, _74157_3_pin7, _74157_3_pin9, _74157_3_pin10, _74157_3_pin12, _74157_3_pin13,
       _74157_4_pin3, _74157_4_pin6, _74157_4_pin10, _74157_4_pin13, _74157_5_pin4, _74157_5_pin7,
       _74157_5_pin9, _74157_5_pin12, _74157_6_pin4, _74157_6_pin7, _74157_6_pin9, _74157_6_pin12,
       _74157_7_pin4, _74157_7_pin7, _74157_7_pin9, _74157_7_pin12, _74157_8_pin3, _74157_8_pin6,
       _74157_8_pin10, _74157_8_pin13, _74157_9_pin4, _74157_9_pin7, _74157_9_pin9, _74157_9_pin12,
       _74157_10_pin4, _74157_10_pin7, _74157_10_pin9, _74157_10_pin12, _74157_13_pin4, _74157_13_pin7;

  _74157 _74157_1 (
    .pin1(shift[0]), .pin2(D_in[0]), .pin3(D_in[15]), .pin4(_74157_1_pin4), .pin5(D_in[1]), .pin6(D_in[0]),
    .pin7(_74157_1_pin7), .pin8(1'b0), .pin9(_74157_1_pin9), .pin10(D_in[2]), .pin11(D_in[3]),
    .pin12(_74157_1_pin12), .pin13(D_in[1]), .pin14(D_in[2]), .pin15(1'b0), .pin16(1'b1));
  _74157 _74157_2 (
    .pin1(shift[1]), .pin2(_74157_1_pin4), .pin3(_74157_2_pin3), .pin4(_74157_2_pin4), .pin5(_74157_1_pin7),
    .pin6(_74157_2_pin6), .pin7(_74157_2_pin7), .pin8(1'b0), .pin9(_74157_2_pin9), .pin10(_74157_1_pin7),
    .pin11(_74157_1_pin9), .pin12(_74157_2_pin12), .pin13(_74157_1_pin4), .pin14(_74157_1_pin12),
    .pin15(1'b0), .pin16(1'b1));
  _74157 _74157_3 (
    .pin1(shift[2]), .pin2(_74157_2_pin4), .pin3(_74157_3_pin3), .pin4(_74157_3_pin4), .pin5(_74157_2_pin7),
    .pin6(_74157_3_pin6), .pin7(_74157_3_pin7), .pin8(1'b0), .pin9(_74157_3_pin9), .pin10(_74157_3_pin10),
    .pin11(_74157_2_pin9), .pin12(_74157_3_pin12), .pin13(_74157_3_pin13), .pin14(_74157_2_pin12),
    .pin15(1'b0), .pin16(1'b1));
  _74157 _74157_4 (
    .pin1(shift[3]), .pin2(_74157_3_pin4), .pin3(_74157_4_pin3), .pin4(Output[0]), .pin5(_74157_3_pin7),
    .pin6(_74157_4_pin6), .pin7(Output[1]), .pin8(1'b0), .pin9(Output[3]), .pin10(_74157_4_pin10),
    .pin11(_74157_3_pin9), .pin12(Output[2]), .pin13(_74157_4_pin13), .pin14(_74157_3_pin12), .pin15(1'b0),
    .pin16(1'b1));
  _74157 _74157_5 (
    .pin1(shift[0]), .pin2(D_in[4]), .pin3(D_in[3]), .pin4(_74157_5_pin4), .pin5(D_in[5]), .pin6(D_in[4]),
    .pin7(_74157_5_pin7), .pin8(1'b0), .pin9(_74157_5_pin9), .pin10(D_in[6]), .pin11(D_in[7]),
    .pin12(_74157_5_pin12), .pin13(D_in[5]), .pin14(D_in[6]), .pin15(1'b0), .pin16(1'b1));
  _74157 _74157_6 (
    .pin1(shift[1]), .pin2(_74157_5_pin4), .pin3(_74157_1_pin12), .pin4(_74157_6_pin4), .pin5(_74157_5_pin7),
    .pin6(_74157_1_pin9), .pin7(_74157_6_pin7), .pin8(1'b0), .pin9(_74157_6_pin9), .pin10(_74157_5_pin7),
    .pin11(_74157_5_pin9), .pin12(_74157_6_pin12), .pin13(_74157_5_pin4), .pin14(_74157_5_pin12),
    .pin15(1'b0), .pin16(1'b1));
  _74157 _74157_7 (
    .pin1(shift[2]), .pin2(_74157_6_pin4), .pin3(_74157_2_pin4), .pin4(_74157_7_pin4), .pin5(_74157_6_pin7),
    .pin6(_74157_2_pin7), .pin7(_74157_7_pin7), .pin8(1'b0), .pin9(_74157_7_pin9), .pin10(_74157_2_pin9),
    .pin11(_74157_6_pin9), .pin12(_74157_7_pin12), .pin13(_74157_2_pin12), .pin14(_74157_6_pin12),
    .pin15(1'b0), .pin16(1'b1));
  _74157 _74157_8 (
    .pin1(shift[3]), .pin2(_74157_7_pin4), .pin3(_74157_8_pin3), .pin4(Output[4]), .pin5(_74157_7_pin7),
    .pin6(_74157_8_pin6), .pin7(Output[5]), .pin8(1'b0), .pin9(Output[7]), .pin10(_74157_8_pin10),
    .pin11(_74157_7_pin9), .pin12(Output[6]), .pin13(_74157_8_pin13), .pin14(_74157_7_pin12), .pin15(1'b0),
    .pin16(1'b1));
  LED led_1 (.in(Output[15]));
  _74157 _74157_9 (
    .pin1(shift[0]), .pin2(D_in[8]), .pin3(D_in[7]), .pin4(_74157_9_pin4), .pin5(D_in[9]), .pin6(D_in[8]),
    .pin7(_74157_9_pin7), .pin8(1'b0), .pin9(_74157_9_pin9), .pin10(D_in[10]), .pin11(D_in[11]),
    .pin12(_74157_9_pin12), .pin13(D_in[9]), .pin14(D_in[10]), .pin15(1'b0), .pin16(1'b1));
  _74157 _74157_10 (
    .pin1(shift[1]), .pin2(_74157_9_pin4), .pin3(_74157_5_pin12), .pin4(_74157_10_pin4),
    .pin5(_74157_9_pin7), .pin6(_74157_5_pin9), .pin7(_74157_10_pin7), .pin8(1'b0), .pin9(_74157_10_pin9),
    .pin10(_74157_9_pin7), .pin11(_74157_9_pin9), .pin12(_74157_10_pin12), .pin13(_74157_9_pin4),
    .pin14(_74157_9_pin12), .pin15(1'b0), .pin16(1'b1));
  _74157 _74157_11 (
    .pin1(shift[2]), .pin2(_74157_10_pin4), .pin3(_74157_6_pin4), .pin4(_74157_4_pin3),
    .pin5(_74157_10_pin7), .pin6(_74157_6_pin7), .pin7(_74157_4_pin6), .pin8(1'b0), .pin9(_74157_4_pin10),
    .pin10(_74157_6_pin9), .pin11(_74157_10_pin9), .pin12(_74157_4_pin13), .pin13(_74157_6_pin12),
    .pin14(_74157_10_pin12), .pin15(1'b0), .pin16(1'b1));
  _74157 _74157_12 (
    .pin1(shift[3]), .pin2(_74157_4_pin3), .pin3(_74157_3_pin4), .pin4(Output[8]), .pin5(_74157_4_pin6),
    .pin6(_74157_3_pin7), .pin7(Output[9]), .pin8(1'b0), .pin9(Output[11]), .pin10(_74157_3_pin9),
    .pin11(_74157_4_pin10), .pin12(Output[10]), .pin13(_74157_3_pin12), .pin14(_74157_4_pin13), .pin15(1'b0),
    .pin16(1'b1));
  LED led_2 (.in(Output[14]));
  LED led_3 (.in(Output[13]));
  LED led_4 (.in(Output[12]));
  LED led_5 (.in(Output[11]));
  LED led_6 (.in(Output[10]));
  LED led_7 (.in(Output[9]));
  LED led_8 (.in(Output[8]));
  LED led_9 (.in(Output[7]));
  LED led_10 (.in(Output[6]));
  LED led_11 (.in(Output[5]));
  LED led_12 (.in(Output[4]));
  LED led_13 (.in(Output[3]));
  _74157 _74157_13 (
    .pin1(shift[0]), .pin2(D_in[12]), .pin3(D_in[11]), .pin4(_74157_13_pin4), .pin5(D_in[13]),
    .pin6(D_in[12]), .pin7(_74157_13_pin7), .pin8(1'b0), .pin9(_74157_2_pin6), .pin10(D_in[14]),
    .pin11(D_in[15]), .pin12(_74157_2_pin3), .pin13(D_in[13]), .pin14(D_in[14]), .pin15(1'b0), .pin16(1'b1));
  _74157 _74157_14 (
    .pin1(shift[1]), .pin2(_74157_13_pin4), .pin3(_74157_9_pin12), .pin4(_74157_3_pin3),
    .pin5(_74157_13_pin7), .pin6(_74157_9_pin9), .pin7(_74157_3_pin6), .pin8(1'b0), .pin9(_74157_3_pin10),
    .pin10(_74157_13_pin7), .pin11(_74157_2_pin6), .pin12(_74157_3_pin13), .pin13(_74157_13_pin4),
    .pin14(_74157_2_pin3), .pin15(1'b0), .pin16(1'b1));
  _74157 _74157_15 (
    .pin1(shift[2]), .pin2(_74157_3_pin3), .pin3(_74157_10_pin4), .pin4(_74157_8_pin3), .pin5(_74157_3_pin6),
    .pin6(_74157_10_pin7), .pin7(_74157_8_pin6), .pin8(1'b0), .pin9(_74157_8_pin10), .pin10(_74157_10_pin9),
    .pin11(_74157_3_pin10), .pin12(_74157_8_pin13), .pin13(_74157_10_pin12), .pin14(_74157_3_pin13),
    .pin15(1'b0), .pin16(1'b1));
  _74157 _74157_16 (
    .pin1(shift[3]), .pin2(_74157_8_pin3), .pin3(_74157_7_pin4), .pin4(Output[12]), .pin5(_74157_8_pin6),
    .pin6(_74157_7_pin7), .pin7(Output[13]), .pin8(1'b0), .pin9(Output[15]), .pin10(_74157_7_pin9),
    .pin11(_74157_8_pin10), .pin12(Output[14]), .pin13(_74157_7_pin12), .pin14(_74157_8_pin13), .pin15(1'b0),
    .pin16(1'b1));
  LED led_14 (.in(Output[2]));
  LED led_15 (.in(Output[1]));
  LED led_16 (.in(Output[0]));

  // Notes on the sheet:
  //   D_in: Data Input
  //   shift: Number of bits to be shifted
  //   0
  //   1
  //   2
  //   3
  //   barrel
  //   4
  //   5
  //   6
  //   7
  //   8
  //   9
  //   A
  //   B
  //   C
  //   D
  //   E
  //   F
endmodule
