// Digital circuit Byte Sign Extender.dig as structural Verilog
// Byte sign extender -- copies bit 7 to all higher bits
module Byte_Sign_Extender (
  input  [15:0] in,
  output [15:0] out
);

  _1_to_8b_extender _1_to_8b_extender_1 (.in(in[7]), .out(out[15:8]));

  assign out[7:0] = in[7:0];
endmodule
