// Digital circuit Incrementor.dig as structural Verilog
module Incrementor (
  input  [7:0] Const,
  input  [15:0] B_in,
  input  Sel,
  output [15:0] B_out
);

  _74157 _74157_1 (
    .pin1(Sel), .pin2(B_in[0]), .pin3(Const[0]), .pin4(B_out[0]), .pin5(B_in[1]), .pin6(Const[1]),
    .pin7(B_out[1]), .pin8(1'b0), .pin9(B_out[3]), .pin10(Const[3]), .pin11(B_in[3]), .pin12(B_out[2]),
    .pin13(Const[2]), .pin14(B_in[2]), .pin15(1'b0), .pin16(1'b1));
  _74157 _74157_2 (
    .pin1(Sel), .pin2(B_in[4]), .pin3(Const[4]), .pin4(B_out[4]), .pin5(B_in[5]), .pin6(Const[5]),
    .pin7(B_out[5]), .pin8(1'b0), .pin9(B_out[7]), .pin10(Const[7]), .pin11(B_in[7]), .pin12(B_out[6]),
    .pin13(Const[6]), .pin14(B_in[6]), .pin15(1'b0), .pin16(1'b1));
  _74157 _74157_3 (
    .pin1(Sel), .pin2(B_in[8]), .pin3(1'b0), .pin4(B_out[8]), .pin5(B_in[9]), .pin6(1'b0), .pin7(B_out[9]),
    .pin8(1'b0), .pin9(B_out[11]), .pin10(1'b0), .pin11(B_in[11]), .pin12(B_out[10]), .pin13(1'b0),
    .pin14(B_in[10]), .pin15(1'b0), .pin16(1'b1));
  _74157 _74157_4 (
    .pin1(Sel), .pin2(B_in[12]), .pin3(1'b0), .pin4(B_out[12]), .pin5(B_in[13]), .pin6(1'b0),
    .pin7(B_out[13]), .pin8(1'b0), .pin9(B_out[15]), .pin10(1'b0), .pin11(B_in[15]), .pin12(B_out[14]),
    .pin13(1'b0), .pin14(B_in[14]), .pin15(1'b0), .pin16(1'b1));

  // Notes on the sheet:
  //   Sel: Selects value for B
  //   0	B from register [0-65535]
  //   1	B from instruction [0-255]
  //   Incrementor
  //   "A"
  //   "B"
endmodule
