// Digital circuit Main ALU no indicators.dig as structural Verilog
module Main_ALU_no_indicators (
  input  [15:0] Src1,
  input  [15:0] Src2,
  input  [7:0] Const,
  input  Carry_in,
  input  Enable_C_in_RotC,
  input  Sub_Inv_Rev,
  input  [2:0] Function,
  input  Const_enable,
  input  Arithm,
  input  ALU_enable,
  output [15:0] Output,
  output C,
  output O,
  output N,
  output Z,
  output [15:0] B_in,
  output [15:0] Sum
);

  wire _7400_1_pin3, _7400_1_pin5, _7400_1_pin6, _7400_1_pin8, _7400_1_pin10, _7400_1_pin11, _7400_1_pin12,
       _7400_1_pin13, _7400_2_pin3, _7400_2_pin6, _7400_2_pin10, _7404_1_pin10, _7404_1_pin12,
       alu_adder_1_c_out, alu_adder_1_e, negator_1_c_in_to_adder, negator_1_c_out, not_1_out,
       shifter_1_c_out, zero_detector_1_z;
  wire [3:0] multiplexer_1_out;
  wire [15:0] barrel_rotator_1_output, byte_sign_extender_1_out, incrementor_1_b_out, logic_operations_1_and,
       logic_operations_1_not, logic_operations_1_or, logic_operations_1_xor, out, shifter_1_d_out;

  _7400 _7400_1 (
    .pin1(Carry_in), .pin2(Enable_C_in_RotC), .pin3(_7400_1_pin3), .pin4(Enable_C_in_RotC),
    .pin5(_7400_1_pin5), .pin6(_7400_1_pin6), .pin7(1'b0), .pin8(_7400_1_pin8), .pin9(Function[0]),
    .pin10(_7400_1_pin10), .pin11(_7400_1_pin11), .pin12(_7400_1_pin12), .pin13(_7400_1_pin13), .pin14(1'b1));
  Multiplexer #(.Bits(4)) multiplexer_1 (
    .sel(Sub_Inv_Rev), .in_0(Src2[3:0]), .in_1(Const[3:0]), .out(multiplexer_1_out));
  Incrementor incrementor_1 (.B_in(Src2), .Const(Const), .Sel(Const_enable), .B_out(incrementor_1_b_out));
  _7404 _7404_1 (
    .pin1(Function[1]), .pin2(_7400_1_pin13), .pin3(Function[2]), .pin4(_7400_1_pin12), .pin5(_7400_1_pin11),
    .pin6(_7400_1_pin10), .pin7(1'b0), .pin8(_7400_1_pin5), .pin9(_7400_1_pin8), .pin10(_7404_1_pin10),
    .pin11(_7400_1_pin6), .pin12(_7404_1_pin12), .pin13(_7400_1_pin3), .pin14(1'b1));
  Negator negator_1 (
    .In(incrementor_1_b_out), .C_in(_7404_1_pin12), .N(Sub_Inv_Rev), .C_from_Adder(alu_adder_1_c_out),
    .E_from_Adder(alu_adder_1_e), .Out(B_in), .C_in_to_Adder(negator_1_c_in_to_adder), .Overflow(O),
    .C_out(negator_1_c_out));
  Byte_Sign_Extender byte_sign_extender_1 (.in(Src1), .out(byte_sign_extender_1_out));
  ALU_Adder alu_adder_1 (
    .A(Src1), .B(B_in), .C_in(negator_1_c_in_to_adder), .C_out(alu_adder_1_c_out), .E(alu_adder_1_e),
    .S({N, Sum[14:0]}));
  Shifter shifter_1 (
    .D_in(Src1), .L_R(Sub_Inv_Rev), .A(Arithm), .C_in(_7404_1_pin12), .sh_RC(_7404_1_pin10),
    .D_out(shifter_1_d_out), .C_out(shifter_1_c_out));
  Barrel_Rotator barrel_rotator_1 (.D_in(Src1), .shift(multiplexer_1_out), .Output(barrel_rotator_1_output));
  Logic_Operations logic_operations_1 (
    .Xor(logic_operations_1_xor), .Or(logic_operations_1_or), .And(logic_operations_1_and),
    .Not(logic_operations_1_not), .A(Src1), .B(B_in));
  not not_1 (not_1_out, ALU_enable);
  _7400 _7400_2 (
    .pin1(_7404_1_pin10), .pin2(_7404_1_pin10), .pin3(_7400_2_pin3), .pin4(_7404_1_pin10),
    .pin5(shifter_1_c_out), .pin6(_7400_2_pin6), .pin7(1'b0), .pin8(C), .pin9(_7400_2_pin6),
    .pin10(_7400_2_pin10), .pin11(_7400_2_pin10), .pin12(_7400_2_pin3), .pin13(negator_1_c_out), .pin14(1'b1));
  Function_selector function_selector_1 (
    .BSE(byte_sign_extender_1_out), .Shift(shifter_1_d_out), .Rotate(barrel_rotator_1_output),
    .Invert(logic_operations_1_not), .Add({N, Sum[14:0]}), .XOR(logic_operations_1_xor),
    .OR(logic_operations_1_or), .AND(logic_operations_1_and), .Function(Function), .Output(out));
  Zero_Detector zero_detector_1 (.D_in(out), .Z(zero_detector_1_z));
  Bus_buffer E2_buffer (.nEnable(not_1_out), .Data_in(out), .Data_out(Output));
  not not_2 (Z, zero_detector_1_z);

  assign Sum[15] = N;

  // Other names for the same wires on the sheet: Ar = Arithm; Carry_en_RotC = Enable_C_in_RotC;
  //   Const_en = Const_enable

  // Notes on the sheet:
  //   Src1: Source register pointed by bits 5,6,7 of inctruction,
  //    or by bits 8,9,A when it is op with constant
  //   Src2: Source register pointed by bits 0,1,2 of inctruction
  //   Const: 8-bit constant value, sourced from instruction register
  //   Carry_in: Carry in
  //   Sub_Inv_Rev: Inverts Src2 and helps with subtraction, reverses shift
  //   Function: Chooses one of 8 possible operation types
  //   Const_enable: Switch to using constant instead of Src2
  //   Arithm: Sets arithmetic shift
  //   C: Carry out
  //   O: Overflow
  //   N: Negative sign
  //   Z: Output is zero
  //   ALU_enable: ALU operation
  //   B_in: ALU B input
  //   Sum: raw ALU output
  //   Controls:
  //   Operands:
  //   Main ALU
  //   Overflow
  //   Negative
  //   4 NAND gates as 2-to-1 Multiplexer
  //   C_out
  //   Zero
endmodule
