// Digital circuit Main ALU.dig as structural Verilog
module Main_ALU (
  input  [15:0] Src1,
  input  [15:0] Src2,
  input  [7:0] Const,
  input  Carry_in,
  input  Enable_C_in_RotC,
  input  Sub_Inv_Rev,
  input  [2:0] Function,
  input  Const_enable,
  input  Arithm,
  input  ALU_enable,
  output [15:0] Output,
  output C,
  output O,
  output N,
  output Z,
  output [15:0] B_in,
  output [15:0] Sum
);

  wire _7400_1_pin3, _7400_1_pin5, _7400_1_pin6, _7400_1_pin8, _7400_1_pin10, _7400_1_pin11, _7400_1_pin12,
       _7400_1_pin13, _7400_2_pin3, _7400_2_pin6, _7400_2_pin10, _7404_1_pin6, _7404_1_pin12, _7404_2_pin10,
       _7404_2_pin12, _7408_1_pin3, _7408_1_pin6, _7408_1_pin8, _7408_1_pin9, _7408_1_pin10, _7408_1_pin11,
       _7408_2_pin3, _7408_2_pin6, _7408_2_pin8, _7408_2_pin11, _74238_1_pin7, _74238_1_pin9, _74238_1_pin10,
       _74238_1_pin11, _74238_1_pin12, _74238_1_pin13, _74238_1_pin14, _74238_1_pin15, alu_adder_1_c_out,
       alu_adder_1_e, and_2_out, and_3_out, nE2, negator_1_c_in_to_adder, negator_1_c_out, or_1_out,
       shifter_1_c_out, zero_detector_1_z;
  wire [3:0] driver_4_out, driver_5_out, multiplexer_1_out, pulldown_2_out;
  wire [11:0] pulldown_1_out;
  wire [15:0] barrel_rotator_1_output, byte_sign_extender_1_out, driver_3_out, incrementor_1_b_out,
       logic_operations_1_and, logic_operations_1_not, logic_operations_1_or, logic_operations_1_xor, out,
       pulldown_6_out, shifter_1_d_out;

  _74238 _74238_1 (
    .pin1(Function[0]), .pin2(Function[1]), .pin3(Function[2]), .pin4(1'b0), .pin5(1'b0), .pin6(ALU_enable),
    .pin7(_74238_1_pin7), .pin8(1'b0), .pin9(_74238_1_pin9), .pin10(_74238_1_pin10), .pin11(_74238_1_pin11),
    .pin12(_74238_1_pin12), .pin13(_74238_1_pin13), .pin14(_74238_1_pin14), .pin15(_74238_1_pin15),
    .pin16(1'b1));
  or or_1 (or_1_out, _74238_1_pin13, Function[2]);
  _7408 _7408_1 (
    .pin1(_74238_1_pin13), .pin2(Sub_Inv_Rev), .pin3(_7408_1_pin3), .pin4(Sub_Inv_Rev), .pin5(Function[2]),
    .pin6(_7408_1_pin6), .pin7(1'b0), .pin8(_7408_1_pin8), .pin9(_7408_1_pin9), .pin10(_7408_1_pin10),
    .pin11(_7408_1_pin11), .pin12(_7408_1_pin8), .pin13(or_1_out), .pin14(1'b1));
  LED BSE (.in(_74238_1_pin15));
  LED SHL (.in(_74238_1_pin14));
  LED ROT (.in(_74238_1_pin13));
  LED INV (.in(_74238_1_pin12));
  LED ADD (.in(_74238_1_pin11));
  LED XOR (.in(_74238_1_pin10));
  LED OR_2 (.in(_74238_1_pin9));
  LED AND (.in(_74238_1_pin7));
  _7400 _7400_1 (
    .pin1(Carry_in), .pin2(Enable_C_in_RotC), .pin3(_7400_1_pin3), .pin4(Enable_C_in_RotC),
    .pin5(_7400_1_pin5), .pin6(_7400_1_pin6), .pin7(1'b0), .pin8(_7400_1_pin8), .pin9(Function[0]),
    .pin10(_7400_1_pin10), .pin11(_7400_1_pin11), .pin12(_7400_1_pin12), .pin13(_7400_1_pin13), .pin14(1'b1));
  _7408 _7408_2 (
    .pin1(_74238_1_pin14), .pin2(Sub_Inv_Rev), .pin3(_7408_2_pin3), .pin4(_74238_1_pin14), .pin5(Arithm),
    .pin6(_7408_2_pin6), .pin7(1'b0), .pin8(_7408_2_pin8), .pin9(_74238_1_pin11), .pin10(Enable_C_in_RotC),
    .pin11(_7408_2_pin11), .pin12(Enable_C_in_RotC), .pin13(_74238_1_pin14), .pin14(1'b1));
  LED Rev (.in(_7408_2_pin3));
  LED Ar (.in(_7408_2_pin6));
  _7404 _7404_1 (
    .pin1(Const_enable), .pin2(_7408_1_pin10), .pin3(_7408_1_pin3), .pin4(_7408_1_pin9), .pin5(_7408_1_pin8),
    .pin6(_7404_1_pin6), .pin7(1'b0), .pin9(1'b0), .pin10(nE2), .pin11(ALU_enable), .pin12(_7404_1_pin12),
    .pin13(_74238_1_pin13), .pin14(1'b1));  // open: pin8
  Multiplexer #(.Bits(4)) multiplexer_1 (
    .sel(Sub_Inv_Rev), .in_0(Src2[3:0]), .in_1(Const[3:0]), .out(multiplexer_1_out));
  Incrementor incrementor_1 (.B_in(Src2), .Const(Const), .Sel(Const_enable), .B_out(incrementor_1_b_out));
  _7404 _7404_2 (
    .pin1(Function[1]), .pin2(_7400_1_pin13), .pin3(Function[2]), .pin4(_7400_1_pin12), .pin5(_7400_1_pin11),
    .pin6(_7400_1_pin10), .pin7(1'b0), .pin8(_7400_1_pin5), .pin9(_7400_1_pin8), .pin10(_7404_2_pin10),
    .pin11(_7400_1_pin6), .pin12(_7404_2_pin12), .pin13(_7400_1_pin3), .pin14(1'b1));
  LED RotC (.in(_7408_2_pin11));
  LED ADDC (.in(_7408_2_pin8));
  Negator negator_1 (
    .In(incrementor_1_b_out), .C_in(_7404_2_pin12), .N(Sub_Inv_Rev), .C_from_Adder(alu_adder_1_c_out),
    .E_from_Adder(alu_adder_1_e), .Out(B_in), .C_in_to_Adder(negator_1_c_in_to_adder), .Overflow(O),
    .C_out(negator_1_c_out));
  LED led_1 (.in(out[15]));
  LED led_2 (.in(out[14]));
  LED led_3 (.in(out[13]));
  and and_2 (and_2_out, _7408_1_pin11, _7404_1_pin12);
  and and_3 (and_3_out, _7404_1_pin6, _7404_1_pin12);
  Byte_Sign_Extender byte_sign_extender_1 (.in(Src1), .out(byte_sign_extender_1_out));
  ALU_Adder alu_adder_1 (
    .A(Src1), .B(B_in), .C_in(negator_1_c_in_to_adder), .C_out(alu_adder_1_c_out), .E(alu_adder_1_e),
    .S({N, Sum[14:0]}));
  Shifter shifter_1 (
    .D_in(Src1), .L_R(Sub_Inv_Rev), .A(Arithm), .C_in(_7404_2_pin12), .sh_RC(_7404_2_pin10),
    .D_out(shifter_1_d_out), .C_out(shifter_1_c_out));
  Barrel_Rotator barrel_rotator_1 (.D_in(Src1), .shift(multiplexer_1_out), .Output(barrel_rotator_1_output));
  Logic_Operations logic_operations_1 (
    .Xor(logic_operations_1_xor), .Or(logic_operations_1_or), .And(logic_operations_1_and),
    .Not(logic_operations_1_not), .A(Src1), .B(B_in));
  LED led_4 (.in(out[12]));
  LED led_5 (.in(out[11]));
  PullDown #(.Bits(12)) pulldown_1 (.out(pulldown_1_out));
  LED led_6 (.in(out[10]));
  LED led_7 (.in(out[9]));
  LED led_8 (.in(driver_3_out[15]));
  LED led_9 (.in(driver_3_out[14]));
  LED led_10 (.in(pulldown_1_out[11]));
  LED led_11 (.in(pulldown_1_out[10]));
  LED led_12 (.in(pulldown_6_out[15]));
  LED led_13 (.in(pulldown_6_out[14]));
  LED led_14 (.in(out[8]));
  LED led_15 (.in(out[7]));
  LED led_16 (.in(driver_3_out[13]));
  LED led_17 (.in(driver_3_out[12]));
  LED led_18 (.in(pulldown_1_out[9]));
  LED led_19 (.in(pulldown_1_out[8]));
  LED SUB (.in(_7408_1_pin6));
  LED led_20 (.in(pulldown_6_out[13]));
  LED led_21 (.in(pulldown_6_out[12]));
  LED led_22 (.in(out[6]));
  LED led_23 (.in(out[5]));
  LED led_24 (.in(driver_3_out[11]));
  LED led_25 (.in(driver_3_out[10]));
  LED led_26 (.in(pulldown_1_out[7]));
  LED led_27 (.in(pulldown_1_out[6]));
  LED led_28 (.in(pulldown_6_out[11]));
  LED led_29 (.in(pulldown_6_out[10]));
  LED led_30 (.in(out[4]));
  LED led_31 (.in(out[3]));
  LED led_32 (.in(driver_3_out[9]));
  LED led_33 (.in(driver_3_out[8]));
  LED led_34 (.in(pulldown_1_out[5]));
  LED led_35 (.in(pulldown_1_out[4]));
  PullDown #(.Bits(4)) pulldown_2 (.out(pulldown_2_out));
  LED led_36 (.in(pulldown_6_out[9]));
  LED led_37 (.in(pulldown_6_out[8]));
  _7400 _7400_2 (
    .pin1(_7404_2_pin10), .pin2(_7404_2_pin10), .pin3(_7400_2_pin3), .pin4(_7404_2_pin10),
    .pin5(shifter_1_c_out), .pin6(_7400_2_pin6), .pin7(1'b0), .pin8(C), .pin9(_7400_2_pin6),
    .pin10(_7400_2_pin10), .pin11(_7400_2_pin10), .pin12(_7400_2_pin3), .pin13(negator_1_c_out), .pin14(1'b1));
  Function_selector function_selector_1 (
    .BSE(byte_sign_extender_1_out), .Shift(shifter_1_d_out), .Rotate(barrel_rotator_1_output),
    .Invert(logic_operations_1_not), .Add({N, Sum[14:0]}), .XOR(logic_operations_1_xor),
    .OR(logic_operations_1_or), .AND(logic_operations_1_and), .Function(Function), .Output(out));
  LED led_38 (.in(out[2]));
  LED led_39 (.in(out[1]));
  LED led_40 (.in(driver_3_out[7]));
  LED led_41 (.in(driver_3_out[6]));
  LED led_42 (.in(pulldown_1_out[3]));
  LED led_43 (.in(pulldown_1_out[2]));
  LED led_44 (.in(pulldown_2_out[3]));
  LED led_45 (.in(pulldown_2_out[2]));
  LED led_46 (.in(pulldown_6_out[7]));
  LED led_47 (.in(pulldown_6_out[6]));
  LED led_48 (.in(out[0]));
  LED led_49 (.in(driver_3_out[5]));
  LED led_50 (.in(driver_3_out[4]));
  LED led_51 (.in(pulldown_1_out[1]));
  LED led_52 (.in(pulldown_1_out[0]));
  LED led_53 (.in(pulldown_2_out[1]));
  LED led_54 (.in(pulldown_2_out[0]));
  LED led_55 (.in(pulldown_6_out[5]));
  LED led_56 (.in(pulldown_6_out[4]));
  Zero_Detector zero_detector_1 (.D_in(out), .Z(zero_detector_1_z));
  LED led_57 (.in(driver_3_out[3]));
  LED led_58 (.in(driver_3_out[2]));
  assign pulldown_1_out = and_2_out ? Src2[15:4] : 12'bz;  // Driver driver_1
  LED led_59 (.in(driver_4_out[3]));
  LED led_60 (.in(driver_4_out[2]));
  assign pulldown_2_out = and_3_out ? Const[7:4] : 4'bz;  // Driver driver_2
  LED led_61 (.in(driver_5_out[3]));
  LED led_62 (.in(driver_5_out[2]));
  LED led_63 (.in(pulldown_6_out[3]));
  LED led_64 (.in(pulldown_6_out[2]));
  Bus_buffer E2_buffer (.nEnable(nE2), .Data_in(out), .Data_out(Output));
  LED led_65 (.in(driver_3_out[1]));
  LED led_66 (.in(driver_3_out[0]));
  LED led_67 (.in(driver_4_out[1]));
  LED led_68 (.in(driver_4_out[0]));
  LED led_69 (.in(driver_5_out[1]));
  LED led_70 (.in(driver_5_out[0]));
  LED led_71 (.in(pulldown_6_out[1]));
  LED led_72 (.in(pulldown_6_out[0]));
  not not_1 (Z, zero_detector_1_z);
  assign driver_3_out = ALU_enable ? Src1 : 16'bz;  // Driver driver_3
  PullDown #(.Bits(16)) pulldown_3 (.out(driver_3_out));
  assign driver_4_out = _7408_1_pin11 ? Src2[3:0] : 4'bz;  // Driver driver_4
  PullDown #(.Bits(4)) pulldown_4 (.out(driver_4_out));
  assign driver_5_out = _7404_1_pin6 ? Const[3:0] : 4'bz;  // Driver driver_5
  PullDown #(.Bits(4)) pulldown_5 (.out(driver_5_out));
  PullDown #(.Bits(16)) pulldown_6 (.out(pulldown_6_out));
  assign pulldown_6_out = ALU_enable ? out : 16'bz;  // Driver driver_6

  assign Sum[15] = N;

  // Other names for the same wires on the sheet: ALU_en = ALU_enable; Ar = Arithm; Carry_en_RotC = Enable_C_in_RotC;
  //   Const_en = Const_enable

  // Notes on the sheet:
  //   Src1: Source register pointed by bits 5,6,7 of inctruction,
  //    or by bits 8,9,A when it is op with constant
  //   Src2: Source register pointed by bits 0,1,2 of inctruction
  //   Const: 8-bit constant value, sourced from instruction register
  //   Carry_in: Carry in
  //   Sub_Inv_Rev: Inverts Src2 and helps with subtraction, reverses shift
  //   Function: Chooses one of 8 possible operation types
  //   Const_enable: Switch to using constant instead of Src2
  //   Arithm: Sets arithmetic shift
  //   C: Carry out
  //   O: Overflow
  //   N: Negative sign
  //   Z: Output is zero
  //   ALU_enable: ALU operation
  //   B_in: ALU B input
  //   Sum: raw ALU output
  //   Controls:
  //   Operands:
  //   Main ALU
  //   Overflow
  //   Negative
  //   4 NAND gates as 2-to-1 Multiplexer
  //   C_out
  //   Zero
endmodule
