// Digital circuit Zero Detector.dig as structural Verilog
module Zero_Detector (
  input  [15:0] D_in,
  output Z
);

  wire _7402_1_pin1, _7402_1_pin4, _7402_1_pin10, _7402_1_pin13, _7430_1_pin5, _7430_1_pin6, _7430_1_pin11,
       _7430_1_pin12;

  _7402 _7402_1 (
    .pin1(_7402_1_pin1), .pin2(D_in[15]), .pin3(D_in[14]), .pin4(_7402_1_pin4), .pin5(D_in[13]),
    .pin6(D_in[12]), .pin7(1'b0), .pin8(D_in[11]), .pin9(D_in[10]), .pin10(_7402_1_pin10), .pin11(D_in[9]),
    .pin12(D_in[8]), .pin13(_7402_1_pin13), .pin14(1'b1));
  _7430 _7430_1 (
    .pin1(_7402_1_pin1), .pin2(_7402_1_pin13), .pin3(_7402_1_pin4), .pin4(_7402_1_pin10),
    .pin5(_7430_1_pin5), .pin6(_7430_1_pin6), .pin7(1'b0), .pin8(Z), .pin11(_7430_1_pin11),
    .pin12(_7430_1_pin12), .pin14(1'b1));  // open: pin9, pin10, pin13
  _7402 _7402_2 (
    .pin1(_7430_1_pin12), .pin2(D_in[7]), .pin3(D_in[6]), .pin4(_7430_1_pin11), .pin5(D_in[5]),
    .pin6(D_in[4]), .pin7(1'b0), .pin8(D_in[3]), .pin9(D_in[2]), .pin10(_7430_1_pin6), .pin11(D_in[1]),
    .pin12(D_in[0]), .pin13(_7430_1_pin5), .pin14(1'b1));

  // Notes on the sheet:
  //   Z: Becomes 1 only if all 16 inputs are 0
  //   Zero Detector
endmodule
