// Digital circuit Address_Adder.dig as structural Verilog
module Address_Adder (
  input  [31:0] A,
  input  [31:0] B,
  output [31:0] out,
  output Carry
);

  wire _8b_fa_board_1_c_out, _8b_fa_board_2_c_out, _8b_fa_board_3_c_out;

  _8b_FA_board _8b_fa_board_1 (
    .C_in(1'b0), .A(A[7:0]), .B(B[7:0]), .S(out[7:0]), .C_out(_8b_fa_board_1_c_out));  // open: C3_of
  _8b_FA_board _8b_fa_board_2 (
    .C_in(_8b_fa_board_1_c_out), .A(A[15:8]), .B(B[15:8]), .S(out[15:8]), .C_out(_8b_fa_board_2_c_out));  // open: C3_of
  _8b_FA_board _8b_fa_board_3 (
    .C_in(_8b_fa_board_2_c_out), .A(A[23:16]), .B(B[23:16]), .S(out[23:16]), .C_out(_8b_fa_board_3_c_out));  // open: C3_of
  _8b_FA_board _8b_fa_board_4 (
    .C_in(_8b_fa_board_3_c_out), .A(A[31:24]), .B(B[31:24]), .S(out[31:24]), .C_out(Carry));  // open: C3_of

  // Notes on the sheet:
  //   Carry: should trigger "Out of memory" exception
endmodule
