// Digital circuit MP_selector.dig as structural Verilog
module MP_selector (
  input  [1:0] Addr,
  input  [15:0] _00,
  input  [15:0] _01,
  input  [15:0] _10,
  input  [15:0] _11,
  output [15:0] Out
);

  _74153 _74153_1 (
    .pin1(1'b0), .pin2(Addr[1]), .pin3(_11[0]), .pin4(_10[0]), .pin5(_01[0]), .pin6(_00[0]), .pin7(Out[0]),
    .pin8(1'b0), .pin9(Out[1]), .pin10(_00[1]), .pin11(_01[1]), .pin12(_10[1]), .pin13(_11[1]),
    .pin14(Addr[0]), .pin15(1'b0), .pin16(1'b1));
  _74153 _74153_2 (
    .pin1(1'b0), .pin2(Addr[1]), .pin3(_11[2]), .pin4(_10[2]), .pin5(_01[2]), .pin6(_00[2]), .pin7(Out[2]),
    .pin8(1'b0), .pin9(Out[3]), .pin10(_00[3]), .pin11(_01[3]), .pin12(_10[3]), .pin13(_11[3]),
    .pin14(Addr[0]), .pin15(1'b0), .pin16(1'b1));
  _74153 _74153_3 (
    .pin1(1'b0), .pin2(Addr[1]), .pin3(_11[4]), .pin4(_10[4]), .pin5(_01[4]), .pin6(_00[4]), .pin7(Out[4]),
    .pin8(1'b0), .pin9(Out[5]), .pin10(_00[5]), .pin11(_01[5]), .pin12(_10[5]), .pin13(_11[5]),
    .pin14(Addr[0]), .pin15(1'b0), .pin16(1'b1));
  _74153 _74153_4 (
    .pin1(1'b0), .pin2(Addr[1]), .pin3(_11[6]), .pin4(_10[6]), .pin5(_01[6]), .pin6(_00[6]), .pin7(Out[6]),
    .pin8(1'b0), .pin9(Out[7]), .pin10(_00[7]), .pin11(_01[7]), .pin12(_10[7]), .pin13(_11[7]),
    .pin14(Addr[0]), .pin15(1'b0), .pin16(1'b1));
  _74153 _74153_5 (
    .pin1(1'b0), .pin2(Addr[1]), .pin3(_11[8]), .pin4(_10[8]), .pin5(_01[8]), .pin6(_00[8]), .pin7(Out[8]),
    .pin8(1'b0), .pin9(Out[9]), .pin10(_00[9]), .pin11(_01[9]), .pin12(_10[9]), .pin13(_11[9]),
    .pin14(Addr[0]), .pin15(1'b0), .pin16(1'b1));
  _74153 _74153_6 (
    .pin1(1'b0), .pin2(Addr[1]), .pin3(_11[10]), .pin4(_10[10]), .pin5(_01[10]), .pin6(_00[10]),
    .pin7(Out[10]), .pin8(1'b0), .pin9(Out[11]), .pin10(_00[11]), .pin11(_01[11]), .pin12(_10[11]),
    .pin13(_11[11]), .pin14(Addr[0]), .pin15(1'b0), .pin16(1'b1));
  _74153 _74153_7 (
    .pin1(1'b0), .pin2(Addr[1]), .pin3(_11[12]), .pin4(_10[12]), .pin5(_01[12]), .pin6(_00[12]),
    .pin7(Out[12]), .pin8(1'b0), .pin9(Out[13]), .pin10(_00[13]), .pin11(_01[13]), .pin12(_10[13]),
    .pin13(_11[13]), .pin14(Addr[0]), .pin15(1'b0), .pin16(1'b1));
  _74153 _74153_8 (
    .pin1(1'b0), .pin2(Addr[1]), .pin3(_11[14]), .pin4(_10[14]), .pin5(_01[14]), .pin6(_00[14]),
    .pin7(Out[14]), .pin8(1'b0), .pin9(Out[15]), .pin10(_00[15]), .pin11(_01[15]), .pin12(_10[15]),
    .pin13(_11[15]), .pin14(Addr[0]), .pin15(1'b0), .pin16(1'b1));

  // Notes on the sheet:
  //   1 of 4 selector 16 bit
endmodule
