// Digital circuit Memory_Pointers.dig as structural Verilog
module Memory_Pointers (
  input  nr,
  input  [15:0] D3,
  input  L3,
  input  [1:0] LA34,
  input  [15:0] D4,
  input  L4,
  input  [1:0] S3,
  output [15:0] MP_H,
  output [15:0] MP_L,
  output [31:0] PC,
  output [31:0] SP,
  output [31:0] FP,
  output [31:0] BP
);

  wire _74238_1_pin12, _74238_1_pin13, _74238_1_pin14, _74238_1_pin15, _74238_2_pin12, _74238_2_pin13,
       _74238_2_pin14, _74238_2_pin15;

  _74238 _74238_1 (
    .pin1(LA34[0]), .pin2(LA34[1]), .pin3(1'b0), .pin4(1'b0), .pin5(1'b0), .pin6(L4), .pin8(1'b0),
    .pin12(_74238_1_pin12), .pin13(_74238_1_pin13), .pin14(_74238_1_pin14), .pin15(_74238_1_pin15),
    .pin16(1'b1));  // open: pin7, pin9, pin10, pin11
  _74238 _74238_2 (
    .pin1(LA34[0]), .pin2(LA34[1]), .pin3(1'b0), .pin4(1'b0), .pin5(1'b0), .pin6(L3), .pin8(1'b0),
    .pin12(_74238_2_pin12), .pin13(_74238_2_pin13), .pin14(_74238_2_pin14), .pin15(_74238_2_pin15),
    .pin16(1'b1));  // open: pin7, pin9, pin10, pin11
  Register PCH (.nR(nr), .D_in(D3), .Clk(_74238_1_pin15), .D_out(PC[31:16]));
  Register PCL (.nR(nr), .D_in(D4), .Clk(_74238_2_pin15), .D_out(PC[15:0]));
  Register SPH (.nR(nr), .D_in(D3), .Clk(_74238_1_pin14), .D_out(SP[31:16]));
  Register SPL (.nR(nr), .D_in(D4), .Clk(_74238_2_pin14), .D_out(SP[15:0]));
  Register FPH (.nR(nr), .D_in(D3), .Clk(_74238_1_pin13), .D_out(FP[31:16]));
  Register FPL (.nR(nr), .D_in(D4), .Clk(_74238_2_pin13), .D_out(FP[15:0]));
  Register BPH (.nR(nr), .D_in(D3), .Clk(_74238_1_pin12), .D_out(BP[31:16]));
  Register BPL (.nR(nr), .D_in(D4), .Clk(_74238_2_pin12), .D_out(BP[15:0]));
  MP_selector Sel___H (.Out(MP_H), ._00(PC[31:16]), ._01(SP[31:16]), ._10(FP[31:16]), ._11(BP[31:16]), .Addr(S3));
  MP_selector Sel___L (.Out(MP_L), ._00(PC[15:0]), ._01(SP[15:0]), ._10(FP[15:0]), ._11(BP[15:0]), .Addr(S3));
endmodule
