// Digital circuit 8b_FA_board.dig as structural Verilog
module _8b_FA_board (
  input  C_in,
  input  [7:0] A,
  input  [7:0] B,
  output [7:0] S,
  output C_out,
  output C3_of
);

  wire _7400_1_pin3, _7400_1_pin8, _7400_1_pin11, _7400_2_pin3, _7400_2_pin8, _7400_2_pin11, _7404_1_pin4,
       _7404_1_pin6, _7404_1_pin10, _7404_1_pin12, _7404_2_pin4, _7404_2_pin6, _7404_2_pin10, _7404_2_pin12,
       _7408_1_pin3, _7408_1_pin6, _7408_1_pin8, _7408_1_pin11, _7408_2_pin3, _7408_2_pin6, _7408_2_pin8,
       _7408_2_pin11, _7420_1_pin6, _7420_1_pin12, _7420_2_pin6, _7420_2_pin12, _7420_3_pin8, _7420_4_pin8,
       _7420_5_pin6, _7420_5_pin8, _7420_6_pin6, _7420_6_pin8, _7420_7_pin8, _7420_8_pin8, _7430_1_pin8,
       _7430_2_pin8, _7486_1_pin3, _7486_1_pin6, _7486_1_pin8, _7486_1_pin11, _7486_2_pin3, _7486_2_pin6,
       _7486_2_pin8, _7486_2_pin11, _7486_3_pin4, _7486_3_pin10, _7486_3_pin13, _7486_4_pin1, _7486_4_pin4,
       _7486_4_pin13;

  _7486 _7486_1 (
    .pin1(A[0]), .pin2(B[0]), .pin3(_7486_1_pin3), .pin4(A[1]), .pin5(B[1]), .pin6(_7486_1_pin6),
    .pin7(1'b0), .pin8(_7486_1_pin8), .pin9(B[3]), .pin10(A[3]), .pin11(_7486_1_pin11), .pin12(B[2]),
    .pin13(A[2]), .pin14(1'b1));
  _7486 _7486_2 (
    .pin1(A[4]), .pin2(B[4]), .pin3(_7486_2_pin3), .pin4(A[5]), .pin5(B[5]), .pin6(_7486_2_pin6),
    .pin7(1'b0), .pin8(_7486_2_pin8), .pin9(B[7]), .pin10(A[7]), .pin11(_7486_2_pin11), .pin12(B[6]),
    .pin13(A[6]), .pin14(1'b1));
  _7408 _7408_1 (
    .pin1(A[2]), .pin2(B[2]), .pin3(_7408_1_pin3), .pin4(A[3]), .pin5(B[3]), .pin6(_7408_1_pin6),
    .pin7(1'b0), .pin8(_7408_1_pin8), .pin9(B[1]), .pin10(A[1]), .pin11(_7408_1_pin11), .pin12(B[0]),
    .pin13(A[0]), .pin14(1'b1));
  _7408 _7408_2 (
    .pin1(A[6]), .pin2(B[6]), .pin3(_7408_2_pin3), .pin4(A[7]), .pin5(B[7]), .pin6(_7408_2_pin6),
    .pin7(1'b0), .pin8(_7408_2_pin8), .pin9(B[5]), .pin10(A[5]), .pin11(_7408_2_pin11), .pin12(B[4]),
    .pin13(A[4]), .pin14(1'b1));
  _7486 _7486_3 (
    .pin1(C_in), .pin2(_7486_1_pin3), .pin3(S[0]), .pin4(_7486_3_pin4), .pin5(_7486_1_pin6), .pin6(S[1]),
    .pin7(1'b0), .pin8(S[3]), .pin9(_7486_1_pin8), .pin10(_7486_3_pin10), .pin11(S[2]),
    .pin12(_7486_1_pin11), .pin13(_7486_3_pin13), .pin14(1'b1));
  _7486 _7486_4 (
    .pin1(_7486_4_pin1), .pin2(_7486_2_pin3), .pin3(S[4]), .pin4(_7486_4_pin4), .pin5(_7486_2_pin6),
    .pin6(S[5]), .pin7(1'b0), .pin8(S[7]), .pin9(_7486_2_pin8), .pin10(C3_of), .pin11(S[6]),
    .pin12(_7486_2_pin11), .pin13(_7486_4_pin13), .pin14(1'b1));
  _7404 _7404_1 (
    .pin1(1'b1), .pin3(_7408_1_pin8), .pin4(_7404_1_pin4), .pin5(_7408_1_pin3), .pin6(_7404_1_pin6),
    .pin7(1'b0), .pin9(1'b0), .pin10(_7404_1_pin10), .pin11(_7408_1_pin11), .pin12(_7404_1_pin12),
    .pin13(_7408_1_pin6), .pin14(1'b1));  // open: pin2, pin8
  _7404 _7404_2 (
    .pin1(1'b1), .pin3(_7408_2_pin8), .pin4(_7404_2_pin4), .pin5(_7408_2_pin3), .pin6(_7404_2_pin6),
    .pin7(1'b0), .pin9(1'b0), .pin10(_7404_2_pin10), .pin11(_7408_2_pin11), .pin12(_7404_2_pin12),
    .pin13(_7408_2_pin6), .pin14(1'b1));  // open: pin2, pin8
  _7400 _7400_1 (
    .pin1(C_in), .pin2(_7486_1_pin3), .pin3(_7400_1_pin3), .pin4(_7400_1_pin3), .pin5(_7404_1_pin10),
    .pin6(_7486_3_pin4), .pin7(1'b0), .pin8(_7400_1_pin8), .pin9(_7408_1_pin8), .pin10(_7486_1_pin11),
    .pin11(_7400_1_pin11), .pin12(_7486_1_pin6), .pin13(_7408_1_pin11), .pin14(1'b1));
  _7400 _7400_2 (
    .pin1(_7486_4_pin1), .pin2(_7486_2_pin3), .pin3(_7400_2_pin3), .pin4(_7400_2_pin3), .pin5(_7404_2_pin10),
    .pin6(_7486_4_pin4), .pin7(1'b0), .pin8(_7400_2_pin8), .pin9(_7408_2_pin8), .pin10(_7486_2_pin11),
    .pin11(_7400_2_pin11), .pin12(_7486_2_pin6), .pin13(_7408_2_pin11), .pin14(1'b1));
  _7420 _7420_1 (
    .pin1(_7408_1_pin11), .pin2(_7408_1_pin11), .pin4(_7486_1_pin6), .pin5(_7486_1_pin11),
    .pin6(_7420_1_pin6), .pin7(1'b0), .pin8(_7486_3_pin13), .pin9(_7404_1_pin4), .pin10(_7400_1_pin11),
    .pin12(_7420_1_pin12), .pin13(_7420_1_pin12), .pin14(1'b1));  // open: pin3, pin11
  _7420 _7420_2 (
    .pin1(_7408_2_pin11), .pin2(_7408_2_pin11), .pin4(_7486_2_pin6), .pin5(_7486_2_pin11),
    .pin6(_7420_2_pin6), .pin7(1'b0), .pin8(_7486_4_pin13), .pin9(_7404_2_pin4), .pin10(_7400_2_pin11),
    .pin12(_7420_2_pin12), .pin13(_7420_2_pin12), .pin14(1'b1));  // open: pin3, pin11
  _7420 _7420_3 (
    .pin1(_7486_1_pin6), .pin2(_7486_1_pin3), .pin4(C_in), .pin5(C_in), .pin6(_7420_1_pin12), .pin7(1'b0),
    .pin8(_7420_3_pin8), .pin9(_7408_1_pin8), .pin10(_7486_1_pin11), .pin12(_7486_1_pin8),
    .pin13(_7486_1_pin8), .pin14(1'b1));  // open: pin3, pin11
  _7420 _7420_4 (
    .pin1(_7486_2_pin6), .pin2(_7486_2_pin3), .pin4(_7486_4_pin1), .pin5(_7486_4_pin1), .pin6(_7420_2_pin12),
    .pin7(1'b0), .pin8(_7420_4_pin8), .pin9(_7408_2_pin8), .pin10(_7486_2_pin11), .pin12(_7486_2_pin8),
    .pin13(_7486_2_pin8), .pin14(1'b1));  // open: pin3, pin11
  _7420 _7420_5 (
    .pin1(_7486_1_pin8), .pin2(_7486_1_pin8), .pin4(_7408_1_pin3), .pin5(_7408_1_pin3), .pin6(_7420_5_pin6),
    .pin7(1'b0), .pin8(_7420_5_pin8), .pin9(C_in), .pin10(_7486_1_pin3), .pin12(_7486_1_pin6),
    .pin13(_7486_1_pin11), .pin14(1'b1));  // open: pin3, pin11
  _7420 _7420_6 (
    .pin1(_7486_2_pin8), .pin2(_7486_2_pin8), .pin4(_7408_2_pin3), .pin5(_7408_2_pin3), .pin6(_7420_6_pin6),
    .pin7(1'b0), .pin8(_7420_6_pin8), .pin9(_7486_4_pin1), .pin10(_7486_2_pin3), .pin12(_7486_2_pin6),
    .pin13(_7486_2_pin11), .pin14(1'b1));  // open: pin3, pin11
  _7420 _7420_7 (
    .pin1(_7404_1_pin6), .pin2(_7420_5_pin8), .pin4(_7420_1_pin6), .pin5(_7400_1_pin8), .pin6(_7486_3_pin10),
    .pin7(1'b0), .pin8(_7420_7_pin8), .pin9(_7408_1_pin11), .pin10(_7486_1_pin6), .pin12(_7486_1_pin11),
    .pin13(_7486_1_pin8), .pin14(1'b1));  // open: pin3, pin11
  _7420 _7420_8 (
    .pin1(_7404_2_pin6), .pin2(_7420_6_pin8), .pin4(_7420_2_pin6), .pin5(_7400_2_pin8), .pin6(C3_of),
    .pin7(1'b0), .pin8(_7420_8_pin8), .pin9(_7408_2_pin11), .pin10(_7486_2_pin6), .pin12(_7486_2_pin11),
    .pin13(_7486_2_pin8), .pin14(1'b1));  // open: pin3, pin11
  _7430 _7430_1 (
    .pin1(_7486_1_pin3), .pin2(C_in), .pin3(_7486_1_pin8), .pin4(_7486_1_pin11), .pin5(_7486_1_pin6),
    .pin6(_7486_1_pin6), .pin7(1'b0), .pin8(_7430_1_pin8), .pin11(1'b1), .pin12(1'b1), .pin14(1'b1));  // open: pin9, pin10, pin13
  _7430 _7430_2 (
    .pin1(_7486_2_pin3), .pin2(_7486_4_pin1), .pin3(_7486_2_pin8), .pin4(_7486_2_pin11), .pin5(_7486_2_pin6),
    .pin6(_7486_2_pin6), .pin7(1'b0), .pin8(_7430_2_pin8), .pin11(1'b1), .pin12(1'b1), .pin14(1'b1));  // open: pin9, pin10, pin13
  _7430 _7430_3 (
    .pin1(_7404_1_pin12), .pin2(_7420_5_pin6), .pin3(_7420_7_pin8), .pin4(_7430_1_pin8), .pin5(_7420_3_pin8),
    .pin6(_7420_3_pin8), .pin7(1'b0), .pin8(_7486_4_pin1), .pin11(1'b1), .pin12(1'b1), .pin14(1'b1));  // open: pin9, pin10, pin13
  _7430 _7430_4 (
    .pin1(_7404_2_pin12), .pin2(_7420_6_pin6), .pin3(_7420_8_pin8), .pin4(_7430_2_pin8), .pin5(_7420_4_pin8),
    .pin6(_7420_4_pin8), .pin7(1'b0), .pin8(C_out), .pin11(1'b1), .pin12(1'b1), .pin14(1'b1));  // open: pin9, pin10, pin13

  // Notes on the sheet:
  //   Adder element 4x
  //   8bit Fast adder 74xx
  //   Carry 1
  //   Carry 2
  //   Carry 3
  //   Carry look-ahead
endmodule
