// Digital circuit Function selector.dig as structural Verilog
module Function_selector (
  input  [15:0] Shift,
  input  [15:0] Rotate,
  input  [15:0] Invert,
  input  [15:0] Add,
  input  [15:0] AND,
  input  [15:0] OR,
  input  [15:0] XOR,
  input  [2:0] Function,
  input  [15:0] BSE,
  output [15:0] Output
);

  _74151 _74151_1 (
    .pin1(Invert[12]), .pin2(Rotate[12]), .pin3(Shift[12]), .pin4(BSE[12]), .pin5(Output[12]), .pin7(1'b0),
    .pin8(1'b0), .pin9(Function[2]), .pin10(Function[1]), .pin11(Function[0]), .pin12(AND[12]),
    .pin13(OR[12]), .pin14(XOR[12]), .pin15(Add[12]), .pin16(1'b1));  // open: pin6
  _74151 _74151_2 (
    .pin1(Invert[13]), .pin2(Rotate[13]), .pin3(Shift[13]), .pin4(BSE[13]), .pin5(Output[13]), .pin7(1'b0),
    .pin8(1'b0), .pin9(Function[2]), .pin10(Function[1]), .pin11(Function[0]), .pin12(AND[13]),
    .pin13(OR[13]), .pin14(XOR[13]), .pin15(Add[13]), .pin16(1'b1));  // open: pin6
  _74151 _74151_3 (
    .pin1(Invert[14]), .pin2(Rotate[14]), .pin3(Shift[14]), .pin4(BSE[14]), .pin5(Output[14]), .pin7(1'b0),
    .pin8(1'b0), .pin9(Function[2]), .pin10(Function[1]), .pin11(Function[0]), .pin12(AND[14]),
    .pin13(OR[14]), .pin14(XOR[14]), .pin15(Add[14]), .pin16(1'b1));  // open: pin6
  _74151 _74151_4 (
    .pin1(Invert[15]), .pin2(Rotate[15]), .pin3(Shift[15]), .pin4(BSE[15]), .pin5(Output[15]), .pin7(1'b0),
    .pin8(1'b0), .pin9(Function[2]), .pin10(Function[1]), .pin11(Function[0]), .pin12(AND[15]),
    .pin13(OR[15]), .pin14(XOR[15]), .pin15(Add[15]), .pin16(1'b1));  // open: pin6
  _74151 _74151_5 (
    .pin1(Invert[8]), .pin2(Rotate[8]), .pin3(Shift[8]), .pin4(BSE[8]), .pin5(Output[8]), .pin7(1'b0),
    .pin8(1'b0), .pin9(Function[2]), .pin10(Function[1]), .pin11(Function[0]), .pin12(AND[8]), .pin13(OR[8]),
    .pin14(XOR[8]), .pin15(Add[8]), .pin16(1'b1));  // open: pin6
  _74151 _74151_6 (
    .pin1(Invert[9]), .pin2(Rotate[9]), .pin3(Shift[9]), .pin4(BSE[9]), .pin5(Output[9]), .pin7(1'b0),
    .pin8(1'b0), .pin9(Function[2]), .pin10(Function[1]), .pin11(Function[0]), .pin12(AND[9]), .pin13(OR[9]),
    .pin14(XOR[9]), .pin15(Add[9]), .pin16(1'b1));  // open: pin6
  _74151 _74151_7 (
    .pin1(Invert[10]), .pin2(Rotate[10]), .pin3(Shift[10]), .pin4(BSE[10]), .pin5(Output[10]), .pin7(1'b0),
    .pin8(1'b0), .pin9(Function[2]), .pin10(Function[1]), .pin11(Function[0]), .pin12(AND[10]),
    .pin13(OR[10]), .pin14(XOR[10]), .pin15(Add[10]), .pin16(1'b1));  // open: pin6
  _74151 _74151_8 (
    .pin1(Invert[11]), .pin2(Rotate[11]), .pin3(Shift[11]), .pin4(BSE[11]), .pin5(Output[11]), .pin7(1'b0),
    .pin8(1'b0), .pin9(Function[2]), .pin10(Function[1]), .pin11(Function[0]), .pin12(AND[11]),
    .pin13(OR[11]), .pin14(XOR[11]), .pin15(Add[11]), .pin16(1'b1));  // open: pin6
  _74151 _74151_9 (
    .pin1(Invert[4]), .pin2(Rotate[4]), .pin3(Shift[4]), .pin4(BSE[4]), .pin5(Output[4]), .pin7(1'b0),
    .pin8(1'b0), .pin9(Function[2]), .pin10(Function[1]), .pin11(Function[0]), .pin12(AND[4]), .pin13(OR[4]),
    .pin14(XOR[4]), .pin15(Add[4]), .pin16(1'b1));  // open: pin6
  _74151 _74151_10 (
    .pin1(Invert[5]), .pin2(Rotate[5]), .pin3(Shift[5]), .pin4(BSE[5]), .pin5(Output[5]), .pin7(1'b0),
    .pin8(1'b0), .pin9(Function[2]), .pin10(Function[1]), .pin11(Function[0]), .pin12(AND[5]), .pin13(OR[5]),
    .pin14(XOR[5]), .pin15(Add[5]), .pin16(1'b1));  // open: pin6
  _74151 _74151_11 (
    .pin1(Invert[6]), .pin2(Rotate[6]), .pin3(Shift[6]), .pin4(BSE[6]), .pin5(Output[6]), .pin7(1'b0),
    .pin8(1'b0), .pin9(Function[2]), .pin10(Function[1]), .pin11(Function[0]), .pin12(AND[6]), .pin13(OR[6]),
    .pin14(XOR[6]), .pin15(Add[6]), .pin16(1'b1));  // open: pin6
  _74151 _74151_12 (
    .pin1(Invert[7]), .pin2(Rotate[7]), .pin3(Shift[7]), .pin4(BSE[7]), .pin5(Output[7]), .pin7(1'b0),
    .pin8(1'b0), .pin9(Function[2]), .pin10(Function[1]), .pin11(Function[0]), .pin12(AND[7]), .pin13(OR[7]),
    .pin14(XOR[7]), .pin15(Add[7]), .pin16(1'b1));  // open: pin6
  _74151 _74151_13 (
    .pin1(Invert[0]), .pin2(Rotate[0]), .pin3(Shift[0]), .pin4(BSE[0]), .pin5(Output[0]), .pin7(1'b0),
    .pin8(1'b0), .pin9(Function[2]), .pin10(Function[1]), .pin11(Function[0]), .pin12(AND[0]), .pin13(OR[0]),
    .pin14(XOR[0]), .pin15(Add[0]), .pin16(1'b1));  // open: pin6
  _74151 _74151_14 (
    .pin1(Invert[1]), .pin2(Rotate[1]), .pin3(Shift[1]), .pin4(BSE[1]), .pin5(Output[1]), .pin7(1'b0),
    .pin8(1'b0), .pin9(Function[2]), .pin10(Function[1]), .pin11(Function[0]), .pin12(AND[1]), .pin13(OR[1]),
    .pin14(XOR[1]), .pin15(Add[1]), .pin16(1'b1));  // open: pin6
  _74151 _74151_15 (
    .pin1(Invert[2]), .pin2(Rotate[2]), .pin3(Shift[2]), .pin4(BSE[2]), .pin5(Output[2]), .pin7(1'b0),
    .pin8(1'b0), .pin9(Function[2]), .pin10(Function[1]), .pin11(Function[0]), .pin12(AND[2]), .pin13(OR[2]),
    .pin14(XOR[2]), .pin15(Add[2]), .pin16(1'b1));  // open: pin6
  _74151 _74151_16 (
    .pin1(Invert[3]), .pin2(Rotate[3]), .pin3(Shift[3]), .pin4(BSE[3]), .pin5(Output[3]), .pin7(1'b0),
    .pin8(1'b0), .pin9(Function[2]), .pin10(Function[1]), .pin11(Function[0]), .pin12(AND[3]), .pin13(OR[3]),
    .pin14(XOR[3]), .pin15(Add[3]), .pin16(1'b1));  // open: pin6

  // Notes on the sheet:
  //   BSE: byte sign extend
endmodule
