// Digital circuit Logic Operations.dig as structural Verilog
// Logic Operation unit
module Logic_Operations (
  input  [15:0] A,
  input  [15:0] B,
  output [15:0] And,
  output [15:0] Or,
  output [15:0] Xor,
  output [15:0] Not
);

  Logic_Unit_4bit_slice logic_unit_4bit_slice_1 (.A(A[3:0]), .B(B[3:0]), .And(And[3:0]), .Or(Or[3:0]), .Xor(Xor[3:0]));
  Logic_Unit_4bit_slice logic_unit_4bit_slice_2 (.A(A[7:4]), .B(B[7:4]), .And(And[7:4]), .Or(Or[7:4]), .Xor(Xor[7:4]));
  Logic_Unit_4bit_slice logic_unit_4bit_slice_3 (
    .A(A[11:8]), .B(B[11:8]), .And(And[11:8]), .Or(Or[11:8]), .Xor(Xor[11:8]));
  Logic_Unit_4bit_slice logic_unit_4bit_slice_4 (
    .A(A[15:12]), .B(B[15:12]), .And(And[15:12]), .Or(Or[15:12]), .Xor(Xor[15:12]));
  assign Not = ~A;  // Not not_1, 16 bits wide
endmodule
