// Digital circuit Logic Unit 4bit slice.dig as structural Verilog
module Logic_Unit_4bit_slice (
  input  [3:0] A,
  input  [3:0] B,
  output [3:0] And,
  output [3:0] Or,
  output [3:0] Xor
);

  wire _7402_1_pin1, _7402_1_pin4, _7402_1_pin10, _7402_1_pin13;

  _7408 _7408_1 (
    .pin1(A[2]), .pin2(B[2]), .pin3(And[2]), .pin4(A[3]), .pin5(B[3]), .pin6(And[3]), .pin7(1'b0),
    .pin8(And[0]), .pin9(A[0]), .pin10(B[0]), .pin11(And[1]), .pin12(A[1]), .pin13(B[1]), .pin14(1'b1));
  _7402 _7402_1 (
    .pin1(_7402_1_pin1), .pin2(A[2]), .pin3(B[2]), .pin4(_7402_1_pin4), .pin5(A[3]), .pin6(B[3]),
    .pin7(1'b0), .pin8(A[0]), .pin9(B[0]), .pin10(_7402_1_pin10), .pin11(A[1]), .pin12(B[1]),
    .pin13(_7402_1_pin13), .pin14(1'b1));
  _7404 _7404_1 (
    .pin1(_7402_1_pin10), .pin2(Or[0]), .pin3(_7402_1_pin13), .pin4(Or[1]), .pin5(_7402_1_pin1),
    .pin6(Or[2]), .pin7(1'b0), .pin9(1'b0), .pin11(1'b0), .pin12(Or[3]), .pin13(_7402_1_pin4), .pin14(1'b1));  // open: pin8, pin10
  _7402 _7402_2 (
    .pin1(Xor[3]), .pin2(And[3]), .pin3(_7402_1_pin4), .pin4(Xor[2]), .pin5(And[2]), .pin6(_7402_1_pin1),
    .pin7(1'b0), .pin8(And[1]), .pin9(_7402_1_pin13), .pin10(Xor[1]), .pin11(And[0]), .pin12(_7402_1_pin10),
    .pin13(Xor[0]), .pin14(1'b1));

  // Notes on the sheet:
  //   Logic unit
endmodule
