// Digital circuit Negator.dig as structural Verilog
module Negator (
  input  [15:0] In,
  input  N,
  input  C_in,
  input  C_from_Adder,
  input  E_from_Adder,
  output [15:0] Out,
  output C_in_to_Adder,
  output C_out,
  output Overflow
);

  _7486 _7486_1 (
    .pin1(In[0]), .pin2(N), .pin3(Out[0]), .pin4(In[1]), .pin5(N), .pin6(Out[1]), .pin7(1'b0), .pin8(Out[2]),
    .pin9(In[2]), .pin10(N), .pin11(Out[3]), .pin12(In[3]), .pin13(N), .pin14(1'b1));
  _7486 _7486_2 (
    .pin1(In[4]), .pin2(N), .pin3(Out[4]), .pin4(In[5]), .pin5(N), .pin6(Out[5]), .pin7(1'b0), .pin8(Out[6]),
    .pin9(In[6]), .pin10(N), .pin11(Out[7]), .pin12(In[7]), .pin13(N), .pin14(1'b1));
  _7486 _7486_3 (
    .pin1(In[8]), .pin2(N), .pin3(Out[8]), .pin4(In[9]), .pin5(N), .pin6(Out[9]), .pin7(1'b0),
    .pin8(Out[10]), .pin9(In[10]), .pin10(N), .pin11(Out[11]), .pin12(In[11]), .pin13(N), .pin14(1'b1));
  _7486 _7486_4 (
    .pin1(In[12]), .pin2(N), .pin3(Out[12]), .pin4(In[13]), .pin5(N), .pin6(Out[13]), .pin7(1'b0),
    .pin8(Out[14]), .pin9(In[14]), .pin10(N), .pin11(Out[15]), .pin12(In[15]), .pin13(N), .pin14(1'b1));
  _7486 _7486_5 (
    .pin1(C_in), .pin2(N), .pin3(C_in_to_Adder), .pin4(1'b0), .pin5(1'b0), .pin7(1'b0), .pin8(Overflow),
    .pin9(E_from_Adder), .pin10(C_from_Adder), .pin11(C_out), .pin12(C_from_Adder), .pin13(N), .pin14(1'b1));  // open: pin6

  // Notes on the sheet:
  //   In: 16-bit value
  //   N: Negation
  //   Negator
endmodule
