// Digital circuit Shifter.dig as structural Verilog
module Shifter (
  input  [15:0] D_in,
  input  A,
  input  C_in,
  input  L_R,
  input  sh_RC,
  output [15:0] D_out,
  output C_out
);

  wire _7400_1_pin3, _7400_1_pin5, _7400_1_pin6, _7400_1_pin8, _7400_1_pin9, _7400_1_pin11, _7400_1_pin12,
       _7400_1_pin13, _7404_1_pin1, _7404_1_pin9, _7404_1_pin10;

  _7400 _7400_1 (
    .pin1(C_in), .pin2(sh_RC), .pin3(_7400_1_pin3), .pin4(A), .pin5(_7400_1_pin5), .pin6(_7400_1_pin6),
    .pin7(1'b0), .pin8(_7400_1_pin8), .pin9(_7400_1_pin9), .pin10(D_in[15]), .pin11(_7400_1_pin11),
    .pin12(_7400_1_pin12), .pin13(_7400_1_pin13), .pin14(1'b1));
  _7404 _7404_1 (
    .pin1(_7404_1_pin1), .pin2(_7400_1_pin12), .pin3(sh_RC), .pin4(_7400_1_pin9), .pin5(_7400_1_pin8),
    .pin6(_7400_1_pin5), .pin7(1'b0), .pin8(_7400_1_pin13), .pin9(_7404_1_pin9), .pin10(_7404_1_pin10),
    .pin11(_7400_1_pin3), .pin12(_7404_1_pin1), .pin13(_7400_1_pin6), .pin14(1'b1));
  _74157 _74157_1 (
    .pin1(L_R), .pin2(_7404_1_pin1), .pin3(_7404_1_pin10), .pin4(_7404_1_pin9), .pin5(1'b0), .pin6(1'b0),
    .pin8(1'b0), .pin10(1'b0), .pin11(1'b0), .pin12(C_out), .pin13(D_in[0]), .pin14(D_in[15]), .pin15(1'b0),
    .pin16(1'b1));  // open: pin7, pin9
  _74157 _74157_2 (
    .pin1(L_R), .pin2(_7404_1_pin10), .pin3(D_in[1]), .pin4(D_out[0]), .pin5(D_in[0]), .pin6(D_in[2]),
    .pin7(D_out[1]), .pin8(1'b0), .pin9(D_out[3]), .pin10(D_in[4]), .pin11(D_in[2]), .pin12(D_out[2]),
    .pin13(D_in[3]), .pin14(D_in[1]), .pin15(1'b0), .pin16(1'b1));
  _74157 _74157_3 (
    .pin1(L_R), .pin2(D_in[3]), .pin3(D_in[5]), .pin4(D_out[4]), .pin5(D_in[4]), .pin6(D_in[6]),
    .pin7(D_out[5]), .pin8(1'b0), .pin9(D_out[7]), .pin10(D_in[8]), .pin11(D_in[6]), .pin12(D_out[6]),
    .pin13(D_in[7]), .pin14(D_in[5]), .pin15(1'b0), .pin16(1'b1));
  _74157 _74157_4 (
    .pin1(L_R), .pin2(D_in[7]), .pin3(D_in[9]), .pin4(D_out[8]), .pin5(D_in[8]), .pin6(D_in[10]),
    .pin7(D_out[9]), .pin8(1'b0), .pin9(D_out[11]), .pin10(D_in[12]), .pin11(D_in[10]), .pin12(D_out[10]),
    .pin13(D_in[11]), .pin14(D_in[9]), .pin15(1'b0), .pin16(1'b1));
  LED led_1 (.in(D_out[15]));
  LED led_2 (.in(D_out[14]));
  LED led_3 (.in(D_out[13]));
  LED led_4 (.in(D_out[12]));
  LED led_5 (.in(D_out[11]));
  LED led_6 (.in(D_out[10]));
  LED led_7 (.in(D_out[9]));
  LED led_8 (.in(D_out[8]));
  LED led_9 (.in(D_out[7]));
  LED led_10 (.in(D_out[6]));
  LED led_11 (.in(D_out[5]));
  _74157 _74157_5 (
    .pin1(L_R), .pin2(D_in[11]), .pin3(D_in[13]), .pin4(D_out[12]), .pin5(D_in[12]), .pin6(D_in[14]),
    .pin7(D_out[13]), .pin8(1'b0), .pin9(D_out[15]), .pin10(_7400_1_pin11), .pin11(D_in[14]),
    .pin12(D_out[14]), .pin13(D_in[15]), .pin14(D_in[13]), .pin15(1'b0), .pin16(1'b1));
  LED led_12 (.in(D_out[4]));
  LED led_13 (.in(D_out[3]));
  LED led_14 (.in(D_out[2]));
  LED led_15 (.in(D_out[1]));
  LED led_16 (.in(D_out[0]));

  // Notes on the sheet:
  //   A: Toggles arithmetic shiftright
  //   0	Logic shift right -- adds 0 as msb
  //   1	Arithmetic shift right -- bit15 stays the same
  //   C_out: carry bit
  //   Shifter
  //   0
  //   1
  //   2
  //   3
  //   4
  //   5
  //   6
  //   7
  //   8
  //   9
  //   A
  //   B
  //   C
  //   D
  //   E
  //   F
endmodule
