// Digital circuit Memory_Pointers_gates_tristate.dig as structural Verilog
module Memory_Pointers_gates_tristate (
  input  nr,
  input  [15:0] D3,
  input  L3,
  input  [1:0] LA34,
  input  [15:0] D4,
  input  L4,
  input  [1:0] S3,
  output [15:0] MP_H,
  output [15:0] MP_L,
  output [31:0] PC,
  output [31:0] SP,
  output [31:0] FP,
  output [31:0] BP
);

  wire decoder_1_out_0, decoder_1_out_1, decoder_1_out_2, decoder_1_out_3, demultiplexer_1_out_0,
       demultiplexer_1_out_1, demultiplexer_1_out_2, demultiplexer_1_out_3, demultiplexer_2_out_0,
       demultiplexer_2_out_1, demultiplexer_2_out_2, demultiplexer_2_out_3, multiplexer_1_out, not_1_out;
  wire [15:0] multiplexer_2_out;

  not not_1 (not_1_out, nr);
  Demultiplexer #(.Selector_Bits(2)) demultiplexer_1 (
    .sel(LA34), .in(L4), .out_0(demultiplexer_1_out_0), .out_1(demultiplexer_1_out_1),
    .out_2(demultiplexer_1_out_2), .out_3(demultiplexer_1_out_3));
  Demultiplexer #(.Selector_Bits(2)) demultiplexer_2 (
    .sel(LA34), .in(L3), .out_0(demultiplexer_2_out_0), .out_1(demultiplexer_2_out_1),
    .out_2(demultiplexer_2_out_2), .out_3(demultiplexer_2_out_3));
  Multiplexer multiplexer_1 (.sel(not_1_out), .in_0(demultiplexer_1_out_0), .in_1(not_1_out), .out(multiplexer_1_out));
  Multiplexer #(.Bits(16)) multiplexer_2 (.sel(not_1_out), .in_0(D3), .in_1(16'hff00), .out(multiplexer_2_out));
  D_FF_AS #(.Bits(16)) PCH (
    .Set(1'b0), .D(multiplexer_2_out), .C(multiplexer_1_out), .Clr(1'b0), .Q(PC[31:16]));  // open: nQ
  D_FF_AS #(.Bits(16)) PCL (.Set(1'b0), .D(D4), .C(demultiplexer_2_out_0), .Clr(not_1_out), .Q(PC[15:0]));  // open: nQ
  D_FF_AS #(.Bits(16)) SPH (.Set(1'b0), .D(D3), .C(demultiplexer_1_out_1), .Clr(not_1_out), .Q(SP[31:16]));  // open: nQ
  D_FF_AS #(.Bits(16)) SPL (.Set(1'b0), .D(D4), .C(demultiplexer_2_out_1), .Clr(not_1_out), .Q(SP[15:0]));  // open: nQ
  D_FF_AS #(.Bits(16)) FPH (.Set(1'b0), .D(D3), .C(demultiplexer_1_out_2), .Clr(not_1_out), .Q(FP[31:16]));  // open: nQ
  D_FF_AS #(.Bits(16)) FPL (.Set(1'b0), .D(D4), .C(demultiplexer_2_out_2), .Clr(not_1_out), .Q(FP[15:0]));  // open: nQ
  D_FF_AS #(.Bits(16)) BPH (.Set(1'b0), .D(D3), .C(demultiplexer_1_out_3), .Clr(not_1_out), .Q(BP[31:16]));  // open: nQ
  D_FF_AS #(.Bits(16)) BPL (.Set(1'b0), .D(D4), .C(demultiplexer_2_out_3), .Clr(not_1_out), .Q(BP[15:0]));  // open: nQ
  Decoder #(.Selector_Bits(2)) decoder_1 (
    .sel(S3), .out_0(decoder_1_out_0), .out_1(decoder_1_out_1), .out_2(decoder_1_out_2),
    .out_3(decoder_1_out_3));
  assign MP_H = decoder_1_out_0 ? PC[31:16] : 16'bz;  // Driver driver_1
  assign MP_L = decoder_1_out_0 ? PC[15:0] : 16'bz;  // Driver driver_2
  assign MP_H = decoder_1_out_1 ? SP[31:16] : 16'bz;  // Driver driver_3
  assign MP_L = decoder_1_out_1 ? SP[15:0] : 16'bz;  // Driver driver_4
  assign MP_H = decoder_1_out_2 ? FP[31:16] : 16'bz;  // Driver driver_5
  assign MP_L = decoder_1_out_2 ? FP[15:0] : 16'bz;  // Driver driver_6
  assign MP_H = decoder_1_out_3 ? BP[31:16] : 16'bz;  // Driver driver_7
  assign MP_L = decoder_1_out_3 ? BP[15:0] : 16'bz;  // Driver driver_8

  // Other names for the same wires on the sheet: BPH[15:0] = BP[31:16]; BPL[15:0] = BP[15:0]; FPH[15:0] = FP[31:16];
  //   FPL[15:0] = FP[15:0]; PCH[15:0] = PC[31:16]; PCL[15:0] = PC[15:0]; SPH[15:0] = SP[31:16]; SPL[15:0] = SP[15:0]
endmodule
