// Digital circuit Offset selector.dig as structural Verilog
module Offset_selector (
  input  [31:0] Off_in,
  input  \byte ,
  input  [1:0] Off_sel,
  output [31:0] Off_out
);

  wire decoder_1_out_0, decoder_1_out_1, decoder_1_out_2, decoder_1_out_3;
  wire [1:1] not_1_out;

  not not_1 (not_1_out[1], \byte );
  Decoder #(.Selector_Bits(2)) decoder_1 (
    .sel(Off_sel), .out_0(decoder_1_out_0), .out_1(decoder_1_out_1), .out_2(decoder_1_out_2),
    .out_3(decoder_1_out_3));
  assign Off_out = decoder_1_out_0 ? {32{1'b0}} : 32'bz;  // Driver driver_1
  assign Off_out = decoder_1_out_1 ? {{30{1'b0}}, not_1_out[1], \byte } : 32'bz;  // Driver driver_2
  assign Off_out = decoder_1_out_2 ? 32'hfffffffc : 32'bz;  // Driver driver_3
  assign Off_out = decoder_1_out_3 ? Off_in : 32'bz;  // Driver driver_4

  // Notes on the sheet:
  //   Off_in: Offset value from bus
  //   Off_out: Offset value to adder
  //   Off_sel: Select offset value:
  //   00 = 0
  //   01 = 1 or 2, depending on byte signal
  //   10 = -4
  //   11 = offset from bus
endmodule
