// Digital circuit 1-to-16b extender.dig as structural Verilog
module _1_to_16b_extender (
  input  in,
  output [15:0] out
);


  assign out = {16{in}};

  // Notes on the sheet:
  //   1-to-16 bit extender
endmodule
