// Digital circuit Bus buffer.dig as structural Verilog
module Bus_buffer (
  input  nEnable,
  input  [15:0] Data_in,
  output [15:0] Data_out
);

  _74244 _74244_1 (
    .pin1(nEnable), .pin2(Data_in[0]), .pin3(Data_out[1]), .pin4(Data_in[2]), .pin5(Data_out[3]),
    .pin6(Data_in[4]), .pin7(Data_out[5]), .pin8(Data_in[6]), .pin9(Data_out[7]), .pin10(1'b0),
    .pin11(Data_in[7]), .pin12(Data_out[6]), .pin13(Data_in[5]), .pin14(Data_out[4]), .pin15(Data_in[3]),
    .pin16(Data_out[2]), .pin17(Data_in[1]), .pin18(Data_out[0]), .pin19(nEnable), .pin20(1'b1));
  _74244 _74244_2 (
    .pin1(nEnable), .pin2(Data_in[8]), .pin3(Data_out[9]), .pin4(Data_in[10]), .pin5(Data_out[11]),
    .pin6(Data_in[12]), .pin7(Data_out[13]), .pin8(Data_in[14]), .pin9(Data_out[15]), .pin10(1'b0),
    .pin11(Data_in[15]), .pin12(Data_out[14]), .pin13(Data_in[13]), .pin14(Data_out[12]),
    .pin15(Data_in[11]), .pin16(Data_out[10]), .pin17(Data_in[9]), .pin18(Data_out[8]), .pin19(nEnable),
    .pin20(1'b1));
endmodule
