// Digital circuit Register_8bit.dig as structural Verilog
module Register_8bit (
  input  nR,
  input  [7:0] D_in,
  input  Clk,
  output [7:0] D_out
);

  _74273 _74273_1 (
    .pin1(nR), .pin2(D_out[0]), .pin3(D_in[0]), .pin4(D_in[2]), .pin5(D_out[2]), .pin6(D_out[4]),
    .pin7(D_in[4]), .pin8(D_in[6]), .pin9(D_out[6]), .pin10(1'b0), .pin11(Clk), .pin12(D_out[7]),
    .pin13(D_in[7]), .pin14(D_in[5]), .pin15(D_out[5]), .pin16(D_out[3]), .pin17(D_in[3]), .pin18(D_in[1]),
    .pin19(D_out[1]), .pin20(1'b1));
endmodule
