// Digital circuit Caclulating core interface simplified.dig as structural Verilog
module Caclulating_core_interface_simplified (
  input  ALU_Step,
  input  MOV_state,
  input  [15:0] I_in,
  input  ALU_state,
  output [2:0] Function,
  output Const_enable,
  output Sub_Inv_Rev,
  output Arithm,
  output Enable_C_in_RotC,
  output nCMP,
  output Src2_ind,
  output Src1___eq__Dest
);

  wire nand_1_out, nand_2_out, nand_3_out, nand_4_out, nand_5_out, nand_6_out, nand_7_out, nand_8_out,
       nand_9_out, nand_10_out, nand_11_out, nand_12_out, not_1_out, not_2_out, not_3_out, not_4_out,
       not_5_out, not_6_out, not_7_out, not_11_out, not_13_out, or_1_out, or_2_out;

  not not_1 (not_1_out, I_in[11]);
  not not_2 (not_2_out, I_in[13]);
  not not_3 (not_3_out, I_in[14]);
  nand nand_1 (nand_1_out, not_2_out, not_3_out);
  nand nand_2 (nand_2_out, not_1_out, I_in[3]);
  nand nand_3 (nand_3_out, not_1_out, not_4_out);
  nand nand_4 (nand_4_out, not_1_out, nand_1_out);
  nand nand_5 (nand_5_out, not_1_out, nand_3_out);
  not not_4 (not_4_out, I_in[4]);
  not not_5 (not_5_out, nand_4_out);
  not not_6 (not_6_out, nand_2_out);
  not not_7 (not_7_out, nand_3_out);
  nand nand_6 (nand_6_out, not_7_out, I_in[3], nand_1_out);
  nand nand_7 (nand_7_out, I_in[3], not_4_out, ALU_Step, not_5_out);
  nand nand_8 (nand_8_out, ALU_Step, nand_7_out, not_6_out);
  nand nand_9 (nand_9_out, nand_6_out, ALU_Step, I_in[14]);
  nand nand_10 (nand_10_out, nand_6_out, ALU_Step, I_in[13]);
  not not_8 (Function[1], nand_9_out);
  not not_9 (Enable_C_in_RotC, nand_8_out);
  and and_1 (Arithm, ALU_Step, I_in[2]);
  and and_2 (Const_enable, ALU_Step, I_in[11]);
  and and_3 (Sub_Inv_Rev, I_in[12], ALU_Step);
  and and_4 (Function[2], ALU_Step, nand_5_out);
  not not_10 (nCMP, nand_7_out);
  not not_11 (not_11_out, Function[2]);
  nand nand_11 (nand_11_out, Sub_Inv_Rev, not_11_out, Function[1], nand_10_out);
  not not_12 (Function[0], nand_10_out);
  or or_1 (or_1_out, MOV_state, ALU_state);
  nand nand_12 (nand_12_out, not_1_out, Function[2]);
  not not_13 (not_13_out, or_1_out);
  nand nand_13 (Src2_ind, nand_12_out, nand_11_out);
  or or_2 (or_2_out, not_13_out, Const_enable);
  not not_14 (Src1___eq__Dest, or_2_out);

  // Other names for the same wires on the sheet: i2 = I_in[2]; i3 = I_in[3]; i4 = I_in[4]; i11 = I_in[11];
  //   i12 = I_in[12]; i13 = I_in[13]; i14 = I_in[14]; i15 = I_in[15]; oAr = Arithm; oCMPi = nCMP;
  //   oConst_e = Const_enable; oEnCin = Enable_C_in_RotC; oF0 = Function[0]; oF1 = Function[1]; oF2 = Function[2];
  //   oS2i = Src2_ind; oSub = Sub_Inv_Rev

  // Notes on the sheet:
  //   Arithm: Arythmetic shift (for SHR only)
  //   Enable_C_in_RotC: Use carry in for ADDC, SUBC, RORC, ROLC
  //   nCMP: Compare instruction, signal to prevent write to register
  //   Src1___eq__Dest: Use destination address also as a source address
  //   I_in: Instruction word from IR
  //   ALU operation decoder
  //   Show Src2 for ops that use it:
  //   2-src arythm/logic, and rot (1, 4, 5, 6, 7)
endmodule
