// Digital circuit Caclulating core interface_gates.dig as structural Verilog
module Caclulating_core_interface_gates (
  input  ALU_Step,
  input  nr,
  input  L1,
  input  E1,
  input  clk,
  input  C_in,
  input  MOV_Step,
  input  [15:0] I_in,
  output [2:0] Function,
  output Const_enable,
  output Sub_Inv_Rev,
  output Arithm,
  output Enable_C_in_RotC,
  output nCMP,
  output ALU_instr,
  output Src2_ind,
  output [2:0] Src2,
  output [2:0] Src1,
  output [2:0] Dest,
  output [7:0] Const,
  output nr_o,
  output clk_o,
  output L1_o,
  output E1_o,
  output Carry,
  output E2,
  output Src1__eq__Dest
);

  wire nand_1_out, nand_2_out, nand_3_out, nand_4_out, nand_5_out, nand_6_out, nand_7_out, nand_8_out,
       nand_9_out, nand_10_out, nand_11_out, nand_12_out, nand_13_out, not_1_out, not_2_out, not_3_out,
       not_4_out, not_5_out, not_6_out, not_7_out, not_8_out, not_9_out, not_13_out, not_14_out;

  not not_1 (not_1_out, I_in[11]);
  not not_2 (not_2_out, I_in[13]);
  not not_3 (not_3_out, I_in[14]);
  nand nand_1 (nand_1_out, not_2_out, not_3_out);
  nand nand_2 (nand_2_out, not_1_out, I_in[3]);
  nand nand_3 (nand_3_out, not_1_out, not_4_out);
  nand nand_4 (nand_4_out, not_1_out, nand_1_out);
  nand nand_5 (nand_5_out, not_1_out, nand_3_out);
  not not_4 (not_4_out, I_in[4]);
  not not_5 (not_5_out, nand_4_out);
  not not_6 (not_6_out, nand_2_out);
  not not_7 (not_7_out, nand_3_out);
  nand nand_6 (nand_6_out, not_7_out, I_in[3], nand_1_out);
  not not_8 (not_8_out, MOV_Step);
  not not_9 (not_9_out, ALU_Step);
  nand nand_7 (nand_7_out, I_in[3], not_4_out, ALU_Step, not_5_out);
  nand nand_8 (nand_8_out, ALU_Step, nand_7_out, not_6_out);
  nand nand_9 (nand_9_out, nand_6_out, ALU_Step, I_in[14]);
  nand nand_10 (nand_10_out, nand_6_out, ALU_Step, I_in[13]);
  not not_10 (Function[1], nand_9_out);
  not not_11 (Enable_C_in_RotC, nand_8_out);
  and and_1 (Arithm, ALU_Step, I_in[2]);
  and and_2 (Const_enable, ALU_Step, I_in[11]);
  and and_3 (Sub_Inv_Rev, I_in[12], ALU_Step);
  and and_4 (Function[2], ALU_Step, nand_5_out);
  not not_12 (nCMP, nand_7_out);
  not not_13 (not_13_out, Const_enable);
  not not_14 (not_14_out, Function[2]);
  nand nand_11 (nand_11_out, Sub_Inv_Rev, not_14_out, Function[1], nand_10_out);
  not not_15 (Function[0], nand_10_out);
  nand nand_12 (nand_12_out, not_8_out, not_9_out);
  nand nand_13 (nand_13_out, not_1_out, Function[2]);
  nand nand_14 (Src1__eq__Dest, nand_12_out, not_13_out);
  nand nand_15 (Src2_ind, nand_13_out, nand_11_out);

  assign ALU_instr = ALU_Step;
  assign Carry = C_in;
  assign clk_o = clk;
  assign Const = I_in[7:0];
  assign Dest = I_in[10:8];
  assign E1_o = E1;
  assign E2 = ALU_Step;
  assign L1_o = L1;
  assign nr_o = nr;
  assign Src1 = I_in[7:5];
  assign Src2 = I_in[2:0];

  // Other names for the same wires on the sheet: i2 = I_in[2]; i3 = I_in[3]; i4 = I_in[4]; i11 = I_in[11];
  //   i12 = I_in[12]; i13 = I_in[13]; i14 = I_in[14]; oAr = Arithm; oCMPi = nCMP; oConst_e = Const_enable;
  //   oEnCin = Enable_C_in_RotC; oF0 = Function[0]; oF1 = Function[1]; oF2 = Function[2]; oS2i = Src2_ind;
  //   oSD = Src1__eq__Dest; oSub = Sub_Inv_Rev

  // Notes on the sheet:
  //   Arithm: Arythmetic shift (for SHR only)
  //   Enable_C_in_RotC: Use carry in for ADDC, SUBC, RORC, ROLC
  //   nCMP: Compare instruction, signal to prevent write to register
  //   ALU_instr: 0 -- Display E1 indication
  //   1 -- Display Src1 and Src2 indications
  //   nr: Reset
  //   L1: Latch data to GPR
  //   E1: Enable GPR to data bus
  //   nr_o: Reset
  //   clk_o: clock signal
  //   L1_o: Latch data to GPR
  //   E1_o: Enable GPR to Data bus
  //   C_in: "Carry in" signal
  //   Carry: Carry_in signal
  //   E2: Enable ALU output to Data bus
  //   Src1__eq__Dest: Use destination address also as a source address
  //   I_in: Instruction word from IR
  //   ALU operation decoder +
  //   RF addressing
  //   Show Src2 for ops that use it:
  //   2-src arythm/logic, and rot (1, 4, 5, 6, 7)
endmodule
