// Digital circuit Microinstruction decoder.dig as structural Verilog
module Microinstruction_decoder (
  input  [15:0] Instruction,
  input  ALU_state,
  input  MOV_state,
  input  Ld_MAB_state,
  input  p_i_MP_state,
  input  LDi_state,
  input  LD_ST_direct_state,
  input  LD_ST__MP__state,
  input  Addr_arithm_state,
  input  misc_state,
  input  Fetch1_state,
  input  Fetch2_state,
  input  Fetch_int_state,
  input  EINT_state,
  input  Push_PC_state,
  input  Jump_state,
  input  clk,
  input  [3:0] src_mod,
  input  [3:0] dest_mod,
  input  SP_4_state,
  output [15:0] Select_bits,
  output [8:0] Enable_bits,
  output [9:0] Latch_bits,
  output Soft_int,
  output prefix,
  output clk_stop,
  output NOP,
  output [2:0] Function,
  output Const_enable,
  output Sub_Inv_Rev,
  output Arithm,
  output Enable_C_in_RotC,
  output nCMP,
  output Src1___eq__Dest,
  output RST
);

  wire and_1_out, and_2_out, and_3_out, and_4_out, and_5_out, and_6_out, and_7_out, and_8_out, and_9_out,
       and_10_out, and_11_out, and_12_out, and_13_out, and_14_out, and_15_out, and_16_out, and_17_out,
       and_18_out, and_19_out, and_20_out, and_21_out, and_22_out, and_23_out, and_24_out, and_25_out,
       and_26_out, and_27_out, and_28_out, and_29_out, and_30_out, and_31_out, and_40_out, and_41_out,
       and_42_out, and_43_out, and_44_out, and_45_out, and_46_out, and_47_out, and_48_out, and_49_out,
       and_50_out, and_51_out, and_52_out, and_53_out, and_54_out, and_55_out, and_56_out, and_57_out,
       and_58_out, and_59_out, and_60_out, and_61_out, and_62_out, and_63_out, and_64_out, and_65_out,
       and_66_out, and_67_out, and_68_out, and_69_out, and_70_out, and_71_out, and_76_out, CLIM, clk_stop_t,
       decoder_1_out_0, decoder_1_out_1, decoder_1_out_2, decoder_1_out_3, decoder_2_out_0, decoder_2_out_1,
       decoder_2_out_2, decoder_2_out_3, decoder_3_out_0, decoder_3_out_1, decoder_3_out_2, decoder_3_out_3,
       decoder_3_out_4, decoder_3_out_5, decoder_3_out_6, decoder_3_out_7, nand_1_out, nand_2_out, not_1_out,
       not_2_out, not_3_out, not_4_out, not_5_out, not_6_out, not_7_out, not_8_out, not_9_out, not_10_out,
       not_11_out, not_12_out, not_13_out, not_14_out, not_15_out, not_16_out, not_17_out, not_18_out,
       or_1_out, or_2_out, or_3_out, or_4_out, or_5_out, or_6_out, or_7_out, or_8_out, or_9_out, or_10_out,
       or_11_out, or_12_out, or_13_out, or_15_out, or_16_out, or_18_out, or_19_out, or_20_out, or_21_out,
       or_22_out, or_23_out, or_24_out, or_25_out, or_26_out, or_27_out, or_28_out, or_29_out, or_30_out,
       or_32_out, or_34_out, or_35_out, or_37_out, or_38_out, or_39_out, or_40_out, or_41_out, or_43_out,
       or_44_out, or_45_out, or_46_out, or_47_out, or_48_out, or_49_out, or_50_out, or_51_out, or_52_out,
       or_53_out, or_54_out, or_55_out, or_56_out, or_58_out, or_59_out, or_60_out, or_61_out, or_62_out,
       or_63_out, or_64_out, or_66_out, or_67_out, or_68_out, or_69_out, or_70_out, or_71_out, or_72_out,
       or_73_out, or_74_out, or_76_out, or_77_out, or_78_out, or_79_out, or_80_out, or_81_out, or_82_out,
       or_83_out, or_84_out, or_85_out, or_86_out, or_87_out, or_88_out, or_89_out, or_90_out, or_91_out,
       or_93_out, or_94_out, or_95_out, or_97_out, or_101_out, or_104_out, or_105_out, or_106_out,
       or_109_out, or_111_out, or_112_out, or_113_out, or_117_out, or_118_out, or_119_out, pulldown_1_out,
       pulldown_2_out, pulldown_3_out, pulldown_4_out, pulldown_5_out, pulldown_6_out, pulldown_7_out,
       pulldown_8_out, pulldown_9_out, pulldown_10_out, pulldown_11_out, pulldown_12_out, pulldown_13_out,
       pulldown_14_out, pulldown_15_out, pulldown_16_out, pulldown_17_out, pulldown_18_out, pulldown_19_out,
       pulldown_20_out, pulldown_21_out, pulldown_22_out, pulldown_23_out, pulldown_24_out, pulldown_25_out,
       pulldown_26_out, pulldown_27_out, pulldown_28_out, pulldown_29_out, pulldown_30_out, pulldown_31_out,
       pulldown_32_out, pulldown_33_out, pulldown_34_out, pulldown_35_out, SETIM;

  PullDown pulldown_1 (.out(pulldown_1_out));
  PullDown pulldown_2 (.out(pulldown_2_out));
  PullDown pulldown_3 (.out(pulldown_3_out));
  PullDown pulldown_4 (.out(pulldown_4_out));
  PullDown pulldown_5 (.out(pulldown_5_out));
  PullDown pulldown_6 (.out(pulldown_6_out));
  PullDown pulldown_7 (.out(pulldown_7_out));
  PullDown pulldown_8 (.out(pulldown_8_out));
  PullDown pulldown_9 (.out(pulldown_9_out));
  PullDown pulldown_10 (.out(pulldown_10_out));
  PullDown pulldown_11 (.out(pulldown_11_out));
  PullDown pulldown_12 (.out(pulldown_12_out));
  PullDown pulldown_13 (.out(pulldown_13_out));
  PullDown pulldown_14 (.out(pulldown_14_out));
  PullDown pulldown_15 (.out(pulldown_15_out));
  PullDown pulldown_16 (.out(pulldown_16_out));
  PullDown pulldown_17 (.out(pulldown_17_out));
  PullDown pulldown_18 (.out(pulldown_18_out));
  PullDown pulldown_19 (.out(pulldown_19_out));
  PullDown pulldown_20 (.out(pulldown_20_out));
  PullDown pulldown_21 (.out(pulldown_21_out));
  PullDown pulldown_22 (.out(pulldown_22_out));
  PullDown pulldown_23 (.out(pulldown_23_out));
  PullDown pulldown_24 (.out(pulldown_24_out));
  PullDown pulldown_25 (.out(pulldown_25_out));
  PullDown pulldown_26 (.out(pulldown_26_out));
  PullDown pulldown_27 (.out(pulldown_27_out));
  PullDown pulldown_28 (.out(pulldown_28_out));
  PullDown pulldown_29 (.out(pulldown_29_out));
  PullDown pulldown_30 (.out(pulldown_30_out));
  PullDown pulldown_31 (.out(pulldown_31_out));
  PullDown pulldown_32 (.out(pulldown_32_out));
  PullDown pulldown_33 (.out(pulldown_33_out));
  PullDown pulldown_34 (.out(pulldown_34_out));
  PullDown pulldown_35 (.out(pulldown_35_out));
  or or_1 (or_1_out, Fetch1_state, pulldown_5_out);
  or or_2 (or_2_out, Fetch1_state, pulldown_9_out);
  or or_3 (or_3_out, Fetch1_state, pulldown_22_out);
  or or_4 (or_4_out, Fetch1_state, pulldown_26_out);
  or or_5 (or_5_out, Fetch1_state, pulldown_29_out);
  or or_6 (or_6_out, Fetch1_state, pulldown_30_out);
  or or_7 (or_7_out, Fetch2_state, or_1_out);
  or or_8 (or_8_out, Fetch2_state, or_2_out);
  or or_9 (or_9_out, Fetch2_state, or_3_out);
  or or_10 (or_10_out, Fetch2_state, pulldown_24_out);
  or or_11 (or_11_out, Fetch2_state, or_5_out);
  or or_12 (or_12_out, Fetch2_state, or_6_out);
  or or_13 (or_13_out, Fetch2_state, pulldown_32_out);
  or or_14 (Select_bits[0], Fetch_int_state, pulldown_1_out);
  or or_15 (or_15_out, Fetch_int_state, or_4_out);
  not not_1 (not_1_out, Instruction[4]);
  not not_2 (not_2_out, Instruction[11]);
  or or_16 (or_16_out, Instruction[13], Instruction[14]);
  or or_17 (Enable_bits[1], ALU_state, pulldown_18_out);
  or or_18 (or_18_out, ALU_state, pulldown_27_out);
  or or_19 (or_19_out, ALU_state, pulldown_28_out);
  Decoder #(.Selector_Bits(2)) decoder_1 (
    .sel(Instruction[1:0]), .out_0(decoder_1_out_0), .out_1(decoder_1_out_1), .out_2(decoder_1_out_2),
    .out_3(decoder_1_out_3));
  and and_1 (and_1_out, not_3_out, MOV_state, Instruction[3]);
  not not_3 (not_3_out, Instruction[2]);
  and and_2 (and_2_out, Instruction[2], MOV_state, Instruction[3]);
  not not_4 (not_4_out, src_mod[0]);
  not not_5 (not_5_out, dest_mod[0]);
  not not_6 (not_6_out, dest_mod[3]);
  and and_3 (and_3_out, src_mod[0], MOV_state);
  and and_4 (and_4_out, not_4_out, MOV_state);
  and and_5 (and_5_out, src_mod[1], MOV_state);
  and and_6 (and_6_out, src_mod[2], MOV_state);
  and and_7 (and_7_out, src_mod[3], MOV_state);
  and and_8 (and_8_out, not_5_out, Instruction[11], MOV_state);
  and and_9 (and_9_out, MOV_state, Instruction[11], dest_mod[0]);
  and and_10 (and_10_out, dest_mod[1], MOV_state);
  and and_11 (and_11_out, dest_mod[2], MOV_state);
  and and_12 (and_12_out, not_6_out, MOV_state);
  not not_7 (not_7_out, and_2_out);
  and and_13 (and_13_out, not_7_out, and_8_out);
  and and_14 (and_14_out, not_7_out, and_9_out);
  and and_15 (and_15_out, not_7_out, and_12_out);
  and and_16 (and_16_out, Instruction[3], not_1_out, not_2_out);
  and and_17 (and_17_out, Instruction[3], not_2_out);
  not not_8 (not_8_out, and_1_out);
  and and_18 (and_18_out, not_2_out, Instruction[4]);
  not not_9 (not_9_out, Instruction[3]);
  and and_19 (and_19_out, decoder_1_out_3, and_1_out);
  and and_20 (and_20_out, not_8_out, and_3_out);
  and and_21 (and_21_out, not_8_out, and_4_out);
  and and_22 (and_22_out, not_9_out, Instruction[14]);
  and and_23 (and_23_out, Instruction[4], Instruction[14]);
  and and_24 (and_24_out, Instruction[11], Instruction[14]);
  and and_25 (and_25_out, Instruction[14], Instruction[13]);
  and and_26 (and_26_out, decoder_1_out_2, and_1_out);
  or or_20 (or_20_out, and_10_out, pulldown_15_out);
  or or_21 (or_21_out, and_11_out, pulldown_16_out);
  and and_27 (and_27_out, and_16_out, or_16_out);
  not not_10 (not_10_out, and_18_out);
  or or_22 (or_22_out, and_7_out, pulldown_2_out);
  not not_11 (not_11_out, and_27_out);
  or or_23 (or_23_out, and_22_out, and_23_out, and_24_out, and_25_out);
  and and_28 (and_28_out, decoder_1_out_1, and_1_out);
  or or_24 (or_24_out, and_6_out, pulldown_3_out);
  or or_25 (or_25_out, and_5_out, pulldown_4_out);
  and and_29 (and_29_out, not_11_out, and_17_out);
  or or_26 (or_26_out, and_21_out, pulldown_17_out);
  or or_27 (or_27_out, and_20_out, pulldown_20_out);
  and and_30 (and_30_out, decoder_1_out_3, and_2_out);
  or or_28 (or_28_out, and_15_out, or_18_out);
  or or_29 (or_29_out, and_14_out, or_11_out);
  or or_30 (or_30_out, and_13_out, or_12_out);
  or or_31 (Enable_bits[2], and_28_out, pulldown_19_out);
  or or_32 (or_32_out, and_26_out, pulldown_21_out);
  or or_33 (Enable_bits[6], and_19_out, pulldown_23_out);
  and and_31 (and_31_out, decoder_1_out_2, and_2_out);
  and and_32 (Arithm, ALU_state, Instruction[2]);
  and and_33 (Sub_Inv_Rev, Instruction[12], ALU_state);
  and and_34 (nCMP, ALU_state, and_27_out);
  and and_35 (Enable_C_in_RotC, ALU_state, and_29_out);
  and and_36 (Const_enable, ALU_state, Instruction[11]);
  and and_37 (Function[2], ALU_state, not_10_out);
  and and_38 (Function[1], ALU_state, or_23_out);
  and and_39 (Function[0], ALU_state, Instruction[13]);
  and and_40 (and_40_out, decoder_1_out_1, and_2_out);
  or or_34 (or_34_out, and_30_out, pulldown_34_out);
  or or_35 (or_35_out, MOV_state, ALU_state);
  or or_36 (Select_bits[6], and_40_out, pulldown_7_out);
  or or_37 (or_37_out, and_40_out, or_19_out);
  or or_38 (or_38_out, and_31_out, or_13_out);
  not not_12 (not_12_out, or_35_out);
  or or_39 (or_39_out, not_12_out, Const_enable);
  not not_13 (not_13_out, or_39_out);
  or or_40 (or_40_out, Ld_MAB_state, pulldown_31_out);
  or or_41 (or_41_out, Ld_MAB_state, or_38_out);
  or or_42 (Src1___eq__Dest, and_68_out, Ld_MAB_state, not_13_out);
  and and_41 (and_41_out, Instruction[0], Ld_MAB_state);
  and and_42 (and_42_out, Instruction[1], Ld_MAB_state);
  and and_43 (and_43_out, Ld_MAB_state, Instruction[2]);
  not not_14 (not_14_out, Instruction[2]);
  and and_44 (and_44_out, not_14_out, Ld_MAB_state);
  and and_45 (and_45_out, Instruction[3], Ld_MAB_state);
  and and_46 (and_46_out, Ld_MAB_state, Instruction[3]);
  and and_47 (and_47_out, Ld_MAB_state, Instruction[3], Instruction[4]);
  or or_43 (or_43_out, and_41_out, or_22_out);
  or or_44 (or_44_out, and_47_out, or_29_out);
  or or_45 (or_45_out, and_47_out, or_30_out);
  or or_46 (or_46_out, and_42_out, or_24_out);
  or or_47 (or_47_out, and_47_out, or_7_out);
  and and_48 (and_48_out, and_41_out, and_47_out);
  and and_49 (and_49_out, and_42_out, and_47_out);
  or or_48 (or_48_out, and_46_out, or_8_out);
  or or_49 (or_49_out, and_45_out, pulldown_10_out);
  or or_50 (or_50_out, and_44_out, or_26_out);
  or or_51 (or_51_out, and_43_out, or_32_out);
  or or_52 (or_52_out, and_48_out, or_20_out);
  or or_53 (or_53_out, and_49_out, or_21_out);
  or or_54 (or_54_out, LD_ST__MP__state, pulldown_8_out);
  or or_55 (or_55_out, LD_ST__MP__state, or_48_out);
  or or_56 (or_56_out, LD_ST__MP__state, pulldown_11_out);
  or or_57 (Select_bits[13], LD_ST__MP__state, pulldown_14_out);
  or or_58 (or_58_out, LD_ST__MP__state, or_40_out);
  or or_59 (or_59_out, LD_ST_direct_state, LD_ST__MP__state);
  not not_15 (not_15_out, dest_mod[0]);
  and and_50 (and_50_out, dest_mod[0], or_59_out);
  and and_51 (and_51_out, dest_mod[1], or_59_out);
  and and_52 (and_52_out, dest_mod[2], or_59_out);
  not not_16 (not_16_out, Instruction[12]);
  and and_53 (and_53_out, or_59_out, not_15_out);
  and and_54 (and_54_out, or_59_out, not_16_out);
  and and_55 (and_55_out, Instruction[12], or_59_out);
  or or_60 (or_60_out, and_51_out, or_43_out);
  or or_61 (or_61_out, and_52_out, or_46_out);
  or or_62 (or_62_out, and_51_out, or_52_out);
  or or_63 (or_63_out, and_52_out, or_53_out);
  or or_64 (or_64_out, and_50_out, or_25_out);
  or or_65 (Enable_bits[5], and_54_out, or_9_out);
  or or_66 (or_66_out, and_54_out, or_10_out);
  or or_67 (or_67_out, and_55_out, pulldown_25_out);
  or or_68 (or_68_out, and_55_out, pulldown_35_out);
  Decoder #(.Selector_Bits(2)) decoder_2 (
    .sel({Instruction[12], dest_mod[3]}), .out_0(decoder_2_out_0), .out_1(decoder_2_out_1),
    .out_2(decoder_2_out_2), .out_3(decoder_2_out_3));
  and and_56 (and_56_out, decoder_2_out_3, or_59_out);
  and and_57 (and_57_out, decoder_2_out_2, or_59_out);
  or or_69 (or_69_out, and_56_out, or_27_out);
  or or_70 (or_70_out, and_57_out, or_50_out);
  and and_58 (and_58_out, and_50_out, decoder_2_out_1);
  or or_71 (or_71_out, and_58_out, or_44_out);
  and and_59 (and_59_out, and_53_out, decoder_2_out_1);
  or or_72 (or_72_out, and_59_out, or_45_out);
  and and_60 (and_60_out, decoder_2_out_0, or_59_out);
  or or_73 (or_73_out, and_60_out, or_28_out);
  or or_74 (or_74_out, LD_ST_direct_state, pulldown_12_out);
  and and_61 (and_61_out, Instruction[9], LDi_state);
  and and_62 (and_62_out, Instruction[10], LDi_state);
  not not_17 (not_17_out, Instruction[11]);
  or or_75 (Select_bits[5], LDi_state, pulldown_6_out);
  or or_76 (or_76_out, LDi_state, or_51_out);
  and and_63 (and_63_out, LDi_state, not_17_out);
  and and_64 (and_64_out, Instruction[11], LDi_state);
  or or_77 (or_77_out, and_64_out, or_71_out);
  or or_78 (or_78_out, and_64_out, or_72_out);
  or or_79 (or_79_out, and_63_out, or_73_out);
  or or_80 (or_80_out, and_61_out, or_62_out);
  or or_81 (or_81_out, and_62_out, or_63_out);
  not not_18 (not_18_out, Instruction[8]);
  and and_65 (and_65_out, Instruction[8], Addr_arithm_state);
  and and_66 (and_66_out, Instruction[9], Addr_arithm_state);
  and and_67 (and_67_out, Instruction[10], Addr_arithm_state);
  or or_82 (or_82_out, Jump_state, p_i_MP_state, Addr_arithm_state);
  or or_83 (or_83_out, or_82_out, or_47_out);
  or or_84 (or_84_out, or_82_out, or_55_out);
  or or_85 (or_85_out, or_82_out, or_49_out);
  or or_86 (or_86_out, or_82_out, or_77_out);
  or or_87 (or_87_out, or_82_out, or_78_out);
  and and_68 (and_68_out, Addr_arithm_state, not_18_out);
  or or_88 (or_88_out, and_66_out, or_60_out);
  or or_89 (or_89_out, and_66_out, or_80_out);
  or or_90 (or_90_out, and_67_out, or_61_out);
  or or_91 (or_91_out, and_67_out, or_81_out);
  or or_92 (Enable_bits[0], and_68_out, or_70_out);
  or or_93 (or_93_out, or_94_out, or_76_out);
  or or_94 (or_94_out, p_i_MP_state, and_65_out);
  and and_69 (and_69_out, Instruction[0], p_i_MP_state);
  and and_70 (and_70_out, Instruction[1], p_i_MP_state);
  or or_95 (or_95_out, and_69_out, or_88_out);
  or or_96 (Select_bits[2], and_70_out, or_90_out);
  or or_97 (or_97_out, and_69_out, or_89_out);
  or or_98 (Select_bits[15], and_70_out, or_91_out);
  or or_99 (Enable_bits[4], Jump_state, or_93_out);
  or or_100 (Select_bits[1], SP_4_state, or_95_out);
  or or_101 (or_101_out, SP_4_state, or_83_out);
  or or_102 (Select_bits[9], SP_4_state, or_85_out);
  or or_103 (Select_bits[14], SP_4_state, or_97_out);
  or or_104 (or_104_out, SP_4_state, or_86_out);
  or or_105 (or_105_out, SP_4_state, or_87_out);
  or or_106 (or_106_out, SP_4_state, or_58_out);
  and and_71 (and_71_out, Push_PC_state, dest_mod[0]);
  or or_107 (Select_bits[7], Push_PC_state, or_54_out);
  or or_108 (Select_bits[8], Push_PC_state, or_84_out);
  or or_109 (or_109_out, Push_PC_state, or_56_out);
  or or_110 (Enable_bits[3], Push_PC_state, or_69_out);
  or or_111 (or_111_out, Push_PC_state, or_67_out);
  or or_112 (or_112_out, Push_PC_state, or_106_out);
  or or_113 (or_113_out, Push_PC_state, or_68_out);
  or or_114 (Select_bits[3], and_71_out, or_64_out);
  or or_115 (Select_bits[4], EINT_state, or_101_out);
  or or_116 (Select_bits[12], EINT_state, pulldown_13_out);
  or or_117 (or_117_out, EINT_state, or_104_out);
  or or_118 (or_118_out, EINT_state, or_105_out);
  Decoder #(.Selector_Bits(3)) decoder_3 (
    .sel(Instruction[10:8]), .out_0(decoder_3_out_0), .out_1(decoder_3_out_1), .out_2(decoder_3_out_2),
    .out_3(decoder_3_out_3), .out_4(decoder_3_out_4), .out_5(decoder_3_out_5), .out_6(decoder_3_out_6),
    .out_7(decoder_3_out_7));
  and and_72 (SETIM, misc_state, decoder_3_out_7);
  and and_73 (CLIM, misc_state, decoder_3_out_6);
  and and_74 (prefix, misc_state, decoder_3_out_5);
  and and_75 (Soft_int, misc_state, decoder_3_out_4);
  or or_119 (or_119_out, Soft_int, pulldown_33_out);
  and and_76 (and_76_out, misc_state, decoder_3_out_3);
  or or_120 (Select_bits[10], and_76_out, or_109_out);
  or or_121 (Select_bits[11], and_76_out, or_74_out);
  and and_77 (RST, misc_state, decoder_3_out_2);
  and and_78 (clk_stop_t, misc_state, decoder_3_out_1);
  and and_79 (NOP, misc_state, decoder_3_out_0);
  nand nand_1 (nand_1_out, or_66_out, or_111_out);
  nand nand_2 (nand_2_out, or_66_out, or_111_out);
  and and_80 (Enable_bits[7], or_66_out, nand_1_out);
  and and_81 (Enable_bits[8], nand_2_out, or_111_out);
  and and_82 (Latch_bits[0], or_15_out, clk);
  and and_83 (Latch_bits[1], or_79_out, clk);
  and and_84 (Latch_bits[2], or_37_out, clk);
  and and_85 (Latch_bits[3], or_117_out, clk);
  and and_86 (Latch_bits[4], or_118_out, clk);
  and and_87 (Latch_bits[5], or_112_out, clk);
  and and_88 (Latch_bits[6], or_41_out, clk);
  and and_89 (Latch_bits[7], or_119_out, clk);
  and and_90 (Latch_bits[8], or_34_out, clk);
  and and_91 (Latch_bits[9], or_113_out, clk);
  or or_122 (clk_stop, and_76_out, clk_stop_t);

  // Other names for the same wires on the sheet: i0 = Instruction[0]; i1 = Instruction[1]; i2 = Instruction[2];
  //   i3 = Instruction[3]; i4 = Instruction[4]; i5 = Instruction[5]; i6 = Instruction[6]; i7 = Instruction[7];
  //   i8 = Instruction[8]; i9 = Instruction[9]; iA = Instruction[10]; iB = Instruction[11]; iC = Instruction[12];
  //   iD = Instruction[13]; iE = Instruction[14]; iF = Instruction[15]; noCMP = nCMP; oAr = Arithm;
  //   oConst_e = Const_enable; oEnCin = Enable_C_in_RotC; oF0 = Function[0]; oF1 = Function[1]; oF2 = Function[2];
  //   oSub = Sub_Inv_Rev; reset_pulse = RST

  // Notes on the sheet:
  //   src_mod: MOV source register address, 
  //   modified by sequencer
  //   dest_mod: MOV destination address
  //   LD/ST destination/source address
  //   modified by sequencer
  //   Arithm: Arythmetic shift (for SHR only)
  //   Enable_C_in_RotC: Use carry in for ADDC, SUBC, RORC, ROLC
  //   nCMP: Compare instruction, signal to prevent write to register
  //   Src1___eq__Dest: Use destination address also as a source address
  //   SP_4_state: Load MAB with MP - 4 
  //   (S9 = 10; S3 = i1, i0; L5 = 1)
  //   i0
  //   i1
  //   i2
  //   i3
  //   i4
  //   i5
  //   i6
  //   i7
  //   i8
  //   i9
  //   iA
  //   iB
  //   iC
  //   iD
  //   iE
  //   iF
  //   S0
  //   S3_0
  //   S3_1
  //   S4
  //   S5
  //   S6
  //   S7
  //   S8
  //   S9_0
  //   S9_1
  //   S10_0
  //   S10_1
  //   S11
  //   S12
  //   LA3_0
  //   LA3_1
  //   E1
  //   E2
  //   E3
  //   E4
  //   E5
  //   E6
  //   E7
  //   T1
  //   T2
  //   L0
  //   L1
  //   L2
  //   L3
  //   L4
  //   L5
  //   L6
  //   L7
  //   L8
  //   W
  //   F1
  //   Fetch1
  //   Fetch states
  //   Fetch2
  //   F2
  //   F Int
  //   Fetch EInt
  //   ALU
  //   ALU state
  //   Sub / Invert B
  //   ~iB
  //   iD | iE
  //   MOV
  //   MOV state
  //   ~i4
  //   Flags
  //   MDB
  //   IntV
  //   read special
  //   write to special
  //   ~iB & ~i4 & i3
  //   ~iB & i3
  //   ~iB & i4
  //   i8 & iB
  //   ~i8 & iB
  //   ( iD | iE ) & ~iB & ~i4 & i3
  //   ( ~iB & i3 ) & !(( iD | iE ) & ~iB & ~i4 & i3)
  //   !( ~iB & i4 )
  //   rd IVB
  //   rd SR
  //   rd MDB
  //   Int V base wr
  //   Const
  //   L2, S7
  //   SR wr
  //   MDB wr
  //   Comparisons
  //   Carry
  //   Load MAB
  //   Execute states
  //   Pre-increment
  //   MP addr b0
  //   MP addr b1
  //   offset src
  //   bit 3 = 1, bit 4 = 0:
  //   ADD/SUB with carry      
  //   1000  1001 ADDC, SUBC
  //   and comparisons         
  //   1010  1011 TEQ, TCM
  //   1100  1101 CMN, CMP
  //   1110 1111 TST, TIB
  //   Func 210:
  //   100 -- ADD
  //   101 -- XOR
  //   110 -- OR
  //   111 -- AND
  //   If CMP -- substitute OR with ADD
  //   otherwise no substitution
  //   sel offset
  //   ~i2
  //   Microinstruction decoder
  //   LD/ST (MP)
  //   T2
  //   W
  //   ~iC
  //   L3, L4
  //   LD/ST (address)
  //   LDi
  //   L3,L4
  //   Address Arithm
  //   E5 (add imm val to addr)
  //   E1, SnotD (add GPR to addr)
  //   ~i8
  //   MP post-increment
  //   Jump
  //   SP - 4
  //   Push PC
  //   i8*
  //   EINT
  //   Codes for misc ops
  //   NOP just goes straight to Fetch1
  //   NOP
  //   HLT
  //   Reset
  //   Soft Interrupt
  //   Set Prefix
  //   Clear IM
  //   Set IM
  //   Misc
  //   Pause
  //   Sets a number of consecutive words that are to be loaded or stored
  //   Soft Interrupt has a step loading Interrupt #, and then goes straight to the EINT
  //   DMA sets address src selector to 0b11 and stops clock propagation into CPU
  //   Reset is a way to initiate reset sequence in software
  //   DMA
  //   HLT severs clock signals
endmodule
