// Digital circuit MultiWordEnabler.dig as structural Verilog
// This circuit substitues register addresses with counted ones for block transfers.
module MultiWordEnabler (
  input  clk,
  input  [15:0] Instr_in,
  input  block_size_Latch,
  input  load_cnt,
  input  \byte ,
  input  [1:0] word_cnt,
  input  R,
  input  Jump_instr,
  input  MAB_state,
  output Last,
  output Byte_2,
  output [3:0] src_mod,
  output [3:0] dest_mod
);

  wire _2w, _4w, _8w, _16w, _74163_1_pin9, _74163_1_pin11, _74163_1_pin12, _74163_1_pin13, _74163_1_pin14,
       and_1_out, and_2_out, and_3_out, and_4_out, and_5_out, and_6_out, and_7_out, and_8_out, and_9_out,
       d_ff_as_1_q, d_ff_as_2_q, d_ff_as_3_q, d_ff_as_4_q, multiplexer_2_out, multiplexer_3_out,
       multiplexer_4_out, multiplexer_5_out, not_1_out, not_2_out, not_3_out, not_5_out, not_6_out, or_1_out,
       or_2_out, or_3_out, or_4_out;
  wire [11:8] multiplexer_1_out;

  not not_1 (not_1_out, MAB_state);
  not not_2 (not_2_out, word_cnt[0]);
  not not_3 (not_3_out, word_cnt[1]);
  and and_1 (and_1_out, not_2_out, not_3_out);
  and and_2 (and_2_out, word_cnt[0], not_3_out);
  and and_3 (and_3_out, not_2_out, word_cnt[1]);
  and and_4 (and_4_out, word_cnt[0], word_cnt[1]);
  Multiplexer #(.Bits(4)) multiplexer_1 (
    .sel(Jump_instr), .in_0(Instr_in[11:8]), .in_1(4'b1000), .out(multiplexer_1_out));
  Multiplexer multiplexer_2 (.sel(\byte ), .in_0(and_1_out), .in_1(and_2_out), .out(multiplexer_2_out));
  Multiplexer multiplexer_3 (.sel(\byte ), .in_0(and_2_out), .in_1(and_3_out), .out(multiplexer_3_out));
  Multiplexer multiplexer_4 (.sel(\byte ), .in_0(and_3_out), .in_1(and_4_out), .out(multiplexer_4_out));
  Multiplexer multiplexer_5 (.sel(\byte ), .in_0(and_4_out), .in_1(1'b0), .out(multiplexer_5_out));
  or or_1 (or_1_out, and_5_out, R);
  D_FF_AS d_ff_as_1 (
    .Set(1'b0), .D(multiplexer_2_out), .C(block_size_Latch), .Clr(or_1_out), .Q(d_ff_as_1_q));  // open: nQ
  D_FF_AS d_ff_as_2 (
    .Set(1'b0), .D(multiplexer_3_out), .C(block_size_Latch), .Clr(or_1_out), .Q(d_ff_as_2_q));  // open: nQ
  D_FF_AS d_ff_as_3 (
    .Set(1'b0), .D(multiplexer_4_out), .C(block_size_Latch), .Clr(or_1_out), .Q(d_ff_as_3_q));  // open: nQ
  D_FF_AS d_ff_as_4 (
    .Set(1'b0), .D(multiplexer_5_out), .C(block_size_Latch), .Clr(or_1_out), .Q(d_ff_as_4_q));  // open: nQ
  D_FF_AS byte__flag (.Set(1'b0), .D(\byte ), .C(block_size_Latch), .Clr(or_1_out), .Q(Byte_2));  // open: nQ
  or or_2 (or_2_out, d_ff_as_3_q, d_ff_as_4_q);
  or or_3 (or_3_out, d_ff_as_2_q, or_2_out);
  _74163 _74163_1 (
    .pin1(1'b1), .pin2(clk), .pin3(_2w), .pin4(_4w), .pin5(_8w), .pin6(_16w), .pin7(1'b1), .pin8(1'b0),
    .pin9(_74163_1_pin9), .pin10(1'b1), .pin11(_74163_1_pin11), .pin12(_74163_1_pin12),
    .pin13(_74163_1_pin13), .pin14(_74163_1_pin14), .pin15(Last), .pin16(1'b1));
  not not_4 (_74163_1_pin9, load_cnt);
  or or_4 (or_4_out, d_ff_as_1_q, or_3_out);
  not not_5 (not_5_out, Last);
  not not_6 (not_6_out, not_5_out);
  and and_5 (and_5_out, not_6_out, not_5_out);
  and and_6 (and_6_out, or_4_out, not_1_out);
  and and_7 (and_7_out, or_3_out, not_1_out);
  and and_8 (and_8_out, or_2_out, not_1_out);
  and and_9 (and_9_out, not_1_out, d_ff_as_4_q);
  not not_7 (_2w, or_4_out);
  not not_8 (_4w, or_3_out);
  not not_9 (_8w, or_2_out);
  not not_10 (_16w, d_ff_as_4_q);
  Multiplexer multiplexer_6 (.sel(and_6_out), .in_0(Instr_in[5]), .in_1(_74163_1_pin14), .out(src_mod[1]));
  Multiplexer multiplexer_7 (.sel(and_7_out), .in_0(Instr_in[6]), .in_1(_74163_1_pin13), .out(src_mod[2]));
  Multiplexer multiplexer_8 (.sel(and_8_out), .in_0(Instr_in[7]), .in_1(_74163_1_pin12), .out(src_mod[3]));
  Multiplexer multiplexer_9 (.sel(and_9_out), .in_0(Instr_in[4]), .in_1(_74163_1_pin11), .out(src_mod[0]));
  LED led_1 (.in(src_mod[1]));
  LED led_2 (.in(src_mod[2]));
  LED led_3 (.in(src_mod[3]));
  LED led_4 (.in(src_mod[0]));
  Multiplexer multiplexer_10 (.sel(or_4_out), .in_0(multiplexer_1_out[8]), .in_1(_74163_1_pin14), .out(dest_mod[0]));
  Multiplexer multiplexer_11 (.sel(or_3_out), .in_0(multiplexer_1_out[9]), .in_1(_74163_1_pin13), .out(dest_mod[1]));
  Multiplexer multiplexer_12 (.sel(or_2_out), .in_0(multiplexer_1_out[10]), .in_1(_74163_1_pin12), .out(dest_mod[2]));
  Multiplexer multiplexer_13 (
    .sel(d_ff_as_4_q), .in_0(multiplexer_1_out[11]), .in_1(_74163_1_pin11), .out(dest_mod[3]));
  LED led_5 (.in(dest_mod[0]));
  LED led_6 (.in(dest_mod[1]));
  LED led_7 (.in(dest_mod[2]));
  LED led_8 (.in(dest_mod[3]));

  // Notes on the sheet:
  //   Instr_in: Instruction word input
  //   block_size_Latch: latching signal, sinchronous with main clock
  //   Last: last word of the block
  //   load_cnt: clocked input for loading counter value
  //   byte: byte flag
  //   this is a standalone self-removing flag that makes LD/ST ops
  //    to work with individual bytes
  //   Byte_2: "byte" flag value
  //   Jump_instr: Substitute CONZ value with PCH address (1000b)
  //   MAB_state: Feed original src value to RF
  //   during MAB state, so the correct offset
  //   is added to base address
  //   Block size flags
  //   Multi-word transfer enabler
endmodule
