// Digital circuit ECM-16 CPU.dig as structural Verilog
// Core component of the computer, performs calculations and computations
module ECM_16_CPU (
  input  [31:0] DMA_addr,
  input  [7:0] iN,
  input  clk,
  input  IRQ,
  input  nR,
  input  DMA_RQ,
  output [31:0] Address,
  output [15:0] Data,
  output [15:0] States_disp,
  output [63:0] r0_r3,
  output [63:0] r4_r7,
  output [15:0] IR,
  output [3:0] SR,
  output [15:0] MDB,
  output [31:0] PC,
  output [31:0] SP,
  output [31:0] FP,
  output [31:0] BP,
  output [31:0] MAB,
  output [31:0] Addr,
  output [31:0] IV,
  output [15:0] CW_SEL,
  output [8:0] CW_EN,
  output [9:0] CW_LATCH,
  output soft_int,
  output RST,
  output clk_stp,
  output \byte ,
  output write,
  output read,
  output iAck
);

  wire decoder_1_out_0, decoder_1_out_1, decoder_1_out_2, decoder_1_out_3, decoder_2_out_0, decoder_2_out_1,
       decoder_2_out_2, decoder_2_out_3, microinstruction_decoder_1_nop, nclk, nCMP, not_3_out, not_4_out,
       prefix, sequencer_1_addr_arithm_state, sequencer_1_alu_state, sequencer_1_eint_state,
       sequencer_1_fetch1_state, sequencer_1_fetch2_state, sequencer_1_fetch_int_state,
       sequencer_1_jump_state, sequencer_1_ld_mab_state, sequencer_1_ld_st__mp__state,
       sequencer_1_ldd_std_state, sequencer_1_ldi_state, sequencer_1_misc_state, sequencer_1_mov_state,
       sequencer_1_p_i_mp_state, sequencer_1_push_pc_state, sequencer_1_sp_4_state, SnotD;
  wire [1:0] or_1_out;
  wire [1:1] not_2_out;
  wire [3:0] dest_mod, main_alu_tristates_1_flags, multiplexer_5_out, src_mod;
  wire [6:0] ALU_signal;
  wire [7:0] _1_to_8b_extender_1_out, _1_to_8b_extender_2_out, _1_to_8b_extender_3_out, multiplexer_10_out;
  wire [15:0] _1_to_16b_extender_1_out, address_adder_1_out, address_adder_1_out_2, driver_1_out,
       GPR_src1_out, GPR_src1_to_bus, GPR_src2_out, Instruction_Register_d_out, main_alu_tristates_1_output,
       MP_mp_h, MP_mp_l, multiplexer_1_out, multiplexer_2_out, multiplexer_3_out, multiplexer_4_out,
       multiplexer_6_out, multiplexer_8_out, pullup_1_out, SBE_fr_cpu, SBE_fr_mem;
  wire [31:0] driver_5_out, multiplexer_7_out, multiplexer_9_out;

  not not_1 (nclk, clk);
  Multiplexer #(.Bits(16)) multiplexer_1 (
    .sel(CW_SEL[4]), .in_0(driver_1_out), .in_1(address_adder_1_out), .out(multiplexer_1_out));
  _1_to_8b_extender _1_to_8b_extender_1 (.in(IR[8]), .out(_1_to_8b_extender_1_out));
  Multiplexer #(.Bits(16)) multiplexer_2 (
    .sel(CW_SEL[5]), .in_0(driver_1_out), .in_1({_1_to_8b_extender_1_out, IR[7:0]}), .out(multiplexer_2_out));
  Multiplexer #(.Bits(16)) multiplexer_3 (
    .sel(CW_SEL[4]), .in_0(multiplexer_2_out), .in_1(address_adder_1_out_2), .out(multiplexer_3_out));
  _1_to_16b_extender _1_to_16b_extender_1 (.in(driver_1_out[15]), .out(_1_to_16b_extender_1_out));
  Register_file_gates_tristates GPR (
    .Src2_out(GPR_src2_out), .Src1_out(GPR_src1_out), .nr(nR), .nCMP(nCMP), .L1(CW_LATCH[1]),
    .S1__eq_D(SnotD), .Dest(dest_mod[2:0]), .Src1(src_mod[3:1]), .Src2(IR[2:0]), .D_in(driver_1_out),
    .R0_3(r0_r3), .R4_7(r4_r7), .Src1_to_bus(GPR_src1_to_bus));
  Main_ALU_tristates main_alu_tristates_1 (
    .Src2(GPR_src2_out), .Src1(GPR_src1_out), .Const(IR[7:0]), .Carry_in(SR[3]),
    .Const_enable(ALU_signal[0]), .Sub_Inv_Rev(ALU_signal[1]), .Arithm(ALU_signal[2]),
    .Enable_C_in_RotC(ALU_signal[3]), .Function(ALU_signal[6:4]), .Output(main_alu_tristates_1_output),
    .Flags(main_alu_tristates_1_flags));
  _1_to_8b_extender _1_to_8b_extender_2 (.in(IR[7]), .out(_1_to_8b_extender_2_out));
  assign driver_1_out = CW_EN[1] ? main_alu_tristates_1_output : 16'bz;  // Driver driver_1
  Memory_Pointers_gates_tristate MP (
    .nr(nR), .L3(CW_LATCH[3]), .L4(CW_LATCH[4]), .D3(multiplexer_3_out), .D4(multiplexer_1_out),
    .S3(CW_SEL[2:1]), .LA34(CW_SEL[15:14]), .PC(PC), .SP(SP), .FP(FP), .BP(BP), .MP_H(MP_mp_h), .MP_L(MP_mp_l));
  Multiplexer #(.Bits(16)) multiplexer_4 (
    .sel(CW_SEL[13]), .in_0({_1_to_8b_extender_2_out, IR[7:0]}), .in_1(_1_to_16b_extender_1_out),
    .out(multiplexer_4_out));
  Multiplexer #(.Bits(4)) multiplexer_5 (
    .sel(CW_SEL[6]), .in_0(main_alu_tristates_1_flags), .in_1(driver_1_out[3:0]), .out(multiplexer_5_out));
  Flags_Register_8bit Status_Register (.nR(nR), .Flags_in(multiplexer_5_out), .Clk(CW_LATCH[2]), .Flags_out(SR));
  not not_2 (not_2_out[1], \byte );
  PullUp #(.Bits(16)) pullup_1 (.out(pullup_1_out));
  assign driver_1_out = CW_EN[0] ? GPR_src1_to_bus : 16'bz;  // Driver driver_2
  assign driver_1_out = CW_EN[3] ? multiplexer_6_out : 16'bz;  // Driver driver_3
  Multiplexer #(.Bits(16)) multiplexer_6 (.sel(CW_SEL[3]), .in_0(MP_mp_h), .in_1(MP_mp_l), .out(multiplexer_6_out));
  Decoder #(.Selector_Bits(2)) decoder_1 (
    .sel(CW_SEL[9:8]), .out_0(decoder_1_out_0), .out_1(decoder_1_out_1), .out_2(decoder_1_out_2),
    .out_3(decoder_1_out_3));
  assign driver_1_out = CW_EN[2] ? {{12{1'b0}}, SR} : 16'bz;  // Driver driver_4
  Multiplexer #(.Bits(32)) multiplexer_7 (
    .sel(CW_SEL[7]), .in_0({MP_mp_h, MP_mp_l}), .in_1(MAB), .out(multiplexer_7_out));
  assign driver_5_out = decoder_1_out_0 ? {32{1'b0}} : 32'bz;  // Driver driver_5
  assign driver_5_out = decoder_1_out_1 ? {{30{1'b0}}, not_2_out[1], \byte } : 32'bz;  // Driver driver_6
  assign driver_5_out = decoder_1_out_2 ? 32'hfffffffc : 32'bz;  // Driver driver_7
  assign driver_5_out = decoder_1_out_3 ? {multiplexer_4_out, driver_1_out} : 32'bz;  // Driver driver_8
  Multiplexer #(.Bits(16)) multiplexer_8 (.sel(CW_SEL[0]), .in_0(Data), .in_1(16'h1f01), .out(multiplexer_8_out));
  Multiplexer #(.Bits(32)) multiplexer_9 (
    .sel(CW_SEL[12]), .in_0(multiplexer_7_out), .in_1({IV[31:8], {8{1'b0}}}), .out(multiplexer_9_out));
  Register Instruction_Register (
    .nR(nR), .D_in(multiplexer_8_out), .Clk(CW_LATCH[0]), .D_out(Instruction_Register_d_out));
  Address_Adder address_adder_1 (
    .A(multiplexer_9_out), .B(driver_5_out), .out({address_adder_1_out_2, address_adder_1_out}));  // open: Carry
  not not_3 (not_3_out, CW_LATCH[0]);
  not not_4 (not_4_out, not_3_out);
  Register Shadow_Register (.nR(nR), .D_in(Instruction_Register_d_out), .Clk(not_4_out), .D_out(IR));
  Register MABH (.nR(nR), .D_in(address_adder_1_out), .Clk(CW_LATCH[5]), .D_out(MAB[15:0]));
  Register MABL (.nR(nR), .D_in(address_adder_1_out_2), .Clk(CW_LATCH[5]), .D_out(MAB[31:16]));
  Sequencer sequencer_1 (
    .nR(nR), .Instruction(IR), .Clk(clk), .prefix(prefix), .Interrupt(IRQ), .Status(SR), .src_mod(src_mod),
    .dest_mod(dest_mod), .Byte(\byte ), .States_disp(States_disp), .Fetch1_state(sequencer_1_fetch1_state),
    .Fetch2_state(sequencer_1_fetch2_state), .Fetch_int_state(sequencer_1_fetch_int_state),
    .ALU_state(sequencer_1_alu_state), .MOV_state(sequencer_1_mov_state),
    .Ld_MAB_state(sequencer_1_ld_mab_state), .LD_ST__MP__state(sequencer_1_ld_st__mp__state),
    .LDd_STd_state(sequencer_1_ldd_std_state), .LDi_state(sequencer_1_ldi_state),
    .Addr_arithm_state(sequencer_1_addr_arithm_state), .p_i_MP_state(sequencer_1_p_i_mp_state),
    .Jump_state(sequencer_1_jump_state), .SP_4_state(sequencer_1_sp_4_state),
    .Push_PC_state(sequencer_1_push_pc_state), .EINT_state(sequencer_1_eint_state),
    .misc_state(sequencer_1_misc_state));
  Microinstruction_decoder microinstruction_decoder_1 (
    .clk(clk), .src_mod(src_mod), .dest_mod(dest_mod), .Instruction(IR), .Select_bits(CW_SEL),
    .Enable_bits(CW_EN), .Latch_bits(CW_LATCH), .Soft_int(soft_int), .prefix(prefix), .RST(RST),
    .clk_stop(clk_stp), .NOP(microinstruction_decoder_1_nop), .Src1___eq__Dest(SnotD), .nCMP(nCMP),
    .Const_enable(ALU_signal[0]), .Sub_Inv_Rev(ALU_signal[1]), .Arithm(ALU_signal[2]),
    .Enable_C_in_RotC(ALU_signal[3]), .Function(ALU_signal[6:4]), .Fetch1_state(sequencer_1_fetch1_state),
    .Fetch2_state(sequencer_1_fetch2_state), .Fetch_int_state(sequencer_1_fetch_int_state),
    .ALU_state(sequencer_1_alu_state), .MOV_state(sequencer_1_mov_state),
    .Ld_MAB_state(sequencer_1_ld_mab_state), .LD_ST__MP__state(sequencer_1_ld_st__mp__state),
    .LD_ST_direct_state(sequencer_1_ldd_std_state), .LDi_state(sequencer_1_ldi_state),
    .Addr_arithm_state(sequencer_1_addr_arithm_state), .p_i_MP_state(sequencer_1_p_i_mp_state),
    .Jump_state(sequencer_1_jump_state), .SP_4_state(sequencer_1_sp_4_state),
    .Push_PC_state(sequencer_1_push_pc_state), .EINT_state(sequencer_1_eint_state),
    .misc_state(sequencer_1_misc_state));
  Multiplexer #(.Bits(8)) multiplexer_10 (.sel(IRQ), .in_0(IR[7:0]), .in_1(iN), .out(multiplexer_10_out));
  Register u_MDB (.nR(nR), .D_in(driver_1_out), .Clk(CW_LATCH[6]), .D_out(MDB));
  Register IV_base (.nR(nR), .D_in(driver_1_out), .Clk(CW_LATCH[8]), .D_out(IV[31:16]));
  Register_8bit int_number (.nR(nR), .D_in(multiplexer_10_out), .Clk(CW_LATCH[7]), .D_out(IV[15:8]));
  assign driver_1_out = CW_EN[4] ? MDB : 16'bz;  // Driver driver_9
  _1_to_8b_extender _1_to_8b_extender_3 (.in(IR[7]), .out(_1_to_8b_extender_3_out));
  LED led_1 (.in(microinstruction_decoder_1_nop));
  assign driver_1_out = CW_EN[6] ? IV[31:16] : 16'bz;  // Driver driver_10
  LED led_2 (.in(CW_SEL[0]));
  LED led_3 (.in(CW_SEL[1]));
  LED led_4 (.in(CW_SEL[2]));
  LED led_5 (.in(CW_SEL[3]));
  LED led_6 (.in(CW_SEL[4]));
  LED led_7 (.in(CW_SEL[5]));
  LED led_8 (.in(CW_SEL[6]));
  LED led_9 (.in(CW_SEL[7]));
  LED led_10 (.in(CW_SEL[8]));
  LED led_11 (.in(CW_SEL[9]));
  LED led_12 (.in(CW_SEL[10]));
  LED led_13 (.in(CW_SEL[11]));
  LED led_14 (.in(CW_SEL[12]));
  LED led_15 (.in(CW_SEL[13]));
  LED led_16 (.in(CW_SEL[14]));
  LED led_17 (.in(CW_SEL[15]));
  or or_1 (or_1_out[0], CW_SEL[10], DMA_RQ);
  or or_2 (or_1_out[1], CW_SEL[11], DMA_RQ);
  LED led_18 (.in(CW_EN[0]));
  LED led_19 (.in(CW_EN[1]));
  LED led_20 (.in(CW_EN[2]));
  LED led_21 (.in(CW_EN[3]));
  LED led_22 (.in(CW_EN[4]));
  LED led_23 (.in(CW_EN[5]));
  LED led_24 (.in(CW_EN[6]));
  LED led_25 (.in(CW_EN[7]));
  LED led_26 (.in(CW_EN[8]));
  assign driver_1_out = CW_EN[7] ? SBE_fr_mem : 16'bz;  // Driver driver_11
  Decoder #(.Selector_Bits(2)) decoder_2 (
    .sel(or_1_out), .out_0(decoder_2_out_0), .out_1(decoder_2_out_1), .out_2(decoder_2_out_2),
    .out_3(decoder_2_out_3));
  single_byte_enabler SBE (
    .to_mem(driver_1_out), .fr_mem(SBE_fr_mem), .odd(Addr[0]), .\byte (\byte ), .fr_CPU(SBE_fr_cpu),
    .to_CPU(Data));
  assign Addr = decoder_2_out_0 ? {MP_mp_h, MP_mp_l} : 32'bz;  // Driver driver_12
  assign Addr = decoder_2_out_1 ? MAB : 32'bz;  // Driver driver_13
  assign Addr = decoder_2_out_2 ? {_1_to_8b_extender_3_out[6:0], IR[7:0], MDB, 1'b0} : 32'bz;  // Driver driver_14
  assign Addr = decoder_2_out_3 ? DMA_addr : 32'bz;  // Driver driver_15
  LED led_27 (.in(CW_LATCH[0]));
  LED led_28 (.in(CW_LATCH[1]));
  LED led_29 (.in(CW_LATCH[2]));
  LED led_30 (.in(CW_LATCH[3]));
  LED led_31 (.in(CW_LATCH[4]));
  LED led_32 (.in(CW_LATCH[5]));
  LED led_33 (.in(CW_LATCH[6]));
  LED led_34 (.in(CW_LATCH[7]));
  LED led_35 (.in(CW_LATCH[8]));
  LED led_36 (.in(CW_LATCH[9]));
  assign Data = CW_EN[8] ? SBE_fr_cpu : 16'bz;  // Driver driver_16

  assign Address = Addr;
  assign iAck = CW_SEL[0];
  assign IV[7:0] = {8{1'b0}};
  assign read = CW_EN[5];
  assign write = CW_LATCH[9];

  // Other names for the same wires on the sheet: MAB_disp[31:0] = MAB; IV_disp[31:8] = IV[31:8];
  //   Addr_disp[31:0] = Addr; E1 = CW_EN[0]; en[8:0] = CW_EN; E2 = CW_EN[1]; E3 = CW_EN[2]; E4 = CW_EN[3];
  //   E5 = CW_EN[4]; E6 = CW_EN[5]; E7 = CW_EN[6]; T1 = CW_EN[7]; T2 = CW_EN[8]; HLT = clk_stp; IR_disp[15:0] = IR;
  //   L0 = CW_LATCH[0]; latch[9:0] = CW_LATCH; L1 = CW_LATCH[1]; L2 = CW_LATCH[2]; L3 = CW_LATCH[3]; L4 = CW_LATCH[4];
  //   L5 = CW_LATCH[5]; L6 = CW_LATCH[6]; L7 = CW_LATCH[7]; L8 = CW_LATCH[8]; W = CW_LATCH[9]; MDB_disp[15:0] = MDB;
  //   R0_3[63:0] = r0_r3; R4_7[63:0] = r4_r7; S0 = CW_SEL[0]; sel[15:0] = CW_SEL; S3[1:0] = CW_SEL[2:1];
  //   S4 = CW_SEL[3]; S5 = CW_SEL[4]; S6 = CW_SEL[5]; S7 = CW_SEL[6]; S8 = CW_SEL[7]; S9[1:0] = CW_SEL[9:8];
  //   Addr_MAB = CW_SEL[10]; Addr_Direct = CW_SEL[11]; S11 = CW_SEL[12]; S12 = CW_SEL[13]; LA34[1:0] = CW_SEL[15:14];
  //   SR_disp[3:0] = SR

  // Notes on the sheet:
  //   DMA_addr: Address for DMA
  //   iN: Interrupt #
  //   from interrupt controller
  //   IRQ: Interrupt request
  //   r0_r3: Display register values
  //   r4_r7: Display register values
  //   IR: Display register values
  //   SR: Display register values
  //   MDB: Display register values
  //   nR: Reset
  //   PC: Display register values
  //   SP: Display register values
  //   FP: Display register values
  //   BP: Display register values
  //   MAB: Display register values
  //   Addr: Display register values
  //   IV: Display register values
  //   CW_SEL: SELECT signals of the control word
  //   CW_EN: ENABLE signals of the control word
  //   CW_LATCH: LATCH signals of the control word
  //   RST: Software reset signal
  //   clk_stp: Halt instruction
  //   write: Write to memory
  //   read: Read from memory
  //   iAck: interrupt acknowledge
  //   DMA_RQ: Request Direct Memory Access
  //   Const (8bit)
  //   MP + offset (32bit)
  //   Calculating core
  //   Data bus (16bit)
  //   Addressing Unit
  //   ECM-16/TTL CPU
  //   Flags (C,O,N,Z)
  //   MP value
  //   MAB value
  //   Control
  //   interrupt #
  //   Data/Instr bus (16bit)
  //   NOP
  //   Addr_MAB
  //   Addr_Direct
  //   Const + MDB
  //   DMA
  //   Control word
  //   S0
  //   S3_0
  //   S3_1
  //   S4
  //   S5
  //   S6
  //   S7
  //   S8
  //   S9_0
  //   S9_1
  //   S11
  //   S12
  //   LA3_0
  //   LA3_1
  //   DMA address
  //   E1
  //   E2
  //   E3
  //   E4
  //   E5
  //   E6
  //   E7
  //   T1
  //   T2
  //   L0
  //   L1
  //   L2
  //   L3
  //   L4
  //   L5
  //   L6
  //   L7
  //   L8
  //   W
  //   Address bus (32bit)
endmodule
