// Digital circuit HROM.dig as structural Verilog
// Emulation of 16-word switch bank ROM board
module HROM (
  input  enable_clk___set,
  input  switch_clk___cnt,
  input  chip_select,
  input  clk___set_address,
  input  [3:0] Address,
  output [15:0] D_out,
  output [3:0] Addr
);

  wire _7404_1_pin10, _7404_1_pin12, _74238_1_pin7, _74238_1_pin9, _74238_1_pin10, _74238_1_pin11,
       _74238_1_pin12, _74238_1_pin13, _74238_1_pin14, _74238_1_pin15, _74238_2_pin7, _74238_2_pin9,
       _74238_2_pin10, _74238_2_pin11, _74238_2_pin12, _74238_2_pin13, _74238_2_pin14, _74238_2_pin15;
  wire [3:0] _74163_1_pin14;

  _74163 _74163_1 (
    .pin1(chip_select), .pin2(clk___set_address), .pin3(Address[0]), .pin4(Address[1]), .pin5(Address[2]),
    .pin6(Address[3]), .pin7(1'b1), .pin8(1'b0), .pin9(switch_clk___cnt), .pin10(enable_clk___set),
    .pin11(_74163_1_pin14[3]), .pin12(_74163_1_pin14[2]), .pin13(_74163_1_pin14[1]),
    .pin14(_74163_1_pin14[0]), .pin16(1'b1));  // open: pin15
  _7404 _7404_1 (
    .pin1(1'b0), .pin3(1'b0), .pin5(1'b0), .pin7(1'b0), .pin9(1'b0), .pin10(_7404_1_pin10),
    .pin11(_74163_1_pin14[3]), .pin12(_7404_1_pin12), .pin13(chip_select), .pin14(1'b1));  // open: pin2, pin4, pin6, pin8
  ROM #(.AddrBits(4), .Bits(16)) switch_bank__emulation (.A(_74163_1_pin14), .sel(chip_select), .D(D_out));
  assign Addr = chip_select ? _74163_1_pin14 : 4'bz;  // Driver driver_1
  _74238 _74238_1 (
    .pin1(_74163_1_pin14[0]), .pin2(_74163_1_pin14[1]), .pin3(_74163_1_pin14[2]), .pin4(_7404_1_pin12),
    .pin5(1'b0), .pin6(_7404_1_pin10), .pin7(_74238_1_pin7), .pin8(1'b0), .pin9(_74238_1_pin9),
    .pin10(_74238_1_pin10), .pin11(_74238_1_pin11), .pin12(_74238_1_pin12), .pin13(_74238_1_pin13),
    .pin14(_74238_1_pin14), .pin15(_74238_1_pin15), .pin16(1'b1));
  _74238 _74238_2 (
    .pin1(_74163_1_pin14[0]), .pin2(_74163_1_pin14[1]), .pin3(_74163_1_pin14[2]), .pin4(_7404_1_pin12),
    .pin5(1'b0), .pin6(_74163_1_pin14[3]), .pin7(_74238_2_pin7), .pin8(1'b0), .pin9(_74238_2_pin9),
    .pin10(_74238_2_pin10), .pin11(_74238_2_pin11), .pin12(_74238_2_pin12), .pin13(_74238_2_pin13),
    .pin14(_74238_2_pin14), .pin15(_74238_2_pin15), .pin16(1'b1));
  Seven_Seg_Hex seven_seg_hex_1 (.d(_74163_1_pin14), .dp(1'b0));
  LED led_1 (.in(_74238_1_pin15));
  LED led_2 (.in(_74238_1_pin14));
  LED led_3 (.in(_74238_1_pin13));
  LED led_4 (.in(_74238_1_pin12));
  LED led_5 (.in(_74238_1_pin11));
  LED led_6 (.in(_74238_1_pin10));
  LED led_7 (.in(_74238_1_pin9));
  LED led_8 (.in(_74238_1_pin7));
  LED led_9 (.in(_74238_2_pin15));
  LED led_10 (.in(_74238_2_pin14));
  LED led_11 (.in(_74238_2_pin13));
  LED led_12 (.in(_74238_2_pin12));
  LED led_13 (.in(_74238_2_pin11));
  LED led_14 (.in(_74238_2_pin10));
  LED led_15 (.in(_74238_2_pin9));
  LED led_16 (.in(_74238_2_pin7));

  // Notes on the sheet:
  //   D_out: Data output
  //   Addr: Address by which data is fetched
  //   Black wire
  //   Blue wire
  //   Purple wire
  //   Green wire
  //   contents of switch_bank__emulation (hex, n*v repeats v):
  //   8801,1000,8901,1000,1003,a258,1005,b378,1007,a498,1009,b5b8,100b
  //   ,a6d8,100d,8f01
endmodule
