// Digital circuit single_byte_enabler.dig as structural Verilog
module single_byte_enabler (
  input  [15:0] to_mem,
  input  odd,
  input  \byte ,
  input  [15:0] to_CPU,
  output [15:0] fr_mem,
  output [15:0] fr_CPU
);

  wire and_1_out;

  and and_1 (and_1_out, \byte , odd);
  Multiplexer #(.Bits(8)) multiplexer_1 (.sel(odd), .in_0(to_CPU[15:8]), .in_1({8{1'b0}}), .out(fr_mem[15:8]));
  Multiplexer #(.Bits(8)) multiplexer_2 (.sel(and_1_out), .in_0(to_mem[15:8]), .in_1(to_mem[7:0]), .out(fr_CPU[15:8]));
  Multiplexer #(.Bits(8)) multiplexer_3 (.sel(and_1_out), .in_0(to_CPU[7:0]), .in_1(to_CPU[15:8]), .out(fr_mem[7:0]));

  assign fr_CPU[7:0] = to_mem[7:0];

  // Notes on the sheet:
  //   to_mem: Data coming from CPU
  //   fr_mem: data coming into CPU
  //   fr_CPU: data coming into memory
  //   to_CPU: Data coming from memory
  //   Store
  //   Load
  //   If even single byte is stored - nothing changes (the high chip is disabled)
  //   if odd single byte is stored - low byte is copied to high byte
  //   if even byte is loaded, high byte is all zeros
  //   if odd byte is loaded -- high byte is copied to low byte, and high is zeros
endmodule
