// Digital circuit Register file_gates_tristates.dig as structural Verilog
module Register_file_gates_tristates (
  input  nr,
  input  [15:0] D_in,
  input  L1,
  input  [2:0] Dest,
  input  [2:0] Src1,
  input  [2:0] Src2,
  input  S1__eq_D,
  input  nCMP,
  output [15:0] Src1_out,
  output [15:0] Src2_out,
  output [63:0] R0_3,
  output [63:0] R4_7,
  output [15:0] Src1_to_bus,
  output [2:0] RF_src1,
  output [2:0] RF_dest,
  output [2:0] RF_src2
);

  wire and_1_out, and_2_out, decoder_1_out_0, decoder_1_out_1, decoder_1_out_2, decoder_1_out_3,
       decoder_1_out_4, decoder_1_out_5, decoder_1_out_6, decoder_1_out_7, decoder_2_out_0, decoder_2_out_1,
       decoder_2_out_2, decoder_2_out_3, decoder_2_out_4, decoder_2_out_5, decoder_2_out_6, decoder_2_out_7,
       demultiplexer_1_out_0, demultiplexer_1_out_1, demultiplexer_1_out_2, demultiplexer_1_out_3,
       demultiplexer_1_out_4, demultiplexer_1_out_5, demultiplexer_1_out_6, demultiplexer_1_out_7, not_1_out,
       not_2_out, not_3_out, not_4_out, not_5_out;

  not not_1 (not_1_out, L1);
  not not_2 (not_2_out, nr);
  not not_3 (not_3_out, not_1_out);
  not not_4 (not_4_out, not_3_out);
  not not_5 (not_5_out, nCMP);
  and and_1 (and_1_out, not_4_out, L1);
  and and_2 (and_2_out, not_5_out, and_1_out);
  Demultiplexer #(.Selector_Bits(3)) demultiplexer_1 (
    .sel(Dest), .in(and_2_out), .out_0(demultiplexer_1_out_0), .out_1(demultiplexer_1_out_1),
    .out_2(demultiplexer_1_out_2), .out_3(demultiplexer_1_out_3), .out_4(demultiplexer_1_out_4),
    .out_5(demultiplexer_1_out_5), .out_6(demultiplexer_1_out_6), .out_7(demultiplexer_1_out_7));
  Multiplexer #(.Bits(3)) multiplexer_1 (.sel(S1__eq_D), .in_0(Dest), .in_1(Src1), .out(RF_src1));
  D_FF_AS #(.Bits(16)) r0 (
    .Set(1'b0), .D(D_in), .C(demultiplexer_1_out_0), .Clr(not_2_out), .Q(R0_3[15:0]));  // open: nQ
  D_FF_AS #(.Bits(16)) r1 (
    .Set(1'b0), .D(D_in), .C(demultiplexer_1_out_1), .Clr(not_2_out), .Q(R0_3[31:16]));  // open: nQ
  D_FF_AS #(.Bits(16)) r2 (
    .Set(1'b0), .D(D_in), .C(demultiplexer_1_out_2), .Clr(not_2_out), .Q(R0_3[47:32]));  // open: nQ
  D_FF_AS #(.Bits(16)) r3 (
    .Set(1'b0), .D(D_in), .C(demultiplexer_1_out_3), .Clr(not_2_out), .Q(R0_3[63:48]));  // open: nQ
  D_FF_AS #(.Bits(16)) r4 (
    .Set(1'b0), .D(D_in), .C(demultiplexer_1_out_4), .Clr(not_2_out), .Q(R4_7[15:0]));  // open: nQ
  D_FF_AS #(.Bits(16)) r5 (
    .Set(1'b0), .D(D_in), .C(demultiplexer_1_out_5), .Clr(not_2_out), .Q(R4_7[31:16]));  // open: nQ
  D_FF_AS #(.Bits(16)) r6 (
    .Set(1'b0), .D(D_in), .C(demultiplexer_1_out_6), .Clr(not_2_out), .Q(R4_7[47:32]));  // open: nQ
  D_FF_AS #(.Bits(16)) r7 (
    .Set(1'b0), .D(D_in), .C(demultiplexer_1_out_7), .Clr(not_2_out), .Q(R4_7[63:48]));  // open: nQ
  Decoder #(.Selector_Bits(3)) decoder_1 (
    .sel(Src2), .out_0(decoder_1_out_0), .out_1(decoder_1_out_1), .out_2(decoder_1_out_2),
    .out_3(decoder_1_out_3), .out_4(decoder_1_out_4), .out_5(decoder_1_out_5), .out_6(decoder_1_out_6),
    .out_7(decoder_1_out_7));
  assign Src2_out = decoder_1_out_0 ? R0_3[15:0] : 16'bz;  // Driver driver_1
  assign Src2_out = decoder_1_out_1 ? R0_3[31:16] : 16'bz;  // Driver driver_2
  assign Src2_out = decoder_1_out_2 ? R0_3[47:32] : 16'bz;  // Driver driver_3
  assign Src2_out = decoder_1_out_3 ? R0_3[63:48] : 16'bz;  // Driver driver_4
  assign Src2_out = decoder_1_out_4 ? R4_7[15:0] : 16'bz;  // Driver driver_5
  assign Src2_out = decoder_1_out_5 ? R4_7[31:16] : 16'bz;  // Driver driver_6
  assign Src2_out = decoder_1_out_6 ? R4_7[47:32] : 16'bz;  // Driver driver_7
  assign Src2_out = decoder_1_out_7 ? R4_7[63:48] : 16'bz;  // Driver driver_8
  Decoder #(.Selector_Bits(3)) decoder_2 (
    .sel(RF_src1), .out_0(decoder_2_out_0), .out_1(decoder_2_out_1), .out_2(decoder_2_out_2),
    .out_3(decoder_2_out_3), .out_4(decoder_2_out_4), .out_5(decoder_2_out_5), .out_6(decoder_2_out_6),
    .out_7(decoder_2_out_7));
  assign Src1_out = decoder_2_out_0 ? R0_3[15:0] : 16'bz;  // Driver driver_9
  assign Src1_out = decoder_2_out_1 ? R0_3[31:16] : 16'bz;  // Driver driver_10
  assign Src1_out = decoder_2_out_2 ? R0_3[47:32] : 16'bz;  // Driver driver_11
  assign Src1_out = decoder_2_out_3 ? R0_3[63:48] : 16'bz;  // Driver driver_12
  assign Src1_out = decoder_2_out_4 ? R4_7[15:0] : 16'bz;  // Driver driver_13
  assign Src1_out = decoder_2_out_5 ? R4_7[31:16] : 16'bz;  // Driver driver_14
  assign Src1_out = decoder_2_out_6 ? R4_7[47:32] : 16'bz;  // Driver driver_15
  assign Src1_out = decoder_2_out_7 ? R4_7[63:48] : 16'bz;  // Driver driver_16

  assign RF_dest = Dest;
  assign RF_src2 = Src2;
  assign Src1_to_bus = Src1_out;

  // Other names for the same wires on the sheet: r0[15:0] = R0_3[15:0]; r1[15:0] = R0_3[31:16];
  //   r2[15:0] = R0_3[47:32]; r3[15:0] = R0_3[63:48]; r4[15:0] = R4_7[15:0]; r5[15:0] = R4_7[31:16];
  //   r6[15:0] = R4_7[47:32]; r7[15:0] = R4_7[63:48]

  // Notes on the sheet:
  //   L1: Latch data to register
  //   S1__eq_D: For all instructions except non-const ALU and MOVs
  //    should be 0
  //   nCMP: Compare instr from ALU decoder, prevents write to register
endmodule
