// Digital circuit 1-to-8b extender.dig as structural Verilog
module _1_to_8b_extender (
  input  in,
  output [7:0] out
);


  assign out = {8{in}};

  // Notes on the sheet:
  //   1-to-8 bit extender
endmodule
