// Digital circuit Flags Register_8bit.dig as structural Verilog
module Flags_Register_8bit (
  input  nR,
  input  [3:0] Flags_in,
  input  Clk,
  output [3:0] Flags_out
);

  _74273 _74273_1 (
    .pin1(nR), .pin2(Flags_out[0]), .pin3(Flags_in[0]), .pin4(Flags_in[2]), .pin5(Flags_out[2]), .pin7(1'b0),
    .pin8(1'b0), .pin10(1'b0), .pin11(Clk), .pin13(1'b0), .pin14(1'b0), .pin16(Flags_out[3]),
    .pin17(Flags_in[3]), .pin18(Flags_in[1]), .pin19(Flags_out[1]), .pin20(1'b1));  // open: pin6, pin9, pin12, pin15
endmodule
