// Digital circuit Caclulating core interface.dig as structural Verilog
module Caclulating_core_interface (
  input  ALU_Step,
  input  nr,
  input  L1,
  input  E1,
  input  clk,
  input  C_in,
  input  MOV_mi,
  input  [15:0] I_in,
  output [2:0] Function,
  output Const_enable,
  output Sub_Inv_Rev,
  output Arithm,
  output Enable_C_in_RotC,
  output nCMP,
  output ALU_instr,
  output Src2_ind,
  output [2:0] Src2,
  output [2:0] Src1,
  output [2:0] Dest,
  output [7:0] Const,
  output nr_o,
  output clk_o,
  output L1_o,
  output E1_o,
  output Carry,
  output E2,
  output Src1__eq__Dest
);

  wire _7400_1_pin3, _7400_1_pin6, _7400_1_pin8, _7400_1_pin10, _7400_2_pin1, _7400_2_pin3, _7400_2_pin6,
       _7400_2_pin8, _7400_2_pin11, _7400_3_pin3, _7400_3_pin6, _7404_1_pin4, _7404_1_pin6, _7404_1_pin9,
       _7404_1_pin10, _7404_1_pin12, _7420_1_pin5, _7420_1_pin8, _7420_2_pin2, _7420_2_pin6, _7420_2_pin8,
       _7420_3_pin1, _7420_3_pin8, _7420_3_pin12;

  _7400 _7400_1 (
    .pin1(I_in[11]), .pin2(I_in[11]), .pin3(_7400_1_pin3), .pin4(I_in[13]), .pin5(I_in[13]),
    .pin6(_7400_1_pin6), .pin7(1'b0), .pin8(_7400_1_pin8), .pin9(_7400_1_pin6), .pin10(_7400_1_pin10),
    .pin11(_7400_1_pin10), .pin12(I_in[14]), .pin13(I_in[14]), .pin14(1'b1));
  _7400 _7400_2 (
    .pin1(_7400_2_pin1), .pin2(_7400_1_pin3), .pin3(_7400_2_pin3), .pin4(I_in[3]), .pin5(_7400_1_pin3),
    .pin6(_7400_2_pin6), .pin7(1'b0), .pin8(_7400_2_pin8), .pin9(_7400_1_pin8), .pin10(_7400_1_pin3),
    .pin11(_7400_2_pin11), .pin12(_7400_2_pin3), .pin13(_7400_1_pin3), .pin14(1'b1));
  _7404 _7404_1 (
    .pin1(I_in[4]), .pin2(_7400_2_pin1), .pin3(ALU_Step), .pin4(_7404_1_pin4), .pin5(MOV_mi),
    .pin6(_7404_1_pin6), .pin7(1'b0), .pin8(nCMP), .pin9(_7404_1_pin9), .pin10(_7404_1_pin10),
    .pin11(Const_enable), .pin12(_7404_1_pin12), .pin13(_7400_2_pin6), .pin14(1'b1));
  _7420 _7420_1 (
    .pin1(I_in[3]), .pin2(_7400_2_pin1), .pin4(ALU_Step), .pin5(_7420_1_pin5), .pin6(_7404_1_pin9),
    .pin7(1'b0), .pin8(_7420_1_pin8), .pin9(_7404_1_pin9), .pin10(_7404_1_pin9), .pin12(ALU_Step),
    .pin13(_7404_1_pin12), .pin14(1'b1));  // open: pin3, pin11
  _7420 _7420_2 (
    .pin1(ALU_Step), .pin2(_7420_2_pin2), .pin4(I_in[14]), .pin5(I_in[14]), .pin6(_7420_2_pin6), .pin7(1'b0),
    .pin8(_7420_2_pin8), .pin9(I_in[13]), .pin10(I_in[13]), .pin12(_7420_2_pin2), .pin13(ALU_Step),
    .pin14(1'b1));  // open: pin3, pin11
  _7408 _7408_1 (
    .pin1(I_in[2]), .pin2(ALU_Step), .pin3(Arithm), .pin4(_7400_2_pin11), .pin5(ALU_Step),
    .pin6(Function[2]), .pin7(1'b0), .pin8(Sub_Inv_Rev), .pin9(I_in[12]), .pin10(ALU_Step),
    .pin11(Const_enable), .pin12(I_in[11]), .pin13(ALU_Step), .pin14(1'b1));
  _7420 _7420_3 (
    .pin1(_7420_3_pin1), .pin2(_7420_3_pin1), .pin4(I_in[3]), .pin5(_7400_1_pin8), .pin6(_7420_2_pin2),
    .pin7(1'b0), .pin8(_7420_3_pin8), .pin9(_7420_2_pin8), .pin10(Function[1]), .pin12(_7420_3_pin12),
    .pin13(Sub_Inv_Rev), .pin14(1'b1));  // open: pin3, pin11
  _7400 _7400_3 (
    .pin1(_7404_1_pin6), .pin2(_7404_1_pin4), .pin3(_7400_3_pin3), .pin4(_7400_1_pin3), .pin5(Function[2]),
    .pin6(_7400_3_pin6), .pin7(1'b0), .pin8(Src2_ind), .pin9(_7400_3_pin6), .pin10(_7420_3_pin8),
    .pin11(Src1__eq__Dest), .pin12(_7400_3_pin3), .pin13(_7404_1_pin10), .pin14(1'b1));
  _7404 _7404_2 (
    .pin1(Function[2]), .pin2(_7420_3_pin12), .pin3(_7420_2_pin6), .pin4(Function[1]), .pin5(_7420_2_pin8),
    .pin6(Function[0]), .pin7(1'b0), .pin8(Enable_C_in_RotC), .pin9(_7420_1_pin8), .pin10(_7420_1_pin5),
    .pin11(_7400_2_pin8), .pin12(_7420_3_pin1), .pin13(_7400_2_pin3), .pin14(1'b1));

  assign ALU_instr = ALU_Step;
  assign Carry = C_in;
  assign clk_o = clk;
  assign Const = I_in[7:0];
  assign Dest = I_in[10:8];
  assign E1_o = E1;
  assign E2 = ALU_Step;
  assign L1_o = L1;
  assign nr_o = nr;
  assign Src1 = I_in[7:5];
  assign Src2 = I_in[2:0];

  // Other names for the same wires on the sheet: i2 = I_in[2]; i3 = I_in[3]; i4 = I_in[4]; i11 = I_in[11];
  //   i12 = I_in[12]; i13 = I_in[13]; i14 = I_in[14]; iALU = ALU_Step; iMOV = MOV_mi; oAr = Arithm; oCMPi = nCMP;
  //   oConst_e = Const_enable; oEnCin = Enable_C_in_RotC; oF0 = Function[0]; oF1 = Function[1]; oF2 = Function[2];
  //   oS2i = Src2_ind; oSD = Src1__eq__Dest; oSub = Sub_Inv_Rev

  // Notes on the sheet:
  //   Arithm: Arythmetic shift (for SHR only)
  //   Enable_C_in_RotC: Use carry in for ADDC, SUBC, RORC, ROLC
  //   nCMP: Compare instruction, signal to prevent write to register
  //   ALU_instr: 0 -- Display E1 indication
  //   1 -- Display Src1 and Src2 indications
  //   nr: Reset
  //   L1: Latch data to GPR
  //   E1: Enable GPR to data bus
  //   nr_o: Reset
  //   clk_o: clock signal
  //   L1_o: Latch data to GPR
  //   E1_o: Enable GPR to Data bus
  //   C_in: "Carry in" signal
  //   Carry: Carry_in signal
  //   E2: Enable ALU output to Data bus
  //   Src1__eq__Dest: Use destination address also as a source address
  //   I_in: Instruction word from IR
  //   ALU operation decoder +
  //   RF addressing
  //   Show Src2 for ops that use it:
  //   2-src arythm/logic, and rot (1, 4, 5, 6, 7)
endmodule
