// Digital circuit Jump decoder.dig as structural Verilog
module Jump_decoder (
  input  Jump,
  input  [3:0] Flags,
  input  [3:0] Condition,
  output JMP,
  output JSR,
  output No_JMP
);

  wire nand_1_out, nand_2_out, nand_3_out, nand_4_out, nand_5_out, nand_6_out, nand_7_out, nand_8_out,
       nand_9_out, nand_10_out, nand_11_out, nor_1_out, not_1_out, not_2_out, not_3_out, not_4_out,
       not_5_out, not_6_out, not_7_out, not_8_out, not_9_out, not_11_out;

  not not_1 (not_1_out, Condition[0]);
  not not_2 (not_2_out, Condition[1]);
  not not_3 (not_3_out, Condition[2]);
  not not_4 (not_4_out, Condition[3]);
  not not_5 (not_5_out, Flags[0]);
  not not_6 (not_6_out, Flags[1]);
  not not_7 (not_7_out, Flags[2]);
  not not_8 (not_8_out, Flags[3]);
  nand nand_1 (nand_1_out, Jump, not_1_out, not_2_out, not_3_out, not_4_out);
  nand nand_2 (nand_2_out, Jump, Condition[0], Condition[1], Condition[2], Condition[3]);
  nand nand_3 (nand_3_out, Jump, Condition[0], not_2_out, not_3_out, not_4_out, Flags[0]);
  nand nand_4 (nand_4_out, Jump, not_1_out, Condition[1], not_3_out, not_4_out, Flags[1]);
  nand nand_5 (nand_5_out, Jump, not_1_out, not_2_out, Condition[2], not_4_out, Flags[2]);
  nand nand_6 (nand_6_out, Jump, not_1_out, not_2_out, not_3_out, Condition[3], Flags[3]);
  nand nand_7 (nand_7_out, Jump, not_1_out, Condition[1], Condition[2], Condition[3], not_5_out);
  nand nand_8 (nand_8_out, Jump, Condition[0], not_2_out, Condition[2], Condition[3], not_6_out);
  nand nand_9 (nand_9_out, Jump, Condition[0], Condition[1], not_3_out, Condition[3], not_7_out);
  nand nand_10 (nand_10_out, Jump, Condition[0], Condition[1], Condition[2], not_4_out, not_8_out);
  not not_9 (not_9_out, nand_1_out);
  not not_10 (JSR, nand_2_out);
  nor nor_1 (nor_1_out, JSR, not_9_out);
  nand nand_11 (nand_11_out, nand_3_out, nand_4_out, nand_5_out, nand_6_out, nand_7_out, nand_8_out, nand_9_out, nand_10_out);
  not not_11 (not_11_out, nand_11_out);
  or or_1 (JMP, not_9_out, nand_11_out);
  and and_1 (No_JMP, nor_1_out, not_11_out, Jump);

  // Notes on the sheet:
  //   Flags: Bits C, O, N, Z (0, 1, 2, 3) of Status Register
  //   Can be replaced via mux with
  //   bits b, 2w, 4w and 8w (4, 5, 6, 7) of Status Register
  //   Condition: Data from instruction bits 8, 9, A, B
  //   JMP: Unconditional jump
  //   JSR: Jump to subroutine
  //   No_JMP: output 
  //   0 if condition is met
  //   1 if it is NOT met
  //   z
  //   n
  //   o
  //   c
  //   Z
  //   N
  //   O
  //   C
  //   Jump condition decoder
  //   NZ
  //   NN
  //   NO
  //   NC
  //   None
  //   All
endmodule
