// Digital circuit Sequencer.dig as structural Verilog
module Sequencer (
  input  Clk,
  input  [15:0] Instruction,
  input  [3:0] Status,
  input  nR,
  input  Interrupt,
  input  clk_stop,
  input  prefix,
  output [3:0] src_mod,
  output Byte,
  output ALU_state,
  output MOV_state,
  output Ld_MAB_state,
  output p_i_MP_state,
  output LDi_state,
  output LDd_STd_state,
  output LD_ST__MP__state,
  output Addr_arithm_state,
  output misc_state,
  output Fetch1_state,
  output Fetch2_state,
  output Fetch_int_state,
  output EINT_state,
  output SP_4_state,
  output Jump_state,
  output [3:0] dest_mod,
  output Push_PC_state,
  output JSR_state,
  output [16:0] States_disp
);

  wire and_2_out, and_3_out, and_5_out, and_6_out, and_7_out, and_8_out, and_9_out, and_11_out, and_12_out,
       and_13_out, and_14_out, and_15_out, and_16_out, and_17_out, and_18_out, and_19_out, and_20_out,
       and_21_out, and_22_out, and_23_out, and_24_out, and_25_out, and_27_out, and_28_out, and_29_out,
       and_30_out, and_31_out, and_32_out, and_33_out, and_34_out, and_35_out, and_36_out, and_37_out, clk_t,
       demultiplexer_1_out_0, demultiplexer_1_out_1, Go_to_Fetch, Interrupt_t, JUMP, jump_decoder_1_jmp,
       jump_decoder_1_jsr, jump_decoder_1_no_jmp, last, ld_cnt, multiplexer_1_out, multiplexer_2_out,
       multiplexer_3_out, multiplexer_4_out, multiplexer_5_out, multiplexer_6_out, multiplexer_7_out, nclk,
       not_1_out, not_4_out, not_5_out, not_6_out, not_7_out, not_8_out, not_9_out, not_10_out, not_11_out,
       not_13_out, not_14_out, or_1_out, or_2_out, or_3_out, or_4_out, or_5_out, or_7_out, or_8_out,
       or_9_out, post_incr, R, startup_1_pulse;
  wire [2:0] and_26_out;
  wire [2:2] not_12_out;

  not not_1 (not_1_out, clk_stop);
  and and_1 (clk_t, Clk, not_1_out);
  not not_2 (nclk, clk_t);
  LED led_1 (.in(clk_t));
  Startup startup_1 (.nR(nR), .clk(nclk), .Pulse(startup_1_pulse));
  not not_3 (R, nR);
  not not_4 (not_4_out, Instruction[15]);
  and and_2 (and_2_out, not_4_out, Instruction[14]);
  and and_3 (and_3_out, not_4_out, not_5_out);
  not not_5 (not_5_out, Instruction[14]);
  not not_6 (not_6_out, Instruction[11]);
  not not_7 (not_7_out, Instruction[3]);
  Demultiplexer demultiplexer_1 (
    .sel(Interrupt), .in(Go_to_Fetch), .out_0(demultiplexer_1_out_0), .out_1(demultiplexer_1_out_1));
  not not_8 (not_8_out, Instruction[12]);
  and and_4 (post_incr, not_7_out, Instruction[4]);
  or or_1 (or_1_out, startup_1_pulse, demultiplexer_1_out_0);
  not not_9 (not_9_out, Instruction[13]);
  not not_10 (not_10_out, Instruction[13]);
  D_FF_AS Fetch_EINT (.Set(1'b0), .D(demultiplexer_1_out_1), .C(nclk), .Clr(R), .Q(Fetch_int_state));  // open: nQ
  D_FF_AS Fetch_1__LD_IR (.Set(1'b0), .D(or_1_out), .C(nclk), .Clr(R), .Q(Fetch1_state));  // open: nQ
  and and_5 (and_5_out, Instruction[13], and_2_out);
  and and_6 (and_6_out, and_2_out, not_9_out);
  and and_7 (and_7_out, and_3_out, Instruction[13], not_8_out);
  and and_8 (and_8_out, and_3_out, not_10_out, not_8_out, Instruction[11]);
  and and_9 (and_9_out, and_3_out, Instruction[12], Instruction[13]);
  and and_10 (JUMP, and_3_out, not_10_out, Instruction[12]);
  and and_11 (and_11_out, and_3_out, not_10_out, not_8_out, not_6_out);
  LED led_2 (.in(Fetch_int_state));
  LED led_3 (.in(Fetch1_state));
  and and_12 (and_12_out, Instruction[15], Fetch1_state);
  and and_13 (and_13_out, Fetch1_state, and_6_out);
  and and_14 (and_14_out, Fetch1_state, and_9_out);
  and and_15 (and_15_out, Fetch1_state, and_7_out);
  and and_16 (and_16_out, JUMP, Fetch1_state);
  and and_17 (and_17_out, Fetch1_state, and_11_out);
  and and_18 (and_18_out, Go_to_Fetch, nclk);
  or or_2 (or_2_out, R, Fetch1_state);
  and and_19 (and_19_out, Fetch1_state, and_5_out);
  and and_20 (and_20_out, Fetch1_state, and_8_out);
  D_FF_AS int_hold (
    .Set(1'b0), .D(demultiplexer_1_out_1), .C(and_18_out), .Clr(or_2_out), .Q(Interrupt_t));  // open: nQ
  and and_21 (and_21_out, Instruction[2], and_16_out);
  not not_11 (not_11_out, Instruction[8]);
  or or_3 (or_3_out, prefix, SP_4_state);
  not not_12 (not_12_out[2], SP_4_state);
  and and_22 (and_22_out, and_19_out, Instruction[2]);
  and and_23 (and_23_out, not_11_out, Instruction[2]);
  and and_24 (and_24_out, clk_t, or_3_out);
  LED led_4 (.in(Interrupt_t));
  or or_4 (or_4_out, and_22_out, and_13_out, and_15_out, and_21_out, and_25_out);
  and and_25 (and_25_out, and_20_out, and_23_out);
  assign and_26_out = {3{not_12_out[2]}} & Instruction[7:5];  // And and_26, 3 bits wide
  // MultiWordEnabler multiwordenabler_1: pin names not known; wires that end beside it: R, nclk, ld_cnt, Instruction, JUMP, and_24_out, and_26_out[1:0], and_26_out[2], last, src_mod, dest_mod, Byte
  D_FF_AS Fetch_2__LD_MDB (.Set(1'b0), .D(or_4_out), .C(nclk), .Clr(R), .Q(Fetch2_state));  // open: nQ
  LED led_5 (.in(Fetch2_state));
  and and_27 (and_27_out, Fetch2_state, and_5_out);
  and and_28 (and_28_out, Fetch2_state, and_6_out);
  and and_29 (and_29_out, Fetch2_state, and_7_out);
  and and_30 (and_30_out, Fetch2_state, JUMP);
  and and_31 (and_31_out, Fetch2_state, and_8_out);
  Multiplexer multiplexer_1 (.sel(Instruction[2]), .in_0(and_19_out), .in_1(and_27_out), .out(multiplexer_1_out));
  Multiplexer multiplexer_2 (.sel(Instruction[2]), .in_0(and_16_out), .in_1(and_30_out), .out(multiplexer_2_out));
  Multiplexer multiplexer_3 (.sel(and_23_out), .in_0(and_20_out), .in_1(and_31_out), .out(multiplexer_3_out));
  or or_5 (or_5_out, multiplexer_2_out, Fetch_int_state);
  Jump_decoder jump_decoder_1 (
    .Jump(or_5_out), .Condition(Instruction[11:8]), .Flags(Status), .JSR(jump_decoder_1_jsr),
    .JMP(jump_decoder_1_jmp), .No_JMP(jump_decoder_1_no_jmp));
  D_FF_AS u_ALU_state (.Set(1'b0), .D(and_12_out), .C(nclk), .Clr(R), .Q(ALU_state));  // open: nQ
  D_FF_AS Load_MAB (.Set(1'b0), .D(multiplexer_1_out), .C(nclk), .Clr(R), .Q(Ld_MAB_state));  // open: nQ
  D_FF_AS SP_4 (.Set(1'b0), .D(jump_decoder_1_jsr), .C(nclk), .Clr(R), .Q(SP_4_state));  // open: nQ
  LED led_6 (.in(ALU_state));
  LED led_7 (.in(Ld_MAB_state));
  LED led_8 (.in(SP_4_state));
  or or_6 (ld_cnt, Ld_MAB_state, and_14_out, SP_4_state);
  or or_7 (or_7_out, Ld_MAB_state, and_32_out);
  or or_8 (or_8_out, and_14_out, and_33_out);
  or or_9 (or_9_out, SP_4_state, and_34_out);
  Multiplexer multiplexer_4 (.sel(or_7_out), .in_0(LD_ST__MP__state), .in_1(Ld_MAB_state), .out(multiplexer_4_out));
  Multiplexer multiplexer_5 (.sel(or_8_out), .in_0(MOV_state), .in_1(and_14_out), .out(multiplexer_5_out));
  Multiplexer multiplexer_6 (.sel(or_9_out), .in_0(Push_PC_state), .in_1(SP_4_state), .out(multiplexer_6_out));
  D_FF_AS Load_store_MP (.Set(1'b0), .D(multiplexer_4_out), .C(nclk), .Clr(R), .Q(LD_ST__MP__state));  // open: nQ
  D_FF_AS Load_store_direct (.Set(1'b0), .D(and_28_out), .C(nclk), .Clr(R), .Q(LDd_STd_state));  // open: nQ
  D_FF_AS u_MOV_state (.Set(1'b0), .D(multiplexer_5_out), .C(nclk), .Clr(R), .Q(MOV_state));  // open: nQ
  D_FF_AS Load_Immediate (.Set(1'b0), .D(and_29_out), .C(nclk), .Clr(R), .Q(LDi_state));  // open: nQ
  D_FF_AS Push_PC (.Set(1'b0), .D(multiplexer_6_out), .C(nclk), .Clr(R), .Q(Push_PC_state));  // open: nQ
  D_FF_AS Addr_Arithmetic (.Set(1'b0), .D(multiplexer_3_out), .C(nclk), .Clr(R), .Q(Addr_arithm_state));  // open: nQ
  D_FF_AS u_Misc_state (.Set(1'b0), .D(and_17_out), .C(nclk), .Clr(R), .Q(misc_state));  // open: nQ
  LED led_9 (.in(LD_ST__MP__state));
  LED led_10 (.in(LDd_STd_state));
  LED led_11 (.in(MOV_state));
  LED led_12 (.in(LDi_state));
  LED led_13 (.in(Push_PC_state));
  LED led_14 (.in(Addr_arithm_state));
  LED led_15 (.in(misc_state));
  and and_32 (and_32_out, last, LD_ST__MP__state);
  and and_33 (and_33_out, last, MOV_state);
  and and_34 (and_34_out, last, Push_PC_state);
  and and_35 (and_35_out, post_incr, and_32_out);
  and and_36 (and_36_out, and_34_out, Interrupt_t);
  not not_13 (not_13_out, Interrupt_t);
  and and_37 (and_37_out, not_13_out, and_34_out);
  not not_14 (not_14_out, post_incr);
  D_FF_AS post_inc_MP (.Set(1'b0), .D(and_35_out), .C(nclk), .Clr(R), .Q(p_i_MP_state));  // open: nQ
  D_FF_AS EINT (.Set(1'b0), .D(and_36_out), .C(nclk), .Clr(R), .Q(EINT_state));  // open: nQ
  D_FF_AS JSR (.Set(1'b0), .D(and_37_out), .C(nclk), .Clr(R), .Q(JSR_state));  // open: nQ
  D_FF_AS u_Jump (.Set(1'b0), .D(jump_decoder_1_jmp), .C(nclk), .Clr(R), .Q(Jump_state));  // open: nQ
  LED led_16 (.in(p_i_MP_state));
  LED led_17 (.in(EINT_state));
  LED led_18 (.in(JSR_state));
  LED led_19 (.in(Jump_state));
  Multiplexer multiplexer_7 (.sel(not_14_out), .in_0(p_i_MP_state), .in_1(and_32_out), .out(multiplexer_7_out));
  or or_10 (Go_to_Fetch, ALU_state, multiplexer_7_out, LDd_STd_state, and_33_out, LDi_state, EINT_state, JSR_state, Jump_state, jump_decoder_1_no_jmp, Addr_arithm_state, misc_state);

  assign States_disp = {Fetch1_state, Fetch2_state, Fetch_int_state, ALU_state, MOV_state, Ld_MAB_state, LD_ST__MP__state, LDd_STd_state, LDi_state, Addr_arithm_state, p_i_MP_state, Jump_state, SP_4_state, Push_PC_state, JSR_state, EINT_state, misc_state};

  // Other names for the same wires on the sheet: Fetch = Fetch1_state; Fetch_EINT = Fetch_int_state;
  //   Flags[3:0] = Status; offset_src = Instruction[2]; condition[3:0] = Instruction[11:8];
  //   misc_codes[2:0] = Instruction[10:8]; use_CONST = Instruction[8]; LD_ST_direct_state = LDd_STd_state

  // Notes on the sheet:
  //   Status: Contents of Status Register
  //   nR: reset signal,
  //   when low, clears all flip-flops
  //   Interrupt: When becomes high, all current instructions are
  //    completed without staggering
  //   src_mod: Source address modified by sequencer
  //   SP_4_state: Load MAB with MP - 4 
  //   (S9 = 10; S3 = i1, i0; L5 = 1)
  //   dest_mod: Destination address modified by sequencer:
  //   also used as source address for Stores
  //   Push_PC_state: Similar to LD/ST, only that this is specifically
  //   Store PC
  //   Codes for misc ops
  //   LD/ST(MP) type
  //   Misc ops flag set/clr codes
  //   ALU op
  //   LD/ST (MP)
  //   LD/ST (addr)
  //   JUMP
  //   Miscellaneous
  //   Fetch states
  //   MOV
  //   LDi
  //   AddressAr
  //   Sequencer / state machine
  //   Set byte
  //   Execute states
  //   When in normal mode, fetch is staggered with ALU op,
  //   when interrupt, EINT is staggered with ALU op
endmodule
