// Digital circuit Startup.dig as structural Verilog
module Startup (
  input  clk,
  input  nR,
  output Pulse
);

  wire and_1_out, and_2_out, d_ff_as_1_q, not_1_out, not_2_out, not_3_out, not_4_out, not_5_out, not_6_out,
       not_7_out;

  not not_1 (not_1_out, clk);
  not not_2 (not_2_out, nR);
  not not_3 (not_3_out, not_2_out);
  not not_4 (not_4_out, not_3_out);
  not not_5 (not_5_out, not_1_out);
  not not_6 (not_6_out, not_5_out);
  not not_7 (not_7_out, not_6_out);
  and and_1 (and_1_out, nR, not_4_out);
  and and_2 (and_2_out, Pulse, nR, not_1_out, not_7_out);
  D_FF_AS d_ff_as_1 (.Set(and_1_out), .D(1'b0), .C(1'b0), .Clr(and_2_out), .Q(d_ff_as_1_q));  // open: nQ
  LED led_1 (.in(d_ff_as_1_q));
  D_FF_AS d_ff_as_2 (.Set(1'b0), .D(d_ff_as_1_q), .C(clk), .Clr(not_2_out), .Q(Pulse));  // open: nQ
  LED led_2 (.in(Pulse));

  // Notes on the sheet:
  //   clk: Hz: 5
  //   nR: Reset signal
  //   Startup pulse generator
endmodule
