// Digital circuit flip-flop chain.dig as structural Verilog
module flip_flop_chain (
  input  clk
);

  wire and_1_out, and_2_out, d_ff_as_1_q, d_ff_as_2_q, d_ff_as_3_q, d_ff_as_4_q, d_ff_as_5_q, d_ff_as_6_q,
       d_ff_as_7_q, d_ff_as_8_q, d_ff_as_9_q, not_1_out, not_2_out, not_3_out, not_4_out, not_5_out,
       not_6_out, not_7_out, or_1_out, R_out;

  Button #(.activeLow("true")) R (.out(R_out));
  not not_1 (not_1_out, clk);
  not not_2 (not_2_out, R_out);
  not not_3 (not_3_out, not_2_out);
  not not_4 (not_4_out, not_3_out);
  not not_5 (not_5_out, not_1_out);
  not not_6 (not_6_out, not_5_out);
  not not_7 (not_7_out, not_6_out);
  and and_1 (and_1_out, R_out, not_4_out);
  and and_2 (and_2_out, d_ff_as_2_q, R_out, not_1_out, not_7_out);
  D_FF_AS d_ff_as_1 (.Set(and_1_out), .D(1'b0), .C(1'b0), .Clr(and_2_out), .Q(d_ff_as_1_q));  // open: nQ
  LED led_1 (.in(d_ff_as_1_q));
  D_FF_AS d_ff_as_2 (.Set(1'b0), .D(d_ff_as_1_q), .C(clk), .Clr(not_2_out), .Q(d_ff_as_2_q));  // open: nQ
  LED led_2 (.in(d_ff_as_2_q));
  or or_1 (or_1_out, d_ff_as_9_q, d_ff_as_2_q);
  D_FF_AS d_ff_as_3 (.Set(1'b0), .D(or_1_out), .C(clk), .Clr(not_2_out), .Q(d_ff_as_3_q));  // open: nQ
  LED led_3 (.in(d_ff_as_3_q));
  D_FF_AS d_ff_as_4 (.Set(1'b0), .D(d_ff_as_3_q), .C(clk), .Clr(not_2_out), .Q(d_ff_as_4_q));  // open: nQ
  LED led_4 (.in(d_ff_as_4_q));
  D_FF_AS d_ff_as_5 (.Set(1'b0), .D(d_ff_as_4_q), .C(clk), .Clr(not_2_out), .Q(d_ff_as_5_q));  // open: nQ
  LED led_5 (.in(d_ff_as_5_q));
  D_FF_AS d_ff_as_6 (.Set(1'b0), .D(d_ff_as_5_q), .C(clk), .Clr(not_2_out), .Q(d_ff_as_6_q));  // open: nQ
  LED led_6 (.in(d_ff_as_6_q));
  D_FF_AS d_ff_as_7 (.Set(1'b0), .D(d_ff_as_6_q), .C(clk), .Clr(not_2_out), .Q(d_ff_as_7_q));  // open: nQ
  LED led_7 (.in(d_ff_as_7_q));
  D_FF_AS d_ff_as_8 (.Set(1'b0), .D(d_ff_as_7_q), .C(clk), .Clr(not_2_out), .Q(d_ff_as_8_q));  // open: nQ
  LED led_8 (.in(d_ff_as_8_q));
  D_FF_AS d_ff_as_9 (.Set(1'b0), .D(d_ff_as_8_q), .C(clk), .Clr(not_2_out), .Q(d_ff_as_9_q));  // open: nQ
  LED led_9 (.in(d_ff_as_9_q));

  // Notes on the sheet:
  //   clk: Hz: 5
endmodule
