// Digital circuit ECM-16 computer.dig as structural Verilog
module ECM_16_computer (
  input  Clk,
  input  [31:0] in_2,
  input  [7:0] in_3
);

  wire and_1_out, and_3_out, and_4_out, and_6_out, Byte, clk_stop, clk_t, Cont_out, d_ff_1_nq, d_ff_1_q,
       d_ff_as_1_nq, d_ff_as_1_q, decoder_1_out_0, decoder_1_out_1, decoder_1_out_2, decoder_1_out_3,
       decoder_2_out_0, decoder_2_out_1, decoder_2_out_2, decoder_2_out_3, E1, E2, E3, E4, E5, E6, E7,
       Int_mock_out, IRQ, L0, L1, L2, L3, L4, L5, L6, L7, L8, microinstruction_decoder_1_nop, nclk, nCMP,
       not_1_out, not_2_out, not_3_out, not_4_out, not_5_out, not_6_out, not_7_out, not_8_out, not_11_out,
       not_12_out, not_13_out, nr, or_1_out, or_2_out, or_3_out, prefix, R_out, RST, S0, S4, S5, S6, S7, S8,
       S11, S12, sequencer_1_addr_arithm_state, sequencer_1_alu_state, sequencer_1_eint_state,
       sequencer_1_fetch1_state, sequencer_1_fetch2_state, sequencer_1_fetch_int_state,
       sequencer_1_jump_state, sequencer_1_ld_mab_state, sequencer_1_ld_st__mp__state,
       sequencer_1_ldd_std_state, sequencer_1_ldi_state, sequencer_1_misc_state, sequencer_1_mov_state,
       sequencer_1_p_i_mp_state, sequencer_1_push_pc_state, sequencer_1_sp_4_state, SnotD, Soft_Int;
  wire [1:0] LA34, S3, S9, S10;
  wire [1:1] not_10_out;
  wire [3:0] dest_mod, main_alu_tristates_1_flags, multiplexer_5_out, SR_disp, src_mod;
  wire [6:0] ALU_signal;
  wire [7:0] _1_to_8b_extender_1_out, _1_to_8b_extender_2_out, _1_to_8b_extender_3_out, multiplexer_10_out;
  wire [8:7] en;
  wire [9:9] latch;
  wire [15:0] _1_to_16b_extender_1_out, driver_1_out, driver_16_out, GPR_src1_out, GPR_src1_to_bus,
       GPR_src2_out, Instruction_Register_d_out, IR_disp, main_alu_tristates_1_output, MDB_disp, MP_mp_h,
       MP_mp_l, multiplexer_1_out, multiplexer_2_out, multiplexer_3_out, multiplexer_4_out,
       multiplexer_6_out, multiplexer_7_out, pullup_1_out, ROM_d, SBE_fr_cpu, SBE_fr_mem,
       sequencer_1_states_disp;
  wire [31:0] Addr_disp, address_adder_1_out, BP, driver_5_out, FP, MAB_disp, multiplexer_8_out,
       multiplexer_9_out, PC, SP;
  wire [31:8] IV_disp;
  wire [63:0] R0_3, R4_7;

  Button Int_mock (.out(Int_mock_out));
  not not_1 (not_1_out, S0);
  or or_1 (or_1_out, Soft_Int, Int_mock_out);
  not not_2 (not_2_out, not_1_out);
  not not_3 (not_3_out, or_1_out);
  and and_1 (and_1_out, not_1_out, not_2_out);
  not not_4 (not_4_out, not_3_out);
  D_FF_AS Int (.Set(1'b0), .D(or_1_out), .C(not_4_out), .Clr(and_1_out), .Q(IRQ));  // open: nQ
  not not_5 (not_5_out, RST);
  Button #(.activeLow("true")) R (.out(R_out));
  LED led_1 (.in(IRQ));
  and and_2 (nr, not_5_out, R_out);
  Button Cont (.out(Cont_out));
  not not_6 (not_6_out, nr);
  or or_2 (or_2_out, not_6_out, Cont_out);
  not not_7 (not_7_out, or_2_out);
  and and_3 (and_3_out, clk_stop, not_7_out);
  D_FF_AS d_ff_as_1 (.Set(1'b0), .D(and_3_out), .C(d_ff_1_q), .Clr(or_2_out), .Q(d_ff_as_1_q), .nQ(d_ff_as_1_nq));
  and and_4 (and_4_out, d_ff_as_1_nq, Clk);
  LED led_2 (.in(d_ff_as_1_q));
  not not_8 (not_8_out, and_4_out);
  D_FF d_ff_1 (.D(d_ff_1_nq), .C(and_4_out), .Q(d_ff_1_q), .nQ(d_ff_1_nq));
  and and_5 (clk_t, not_8_out, d_ff_1_q);
  not not_9 (nclk, d_ff_1_q);
  Multiplexer #(.Bits(16)) multiplexer_1 (
    .sel(S5), .in_0(driver_1_out), .in_1(address_adder_1_out[15:0]), .out(multiplexer_1_out));
  _1_to_8b_extender _1_to_8b_extender_1 (.in(IR_disp[8]), .out(_1_to_8b_extender_1_out));
  Multiplexer #(.Bits(16)) multiplexer_2 (
    .sel(S6), .in_0(driver_1_out), .in_1({_1_to_8b_extender_1_out, IR_disp[7:0]}), .out(multiplexer_2_out));
  Multiplexer #(.Bits(16)) multiplexer_3 (
    .sel(S5), .in_0(multiplexer_2_out), .in_1(address_adder_1_out[31:16]), .out(multiplexer_3_out));
  _1_to_16b_extender _1_to_16b_extender_1 (.in(driver_1_out[15]), .out(_1_to_16b_extender_1_out));
  or or_3 (or_3_out, d_ff_1_q, nclk);
  Register_file_gates_tristates GPR (
    .Src2_out(GPR_src2_out), .Src1_out(GPR_src1_out), .nr(nr), .nCMP(nCMP), .L1(L1), .S1__eq_D(SnotD),
    .Dest(dest_mod[2:0]), .Src1(src_mod[3:1]), .Src2(IR_disp[2:0]), .D_in(driver_1_out), .R0_3(R0_3),
    .R4_7(R4_7), .Src1_to_bus(GPR_src1_to_bus));
  Main_ALU_tristates main_alu_tristates_1 (
    .Src2(GPR_src2_out), .Src1(GPR_src1_out), .Const(IR_disp[7:0]), .Carry_in(SR_disp[3]),
    .Const_enable(ALU_signal[0]), .Sub_Inv_Rev(ALU_signal[1]), .Arithm(ALU_signal[2]),
    .Enable_C_in_RotC(ALU_signal[3]), .Function(ALU_signal[6:4]), .Output(main_alu_tristates_1_output),
    .Flags(main_alu_tristates_1_flags));
  _1_to_8b_extender _1_to_8b_extender_2 (.in(IR_disp[7]), .out(_1_to_8b_extender_2_out));
  assign driver_1_out = E2 ? main_alu_tristates_1_output : 16'bz;  // Driver driver_1
  Memory_Pointers_gates_tristate MP (
    .nr(nr), .L3(L3), .L4(L4), .D3(multiplexer_3_out), .D4(multiplexer_1_out), .S3(S3), .LA34(LA34), .PC(PC),
    .SP(SP), .FP(FP), .BP(BP), .MP_H(MP_mp_h), .MP_L(MP_mp_l));
  Multiplexer #(.Bits(16)) multiplexer_4 (
    .sel(S12), .in_0({_1_to_8b_extender_2_out, IR_disp[7:0]}), .in_1(_1_to_16b_extender_1_out),
    .out(multiplexer_4_out));
  LED u_clk (.in(clk_t));
  LED u_nclk (.in(or_3_out));
  Multiplexer #(.Bits(4)) multiplexer_5 (
    .sel(S7), .in_0(main_alu_tristates_1_flags), .in_1(driver_1_out[3:0]), .out(multiplexer_5_out));
  Flags_Register_8bit Status_Register (.nR(nr), .Flags_in(multiplexer_5_out), .Clk(L2), .Flags_out(SR_disp));
  not not_10 (not_10_out[1], Byte);
  LED led_3 (.in(IR_disp[15]));
  LED led_4 (.in(R0_3[15]));
  LED led_5 (.in(R0_3[31]));
  LED led_6 (.in(R0_3[47]));
  LED led_7 (.in(R0_3[63]));
  LED led_8 (.in(R4_7[15]));
  LED led_9 (.in(R4_7[31]));
  LED led_10 (.in(R4_7[47]));
  LED led_11 (.in(R4_7[63]));
  LED led_12 (.in(MDB_disp[15]));
  PullUp #(.Bits(16)) pullup_1 (.out(pullup_1_out));
  assign driver_1_out = E1 ? GPR_src1_to_bus : 16'bz;  // Driver driver_2
  assign driver_1_out = E4 ? multiplexer_6_out : 16'bz;  // Driver driver_3
  Multiplexer #(.Bits(16)) multiplexer_6 (.sel(S4), .in_0(MP_mp_h), .in_1(MP_mp_l), .out(multiplexer_6_out));
  LED led_13 (.in(IR_disp[14]));
  LED led_14 (.in(IR_disp[13]));
  LED led_15 (.in(IR_disp[12]));
  LED led_16 (.in(IR_disp[11]));
  LED led_17 (.in(R0_3[14]));
  LED led_18 (.in(R0_3[13]));
  LED led_19 (.in(R0_3[12]));
  LED led_20 (.in(R0_3[11]));
  LED led_21 (.in(R0_3[30]));
  LED led_22 (.in(R0_3[29]));
  LED led_23 (.in(R0_3[28]));
  LED led_24 (.in(R0_3[27]));
  LED led_25 (.in(R0_3[46]));
  LED led_26 (.in(R0_3[45]));
  LED led_27 (.in(R0_3[44]));
  LED led_28 (.in(R0_3[43]));
  LED led_29 (.in(R0_3[62]));
  LED led_30 (.in(R0_3[61]));
  LED led_31 (.in(R0_3[60]));
  LED led_32 (.in(R0_3[59]));
  LED led_33 (.in(R4_7[14]));
  LED led_34 (.in(R4_7[13]));
  LED led_35 (.in(R4_7[12]));
  LED led_36 (.in(R4_7[11]));
  LED led_37 (.in(R4_7[30]));
  LED led_38 (.in(R4_7[29]));
  LED led_39 (.in(R4_7[28]));
  LED led_40 (.in(R4_7[27]));
  LED led_41 (.in(R4_7[46]));
  LED led_42 (.in(R4_7[45]));
  LED led_43 (.in(R4_7[44]));
  LED led_44 (.in(R4_7[43]));
  LED led_45 (.in(R4_7[62]));
  LED led_46 (.in(R4_7[61]));
  LED led_47 (.in(R4_7[60]));
  LED led_48 (.in(R4_7[59]));
  LED led_49 (.in(MDB_disp[14]));
  LED led_50 (.in(MDB_disp[13]));
  LED led_51 (.in(MDB_disp[12]));
  LED led_52 (.in(MDB_disp[11]));
  Decoder #(.Selector_Bits(2)) decoder_1 (
    .sel(S9), .out_0(decoder_1_out_0), .out_1(decoder_1_out_1), .out_2(decoder_1_out_2),
    .out_3(decoder_1_out_3));
  LED led_53 (.in(IR_disp[10]));
  LED led_54 (.in(IR_disp[9]));
  LED led_55 (.in(IR_disp[8]));
  LED led_56 (.in(IR_disp[7]));
  LED led_57 (.in(R0_3[10]));
  LED led_58 (.in(R0_3[9]));
  LED led_59 (.in(R0_3[8]));
  LED led_60 (.in(R0_3[7]));
  LED led_61 (.in(R0_3[26]));
  LED led_62 (.in(R0_3[25]));
  LED led_63 (.in(R0_3[24]));
  LED led_64 (.in(R0_3[23]));
  LED led_65 (.in(R0_3[42]));
  LED led_66 (.in(R0_3[41]));
  LED led_67 (.in(R0_3[40]));
  LED led_68 (.in(R0_3[39]));
  LED led_69 (.in(R0_3[58]));
  LED led_70 (.in(R0_3[57]));
  LED led_71 (.in(R0_3[56]));
  LED led_72 (.in(R0_3[55]));
  LED led_73 (.in(R4_7[10]));
  LED led_74 (.in(R4_7[9]));
  LED led_75 (.in(R4_7[8]));
  LED led_76 (.in(R4_7[7]));
  LED led_77 (.in(R4_7[26]));
  LED led_78 (.in(R4_7[25]));
  LED led_79 (.in(R4_7[24]));
  LED led_80 (.in(R4_7[23]));
  LED led_81 (.in(R4_7[42]));
  LED led_82 (.in(R4_7[41]));
  LED led_83 (.in(R4_7[40]));
  LED led_84 (.in(R4_7[39]));
  LED led_85 (.in(R4_7[58]));
  LED led_86 (.in(R4_7[57]));
  LED led_87 (.in(R4_7[56]));
  LED led_88 (.in(R4_7[55]));
  LED led_89 (.in(MDB_disp[10]));
  LED led_90 (.in(MDB_disp[9]));
  LED led_91 (.in(MDB_disp[8]));
  LED led_92 (.in(MDB_disp[7]));
  Multiplexer #(.Bits(16)) multiplexer_7 (.sel(S0), .in_0(driver_16_out), .in_1(16'h1f01), .out(multiplexer_7_out));
  assign driver_1_out = E3 ? {{12{1'b0}}, SR_disp} : 16'bz;  // Driver driver_4
  Multiplexer #(.Bits(32)) multiplexer_8 (
    .sel(S8), .in_0({MP_mp_h, MP_mp_l}), .in_1(MAB_disp), .out(multiplexer_8_out));
  assign driver_5_out = decoder_1_out_0 ? {32{1'b0}} : 32'bz;  // Driver driver_5
  assign driver_5_out = decoder_1_out_1 ? {{30{1'b0}}, not_10_out[1], Byte} : 32'bz;  // Driver driver_6
  assign driver_5_out = decoder_1_out_2 ? 32'hfffffffc : 32'bz;  // Driver driver_7
  assign driver_5_out = decoder_1_out_3 ? {multiplexer_4_out, driver_1_out} : 32'bz;  // Driver driver_8
  LED led_93 (.in(IR_disp[6]));
  LED led_94 (.in(IR_disp[5]));
  LED led_95 (.in(IR_disp[4]));
  LED led_96 (.in(IR_disp[3]));
  LED led_97 (.in(R0_3[6]));
  LED led_98 (.in(R0_3[5]));
  LED led_99 (.in(R0_3[4]));
  LED led_100 (.in(R0_3[3]));
  LED led_101 (.in(R0_3[22]));
  LED led_102 (.in(R0_3[21]));
  LED led_103 (.in(R0_3[20]));
  LED led_104 (.in(R0_3[19]));
  LED led_105 (.in(R0_3[38]));
  LED led_106 (.in(R0_3[37]));
  LED led_107 (.in(R0_3[36]));
  LED led_108 (.in(R0_3[35]));
  LED led_109 (.in(R0_3[54]));
  LED led_110 (.in(R0_3[53]));
  LED led_111 (.in(R0_3[52]));
  LED led_112 (.in(R0_3[51]));
  LED led_113 (.in(R4_7[6]));
  LED led_114 (.in(R4_7[5]));
  LED led_115 (.in(R4_7[4]));
  LED led_116 (.in(R4_7[3]));
  LED led_117 (.in(R4_7[22]));
  LED led_118 (.in(R4_7[21]));
  LED led_119 (.in(R4_7[20]));
  LED led_120 (.in(R4_7[19]));
  LED led_121 (.in(R4_7[38]));
  LED led_122 (.in(R4_7[37]));
  LED led_123 (.in(R4_7[36]));
  LED led_124 (.in(R4_7[35]));
  LED led_125 (.in(R4_7[54]));
  LED led_126 (.in(R4_7[53]));
  LED led_127 (.in(R4_7[52]));
  LED led_128 (.in(R4_7[51]));
  LED led_129 (.in(MDB_disp[6]));
  LED led_130 (.in(MDB_disp[5]));
  LED led_131 (.in(MDB_disp[4]));
  LED led_132 (.in(MDB_disp[3]));
  Register Instruction_Register (.nR(nr), .D_in(multiplexer_7_out), .Clk(L0), .D_out(Instruction_Register_d_out));
  Multiplexer #(.Bits(32)) multiplexer_9 (
    .sel(S11), .in_0(multiplexer_8_out), .in_1({IV_disp, {8{1'b0}}}), .out(multiplexer_9_out));
  LED led_133 (.in(IR_disp[2]));
  LED led_134 (.in(IR_disp[1]));
  LED led_135 (.in(IR_disp[0]));
  LED led_136 (.in(R0_3[2]));
  LED led_137 (.in(R0_3[1]));
  LED led_138 (.in(R0_3[0]));
  LED led_139 (.in(R0_3[18]));
  LED led_140 (.in(R0_3[17]));
  LED led_141 (.in(R0_3[16]));
  LED led_142 (.in(R0_3[34]));
  LED led_143 (.in(R0_3[33]));
  LED led_144 (.in(R0_3[32]));
  LED led_145 (.in(R0_3[50]));
  LED led_146 (.in(R0_3[49]));
  LED led_147 (.in(R0_3[48]));
  LED led_148 (.in(R4_7[2]));
  LED led_149 (.in(R4_7[1]));
  LED led_150 (.in(R4_7[0]));
  LED led_151 (.in(R4_7[18]));
  LED led_152 (.in(R4_7[17]));
  LED led_153 (.in(R4_7[16]));
  LED led_154 (.in(R4_7[34]));
  LED led_155 (.in(R4_7[33]));
  LED led_156 (.in(R4_7[32]));
  LED led_157 (.in(R4_7[50]));
  LED led_158 (.in(R4_7[49]));
  LED led_159 (.in(R4_7[48]));
  LED led_160 (.in(MDB_disp[2]));
  LED led_161 (.in(MDB_disp[1]));
  LED led_162 (.in(MDB_disp[0]));
  not not_11 (not_11_out, L0);
  Address_Adder address_adder_1 (.A(multiplexer_9_out), .B(driver_5_out), .out(address_adder_1_out));  // open: Carry
  LED led_163 (.in(SR_disp[0]));
  LED led_164 (.in(SR_disp[1]));
  LED led_165 (.in(SR_disp[2]));
  LED led_166 (.in(SR_disp[3]));
  not not_12 (not_12_out, not_11_out);
  Register Shadow_Register (.nR(nr), .D_in(Instruction_Register_d_out), .Clk(not_12_out), .D_out(IR_disp));
  LED led_167 (.in(PC[31]));
  LED led_168 (.in(PC[30]));
  LED led_169 (.in(PC[29]));
  LED led_170 (.in(PC[28]));
  LED led_171 (.in(SP[31]));
  LED led_172 (.in(SP[30]));
  LED led_173 (.in(SP[29]));
  LED led_174 (.in(SP[28]));
  LED led_175 (.in(FP[31]));
  LED led_176 (.in(FP[30]));
  LED led_177 (.in(FP[29]));
  LED led_178 (.in(FP[28]));
  LED led_179 (.in(BP[31]));
  LED led_180 (.in(BP[30]));
  LED led_181 (.in(BP[29]));
  LED led_182 (.in(BP[28]));
  LED led_183 (.in(MAB_disp[31]));
  LED led_184 (.in(MAB_disp[30]));
  LED led_185 (.in(MAB_disp[29]));
  LED led_186 (.in(MAB_disp[28]));
  LED led_187 (.in(Addr_disp[31]));
  LED led_188 (.in(Addr_disp[30]));
  LED led_189 (.in(Addr_disp[29]));
  LED led_190 (.in(Addr_disp[28]));
  LED led_191 (.in(IV_disp[31]));
  LED led_192 (.in(IV_disp[30]));
  LED led_193 (.in(IV_disp[29]));
  LED led_194 (.in(IV_disp[28]));
  LED led_195 (.in(PC[27]));
  LED led_196 (.in(PC[26]));
  LED led_197 (.in(PC[25]));
  LED led_198 (.in(PC[24]));
  LED led_199 (.in(SP[27]));
  LED led_200 (.in(SP[26]));
  LED led_201 (.in(SP[25]));
  LED led_202 (.in(SP[24]));
  LED led_203 (.in(FP[27]));
  LED led_204 (.in(FP[26]));
  LED led_205 (.in(FP[25]));
  LED led_206 (.in(FP[24]));
  LED led_207 (.in(BP[27]));
  LED led_208 (.in(BP[26]));
  LED led_209 (.in(BP[25]));
  LED led_210 (.in(BP[24]));
  LED led_211 (.in(MAB_disp[27]));
  LED led_212 (.in(MAB_disp[26]));
  LED led_213 (.in(MAB_disp[25]));
  LED led_214 (.in(MAB_disp[24]));
  LED led_215 (.in(Addr_disp[27]));
  LED led_216 (.in(Addr_disp[26]));
  LED led_217 (.in(Addr_disp[25]));
  LED led_218 (.in(Addr_disp[24]));
  LED led_219 (.in(IV_disp[27]));
  LED led_220 (.in(IV_disp[26]));
  LED led_221 (.in(IV_disp[25]));
  LED led_222 (.in(IV_disp[24]));
  Register MABH (.nR(nr), .D_in(address_adder_1_out[15:0]), .Clk(L5), .D_out(MAB_disp[15:0]));
  Register MABL (.nR(nr), .D_in(address_adder_1_out[31:16]), .Clk(L5), .D_out(MAB_disp[31:16]));
  LED led_223 (.in(PC[23]));
  LED led_224 (.in(PC[22]));
  LED led_225 (.in(PC[21]));
  LED led_226 (.in(PC[20]));
  LED led_227 (.in(SP[23]));
  LED led_228 (.in(SP[22]));
  LED led_229 (.in(SP[21]));
  LED led_230 (.in(SP[20]));
  LED led_231 (.in(FP[23]));
  LED led_232 (.in(FP[22]));
  LED led_233 (.in(FP[21]));
  LED led_234 (.in(FP[20]));
  LED led_235 (.in(BP[23]));
  LED led_236 (.in(BP[22]));
  LED led_237 (.in(BP[21]));
  LED led_238 (.in(BP[20]));
  LED led_239 (.in(MAB_disp[23]));
  LED led_240 (.in(MAB_disp[22]));
  LED led_241 (.in(MAB_disp[21]));
  LED led_242 (.in(MAB_disp[20]));
  LED led_243 (.in(Addr_disp[23]));
  LED led_244 (.in(Addr_disp[22]));
  LED led_245 (.in(Addr_disp[21]));
  LED led_246 (.in(Addr_disp[20]));
  LED led_247 (.in(IV_disp[23]));
  LED led_248 (.in(IV_disp[22]));
  LED led_249 (.in(IV_disp[21]));
  LED led_250 (.in(IV_disp[20]));
  LED led_251 (.in(PC[19]));
  LED led_252 (.in(PC[18]));
  LED led_253 (.in(PC[17]));
  LED led_254 (.in(PC[16]));
  LED led_255 (.in(SP[19]));
  LED led_256 (.in(SP[18]));
  LED led_257 (.in(SP[17]));
  LED led_258 (.in(SP[16]));
  LED led_259 (.in(FP[19]));
  LED led_260 (.in(FP[18]));
  LED led_261 (.in(FP[17]));
  LED led_262 (.in(FP[16]));
  LED led_263 (.in(BP[19]));
  LED led_264 (.in(BP[18]));
  LED led_265 (.in(BP[17]));
  LED led_266 (.in(BP[16]));
  LED led_267 (.in(MAB_disp[19]));
  LED led_268 (.in(MAB_disp[18]));
  LED led_269 (.in(MAB_disp[17]));
  LED led_270 (.in(MAB_disp[16]));
  LED led_271 (.in(Addr_disp[19]));
  LED led_272 (.in(Addr_disp[18]));
  LED led_273 (.in(Addr_disp[17]));
  LED led_274 (.in(Addr_disp[16]));
  LED led_275 (.in(IV_disp[19]));
  LED led_276 (.in(IV_disp[18]));
  LED led_277 (.in(IV_disp[17]));
  LED led_278 (.in(IV_disp[16]));
  LED led_279 (.in(PC[15]));
  LED led_280 (.in(PC[14]));
  LED led_281 (.in(PC[13]));
  LED led_282 (.in(PC[12]));
  LED led_283 (.in(SP[15]));
  LED led_284 (.in(SP[14]));
  LED led_285 (.in(SP[13]));
  LED led_286 (.in(SP[12]));
  LED led_287 (.in(FP[15]));
  LED led_288 (.in(FP[14]));
  LED led_289 (.in(FP[13]));
  LED led_290 (.in(FP[12]));
  LED led_291 (.in(BP[15]));
  LED led_292 (.in(BP[14]));
  LED led_293 (.in(BP[13]));
  LED led_294 (.in(BP[12]));
  LED led_295 (.in(MAB_disp[15]));
  LED led_296 (.in(MAB_disp[14]));
  LED led_297 (.in(MAB_disp[13]));
  LED led_298 (.in(MAB_disp[12]));
  LED led_299 (.in(Addr_disp[15]));
  LED led_300 (.in(Addr_disp[14]));
  LED led_301 (.in(Addr_disp[13]));
  LED led_302 (.in(Addr_disp[12]));
  LED led_303 (.in(IV_disp[15]));
  LED led_304 (.in(IV_disp[14]));
  LED led_305 (.in(IV_disp[13]));
  LED led_306 (.in(IV_disp[12]));
  Sequencer sequencer_1 (
    .nR(nr), .Instruction(IR_disp), .Clk(clk_t), .prefix(prefix), .Interrupt(IRQ), .Status(SR_disp),
    .src_mod(src_mod), .dest_mod(dest_mod), .Byte(Byte), .States_disp(sequencer_1_states_disp),
    .Fetch1_state(sequencer_1_fetch1_state), .Fetch2_state(sequencer_1_fetch2_state),
    .Fetch_int_state(sequencer_1_fetch_int_state), .ALU_state(sequencer_1_alu_state),
    .MOV_state(sequencer_1_mov_state), .Ld_MAB_state(sequencer_1_ld_mab_state),
    .LD_ST__MP__state(sequencer_1_ld_st__mp__state), .LDd_STd_state(sequencer_1_ldd_std_state),
    .LDi_state(sequencer_1_ldi_state), .Addr_arithm_state(sequencer_1_addr_arithm_state),
    .p_i_MP_state(sequencer_1_p_i_mp_state), .Jump_state(sequencer_1_jump_state),
    .SP_4_state(sequencer_1_sp_4_state), .Push_PC_state(sequencer_1_push_pc_state),
    .EINT_state(sequencer_1_eint_state), .misc_state(sequencer_1_misc_state));
  Microinstruction_decoder microinstruction_decoder_1 (
    .clk(clk_t), .src_mod(src_mod), .dest_mod(dest_mod), .Instruction(IR_disp),
    .Select_bits({LA34, S12, S11, S10, S9, S8, S7, S6, S5, S4, S3, S0}),
    .Enable_bits({en, E7, E6, E5, E4, E3, E2, E1}),
    .Latch_bits({latch[9], L8, L7, L6, L5, L4, L3, L2, L1, L0}), .Soft_int(Soft_Int), .prefix(prefix),
    .RST(RST), .clk_stop(clk_stop), .NOP(microinstruction_decoder_1_nop), .Src1___eq__Dest(SnotD),
    .nCMP(nCMP), .Const_enable(ALU_signal[0]), .Sub_Inv_Rev(ALU_signal[1]), .Arithm(ALU_signal[2]),
    .Enable_C_in_RotC(ALU_signal[3]), .Function(ALU_signal[6:4]), .Fetch1_state(sequencer_1_fetch1_state),
    .Fetch2_state(sequencer_1_fetch2_state), .Fetch_int_state(sequencer_1_fetch_int_state),
    .ALU_state(sequencer_1_alu_state), .MOV_state(sequencer_1_mov_state),
    .Ld_MAB_state(sequencer_1_ld_mab_state), .LD_ST__MP__state(sequencer_1_ld_st__mp__state),
    .LD_ST_direct_state(sequencer_1_ldd_std_state), .LDi_state(sequencer_1_ldi_state),
    .Addr_arithm_state(sequencer_1_addr_arithm_state), .p_i_MP_state(sequencer_1_p_i_mp_state),
    .Jump_state(sequencer_1_jump_state), .SP_4_state(sequencer_1_sp_4_state),
    .Push_PC_state(sequencer_1_push_pc_state), .EINT_state(sequencer_1_eint_state),
    .misc_state(sequencer_1_misc_state));
  LED led_307 (.in(PC[11]));
  LED led_308 (.in(PC[10]));
  LED led_309 (.in(PC[9]));
  LED led_310 (.in(PC[8]));
  LED led_311 (.in(SP[11]));
  LED led_312 (.in(SP[10]));
  LED led_313 (.in(SP[9]));
  LED led_314 (.in(SP[8]));
  LED led_315 (.in(FP[11]));
  LED led_316 (.in(FP[10]));
  LED led_317 (.in(FP[9]));
  LED led_318 (.in(FP[8]));
  LED led_319 (.in(BP[11]));
  LED led_320 (.in(BP[10]));
  LED led_321 (.in(BP[9]));
  LED led_322 (.in(BP[8]));
  LED led_323 (.in(MAB_disp[11]));
  LED led_324 (.in(MAB_disp[10]));
  LED led_325 (.in(MAB_disp[9]));
  LED led_326 (.in(MAB_disp[8]));
  LED led_327 (.in(Addr_disp[11]));
  LED led_328 (.in(Addr_disp[10]));
  LED led_329 (.in(Addr_disp[9]));
  LED led_330 (.in(Addr_disp[8]));
  LED led_331 (.in(IV_disp[11]));
  LED led_332 (.in(IV_disp[10]));
  LED led_333 (.in(IV_disp[9]));
  LED led_334 (.in(IV_disp[8]));
  LED led_335 (.in(PC[7]));
  LED led_336 (.in(PC[6]));
  LED led_337 (.in(PC[5]));
  LED led_338 (.in(PC[4]));
  LED led_339 (.in(SP[7]));
  LED led_340 (.in(SP[6]));
  LED led_341 (.in(SP[5]));
  LED led_342 (.in(SP[4]));
  LED led_343 (.in(FP[7]));
  LED led_344 (.in(FP[6]));
  LED led_345 (.in(FP[5]));
  LED led_346 (.in(FP[4]));
  LED led_347 (.in(BP[7]));
  LED led_348 (.in(BP[6]));
  LED led_349 (.in(BP[5]));
  LED led_350 (.in(BP[4]));
  LED led_351 (.in(MAB_disp[7]));
  LED led_352 (.in(MAB_disp[6]));
  LED led_353 (.in(MAB_disp[5]));
  LED led_354 (.in(MAB_disp[4]));
  LED led_355 (.in(Addr_disp[7]));
  LED led_356 (.in(Addr_disp[6]));
  LED led_357 (.in(Addr_disp[5]));
  LED led_358 (.in(Addr_disp[4]));
  LED led_359 (.in(1'b0));
  LED led_360 (.in(1'b0));
  LED led_361 (.in(1'b0));
  LED led_362 (.in(1'b0));
  Multiplexer #(.Bits(8)) multiplexer_10 (.sel(IRQ), .in_0(IR_disp[7:0]), .in_1(in_3), .out(multiplexer_10_out));
  LED led_363 (.in(PC[3]));
  LED led_364 (.in(PC[2]));
  LED led_365 (.in(PC[1]));
  LED led_366 (.in(PC[0]));
  LED led_367 (.in(SP[3]));
  LED led_368 (.in(SP[2]));
  LED led_369 (.in(SP[1]));
  LED led_370 (.in(SP[0]));
  LED led_371 (.in(FP[3]));
  LED led_372 (.in(FP[2]));
  LED led_373 (.in(FP[1]));
  LED led_374 (.in(FP[0]));
  LED led_375 (.in(BP[3]));
  LED led_376 (.in(BP[2]));
  LED led_377 (.in(BP[1]));
  LED led_378 (.in(BP[0]));
  LED led_379 (.in(MAB_disp[3]));
  LED led_380 (.in(MAB_disp[2]));
  LED led_381 (.in(MAB_disp[1]));
  LED led_382 (.in(MAB_disp[0]));
  LED led_383 (.in(Addr_disp[3]));
  LED led_384 (.in(Addr_disp[2]));
  LED led_385 (.in(Addr_disp[1]));
  LED led_386 (.in(Addr_disp[0]));
  LED led_387 (.in(1'b0));
  LED led_388 (.in(1'b0));
  LED led_389 (.in(1'b0));
  LED led_390 (.in(1'b0));
  Register MDB (.nR(nr), .D_in(driver_1_out), .Clk(L6), .D_out(MDB_disp));
  Register IV_base (.nR(nr), .D_in(driver_1_out), .Clk(L8), .D_out(IV_disp[31:16]));
  Register_8bit int_number (.nR(nr), .D_in(multiplexer_10_out), .Clk(L7), .D_out(IV_disp[15:8]));
  LED led_391 (.in(microinstruction_decoder_1_nop));
  assign driver_1_out = E5 ? MDB_disp : 16'bz;  // Driver driver_9
  _1_to_8b_extender _1_to_8b_extender_3 (.in(IR_disp[7]), .out(_1_to_8b_extender_3_out));
  assign driver_1_out = E7 ? IV_disp[31:16] : 16'bz;  // Driver driver_10
  LED F1 (.in(sequencer_1_states_disp[15]));
  LED F_Int (.in(sequencer_1_states_disp[13]));
  LED F2 (.in(sequencer_1_states_disp[14]));
  single_byte_enabler SBE (
    .to_mem(driver_1_out), .fr_mem(SBE_fr_mem), .odd(Addr_disp[0]), .\byte (Byte), .fr_CPU(SBE_fr_cpu),
    .to_CPU(driver_16_out));
  assign driver_1_out = en[7] ? SBE_fr_mem : 16'bz;  // Driver driver_11
  Decoder #(.Selector_Bits(2)) decoder_2 (
    .sel(S10), .out_0(decoder_2_out_0), .out_1(decoder_2_out_1), .out_2(decoder_2_out_2),
    .out_3(decoder_2_out_3));
  LED MAB_Load (.in(sequencer_1_states_disp[10]));
  LED SP_4 (.in(sequencer_1_states_disp[3]));
  assign Addr_disp = decoder_2_out_0 ? {MP_mp_h, MP_mp_l} : 32'bz;  // Driver driver_12
  assign Addr_disp = decoder_2_out_1 ? MAB_disp : 32'bz;  // Driver driver_13
  assign Addr_disp = decoder_2_out_2 ? {_1_to_8b_extender_3_out[6:0], IR_disp[7:0], MDB_disp, 1'b0} : 32'bz;  // Driver driver_14
  assign Addr_disp = decoder_2_out_3 ? in_2 : 32'bz;  // Driver driver_15
  LED ALU (.in(sequencer_1_states_disp[12]));
  LED MOV (.in(sequencer_1_states_disp[11]));
  LED LD_ST_MP (.in(sequencer_1_states_disp[9]));
  LED LD_ST_Direct (.in(sequencer_1_states_disp[8]));
  LED LDi (.in(sequencer_1_states_disp[7]));
  LED Addr_Arithm (.in(sequencer_1_states_disp[6]));
  LED Push_PC (.in(sequencer_1_states_disp[2]));
  LED Misc (.in(sequencer_1_states_disp[0]));
  assign driver_16_out = en[8] ? SBE_fr_cpu : 16'bz;  // Driver driver_16
  LED MP_post (.in(sequencer_1_states_disp[5]));
  LED JMP (.in(sequencer_1_states_disp[4]));
  LED EINT (.in(sequencer_1_states_disp[1]));
  LED led_392 (.in(S0));
  LED led_393 (.in(S3[0]));
  LED led_394 (.in(S3[1]));
  LED led_395 (.in(S4));
  LED led_396 (.in(S5));
  LED led_397 (.in(S6));
  LED led_398 (.in(S7));
  LED led_399 (.in(S8));
  LED led_400 (.in(S9[0]));
  LED led_401 (.in(S9[1]));
  LED led_402 (.in(S10[0]));
  LED led_403 (.in(S10[1]));
  LED led_404 (.in(S11));
  LED led_405 (.in(S12));
  LED led_406 (.in(LA34[0]));
  LED led_407 (.in(LA34[1]));
  LED led_408 (.in(E1));
  LED led_409 (.in(E2));
  LED led_410 (.in(E3));
  LED led_411 (.in(E4));
  LED led_412 (.in(E5));
  LED led_413 (.in(E6));
  LED led_414 (.in(E7));
  LED led_415 (.in(en[7]));
  LED led_416 (.in(en[8]));
  LED u_L0 (.in(L0));
  LED u_L1 (.in(L1));
  LED led_417 (.in(L2));
  LED led_418 (.in(L3));
  LED led_419 (.in(L4));
  LED led_420 (.in(L5));
  LED led_421 (.in(L6));
  LED led_422 (.in(L7));
  LED led_423 (.in(L8));
  LED led_424 (.in(latch[9]));
  not not_13 (not_13_out, Addr_disp[14]);
  _8K_word_RAM _8k_word_ram_1 (
    .Address(Addr_disp[13:0]), .Single_byte(Byte), .CS(Addr_disp[14]), .WE(latch[9]), .OE(E6),
    .Data(driver_16_out));
  and and_6 (and_6_out, E6, not_13_out);
  ROM #(.AddrBits(7), .Bits(16)) ROM (.A(Addr_disp[7:1]), .sel(not_13_out), .D(ROM_d));
  assign driver_16_out = and_6_out ? ROM_d : 16'bz;  // Driver driver_17

  // Other names for the same wires on the sheet: en[6:0] = {E7, E6, E5, E4, E3, E2, E1}; T1 = en[7]; T2 = en[8];
  //   latch[8:0] = {L8, L7, L6, L5, L4, L3, L2, L1, L0}; W = latch[9];
  //   sel[15:0] = {LA34, S12, S11, S10, S9, S8, S7, S6, S5, S4, S3, S0}

  // Notes on the sheet:
  //   in_3: from interrupt controller
  //   Fetch EINT === int ack
  //   Interrupt controller mock
  //   Clock
  //   Const (8bit)
  //   MP + offset (32bit)
  //   Calculating core
  //   Data bus (16bit)
  //   Addressing Unit
  //   ECM-16/TTL cpu
  //   Registers display
  //   Flags (C,O,N,Z)
  //   MP value
  //   Z
  //   N
  //   O
  //   C
  //   MAB value
  //   Control
  //   interrupt #
  //   DMA address
  //   DMA
  //   Data/Instr bus (16bit)
  //   NOP
  //   States display
  //   Const + MDB
  //   Address bus (32bit)
  //   Control word
  //   S0
  //   S3_0
  //   S3_1
  //   S4
  //   S5
  //   S6
  //   S7
  //   S8
  //   S9_0
  //   S9_1
  //   S10_0
  //   S10_1
  //   S11
  //   S12
  //   LA3_0
  //   LA3_1
  //   E1
  //   E2
  //   E3
  //   E4
  //   E5
  //   E6
  //   E7
  //   T1
  //   T2
  //   L0
  //   L1
  //   L2
  //   L3
  //   L4
  //   L5
  //   L6
  //   L7
  //   L8
  //   W
  //   ROM is on addresses 0x0000 through 0x00FE
  //   RAM is on addresses 0x4000 through 0x7FFF
  //   Memory subsystem
  //   contents of ROM (hex, n*v repeats v):
  //   2000,c,2100,2,e130,f009,3249,1100,16,1000,24,2100,4,e130,f009
  //   ,3369,1e00,e,1000,1a,8caa,d498,8caa,10ff,ffe4,8d33,d5b8,8d33,100
  //   ,8eff,d6d8,8eff,100,8ff7,d7f8,8f77,100
endmodule
