// Digital circuit mask decoder.dig as structural Verilog
module mask_decoder (
  input  [2:0] in_1
);

  wire decoder_1_out_0, decoder_1_out_1, decoder_1_out_2, decoder_1_out_3, decoder_1_out_4, decoder_1_out_5,
       decoder_1_out_6, decoder_1_out_7, or_1_out, or_2_out, or_3_out, or_4_out, or_5_out, or_6_out,
       or_7_out, or_8_out, or_9_out, or_10_out, or_11_out;

  Decoder #(.Selector_Bits(3)) decoder_1 (
    .sel(in_1), .out_0(decoder_1_out_0), .out_1(decoder_1_out_1), .out_2(decoder_1_out_2),
    .out_3(decoder_1_out_3), .out_4(decoder_1_out_4), .out_5(decoder_1_out_5), .out_6(decoder_1_out_6),
    .out_7(decoder_1_out_7));
  or or_1 (or_1_out, decoder_1_out_0, decoder_1_out_1);
  or or_2 (or_2_out, decoder_1_out_2, decoder_1_out_3);
  or or_3 (or_3_out, decoder_1_out_4, decoder_1_out_5);
  or or_4 (or_4_out, decoder_1_out_6, decoder_1_out_7);
  or or_5 (or_5_out, or_1_out, or_2_out);
  or or_6 (or_6_out, or_3_out, or_4_out);
  or or_7 (or_7_out, or_5_out, or_3_out);
  or or_8 (or_8_out, or_1_out, decoder_1_out_2);
  or or_9 (or_9_out, or_5_out, decoder_1_out_4);
  or or_10 (or_10_out, or_7_out, decoder_1_out_6);
  or or_11 (or_11_out, or_5_out, or_6_out);
endmodule
