// Digital circuit 32K word RAM.dig as structural Verilog
module _32K_word_RAM (
  input  [15:0] Address,
  input  Single_byte,
  input  WE,
  input  OE,
  input  CS,
  output [15:0] Data
);

  wire and_1_out, and_2_out, b0, b1, b2, b3, bussplitter_1_d3, bussplitter_1_d4, bussplitter_1_d5,
       bussplitter_1_d6, bussplitter_1_d11, bussplitter_1_d12, bussplitter_1_d13, bussplitter_1_d14,
       bussplitter_2_d3, bussplitter_2_d4, bussplitter_2_d5, bussplitter_2_d6, bussplitter_2_d11,
       bussplitter_2_d12, bussplitter_2_d13, bussplitter_2_d14, bussplitter_3_d3, bussplitter_3_d4,
       bussplitter_3_d5, bussplitter_3_d6, bussplitter_3_d11, bussplitter_3_d12, bussplitter_3_d13,
       bussplitter_3_d14, bussplitter_4_d3, bussplitter_4_d4, bussplitter_4_d5, bussplitter_4_d6,
       bussplitter_4_d11, bussplitter_4_d12, bussplitter_4_d13, bussplitter_4_d14, H_2_p10, H_2_p11, H_2_p19,
       H_2_p20, H_3_p10, H_3_p11, H_3_p19, H_3_p20, H_4_p10, H_4_p11, H_4_p19, H_4_p20, H_p10, H_p11, H_p19,
       H_p20, L_2_p1, L_2_p12, L_2_p13, L_2_p14, L_2_p23, L_2_p24, L_3_p1, L_3_p12, L_3_p13, L_3_p14,
       L_3_p23, L_3_p24, L_4_p1, L_4_p12, L_4_p13, L_4_p14, L_4_p23, L_4_p24, L_p1, L_p12, L_p13, L_p14,
       L_p23, L_p24, nCE_HIGH, nCE_LOW, nOE, not_1_out, not_4_out, not_5_out, not_6_out, nWE, or_5_out,
       or_8_out, or_11_out, or_14_out;

  not not_1 (not_1_out, CS);
  not not_2 (nWE, WE);
  not not_3 (nOE, OE);
  not not_4 (not_4_out, Address[0]);
  not not_5 (not_5_out, Address[14]);
  not not_6 (not_6_out, Address[15]);
  and and_1 (and_1_out, Address[0], Single_byte);
  and and_2 (and_2_out, Single_byte, not_4_out);
  nand nand_1 (b0, not_5_out, not_6_out);
  nand nand_2 (b1, Address[14], not_6_out);
  nand nand_3 (b2, not_5_out, Address[15]);
  nand nand_4 (b3, Address[14], Address[15]);
  or or_1 (nCE_LOW, and_1_out, not_1_out);
  or or_2 (nCE_HIGH, and_2_out, not_1_out);
  // A623308A H: pin names not known; wires that end beside it: Address[13], Address[8], Address[7], Address[6], Address[5], Address[4], Address[3], Address[2], Address[1], H_p10, H_p11, 1'b1, nWE, Address[9], Address[10], Address[12], nOE, Address[11], H_p19, H_p20
  // A623308A L: pin names not known; wires that end beside it: L_p1, 1'b0, Address[13], Address[8], Address[7], Address[6], Address[5], Address[4], Address[3], Address[2], Address[1], L_p12, L_p13, L_p14, 1'b0, 1'b1, nWE, Address[9], Address[10], Address[12], nOE, Address[11], L_p23, L_p24
  or or_3 (H_p19, nCE_HIGH, b0);
  or or_4 (L_p23, nCE_LOW, b0);
  BusSplitter #(.Bits(16)) bussplitter_1 (
    .D(Data), .OE(or_5_out), .D0(L_p12), .D1(L_p13), .D2(L_p14), .D3(bussplitter_1_d3),
    .D4(bussplitter_1_d4), .D5(bussplitter_1_d5), .D6(bussplitter_1_d6), .D7(L_p24), .D8(H_p10), .D9(H_p11),
    .D10(L_p1), .D11(bussplitter_1_d11), .D12(bussplitter_1_d12), .D13(bussplitter_1_d13),
    .D14(bussplitter_1_d14), .D15(H_p20));
  or or_5 (or_5_out, nOE, b0);
  // A623308A H_2: pin names not known; wires that end beside it: Address[13], Address[8], Address[7], Address[6], Address[5], Address[4], Address[3], Address[2], Address[1], H_2_p10, H_2_p11, 1'b1, nWE, Address[9], Address[10], Address[12], nOE, Address[11], H_2_p19, H_2_p20
  // A623308A L_2: pin names not known; wires that end beside it: L_2_p1, 1'b0, Address[13], Address[8], Address[7], Address[6], Address[5], Address[4], Address[3], Address[2], Address[1], L_2_p12, L_2_p13, L_2_p14, 1'b0, 1'b1, nWE, Address[9], Address[10], Address[12], nOE, Address[11], L_2_p23, L_2_p24
  or or_6 (H_2_p19, nCE_HIGH, b1);
  or or_7 (L_2_p23, nCE_LOW, b1);
  BusSplitter #(.Bits(16)) bussplitter_2 (
    .D(Data), .OE(or_8_out), .D0(L_2_p12), .D1(L_2_p13), .D2(L_2_p14), .D3(bussplitter_2_d3),
    .D4(bussplitter_2_d4), .D5(bussplitter_2_d5), .D6(bussplitter_2_d6), .D7(L_2_p24), .D8(H_2_p10),
    .D9(H_2_p11), .D10(L_2_p1), .D11(bussplitter_2_d11), .D12(bussplitter_2_d12), .D13(bussplitter_2_d13),
    .D14(bussplitter_2_d14), .D15(H_2_p20));
  or or_8 (or_8_out, nOE, b1);
  // A623308A H_3: pin names not known; wires that end beside it: Address[13], Address[8], Address[7], Address[6], Address[5], Address[4], Address[3], Address[2], Address[1], H_3_p10, H_3_p11, 1'b1, nWE, Address[9], Address[10], Address[12], nOE, Address[11], H_3_p19, H_3_p20
  // A623308A L_3: pin names not known; wires that end beside it: L_3_p1, 1'b0, Address[13], Address[8], Address[7], Address[6], Address[5], Address[4], Address[3], Address[2], Address[1], L_3_p12, L_3_p13, L_3_p14, 1'b0, 1'b1, nWE, Address[9], Address[10], Address[12], nOE, Address[11], L_3_p23, L_3_p24
  or or_9 (H_3_p19, nCE_HIGH, b2);
  or or_10 (L_3_p23, nCE_LOW, b2);
  BusSplitter #(.Bits(16)) bussplitter_3 (
    .D(Data), .OE(or_11_out), .D0(L_3_p12), .D1(L_3_p13), .D2(L_3_p14), .D3(bussplitter_3_d3),
    .D4(bussplitter_3_d4), .D5(bussplitter_3_d5), .D6(bussplitter_3_d6), .D7(L_3_p24), .D8(H_3_p10),
    .D9(H_3_p11), .D10(L_3_p1), .D11(bussplitter_3_d11), .D12(bussplitter_3_d12), .D13(bussplitter_3_d13),
    .D14(bussplitter_3_d14), .D15(H_3_p20));
  or or_11 (or_11_out, nOE, b2);
  // A623308A H_4: pin names not known; wires that end beside it: Address[13], Address[8], Address[7], Address[6], Address[5], Address[4], Address[3], Address[2], Address[1], H_4_p10, H_4_p11, 1'b1, nWE, Address[9], Address[10], Address[12], nOE, Address[11], H_4_p19, H_4_p20
  // A623308A L_4: pin names not known; wires that end beside it: L_4_p1, 1'b0, Address[13], Address[8], Address[7], Address[6], Address[5], Address[4], Address[3], Address[2], Address[1], L_4_p12, L_4_p13, L_4_p14, 1'b0, 1'b1, nWE, Address[9], Address[10], Address[12], nOE, Address[11], L_4_p23, L_4_p24
  or or_12 (H_4_p19, nCE_HIGH, b3);
  or or_13 (L_4_p23, nCE_LOW, b3);
  BusSplitter #(.Bits(16)) bussplitter_4 (
    .D(Data), .OE(or_14_out), .D0(L_4_p12), .D1(L_4_p13), .D2(L_4_p14), .D3(bussplitter_4_d3),
    .D4(bussplitter_4_d4), .D5(bussplitter_4_d5), .D6(bussplitter_4_d6), .D7(L_4_p24), .D8(H_4_p10),
    .D9(H_4_p11), .D10(L_4_p1), .D11(bussplitter_4_d11), .D12(bussplitter_4_d12), .D13(bussplitter_4_d13),
    .D14(bussplitter_4_d14), .D15(H_4_p20));
  or or_14 (or_14_out, nOE, b3);

  // Notes on the sheet:
  //   Address: lowest 16 bits from address bus
  //   Data: I/O port for data
  //   Low byte
  //   High byte
  //   32K Words RAM
endmodule
