// Digital circuit 8K word RAM.dig as structural Verilog
module _8K_word_RAM (
  input  [13:0] Address,
  input  Single_byte,
  input  WE,
  input  OE,
  input  CS,
  output [15:0] Data
);

  wire and_1_out, and_2_out, bussplitter_1_d3, bussplitter_1_d4, bussplitter_1_d5, bussplitter_1_d6,
       bussplitter_1_d11, bussplitter_1_d12, bussplitter_1_d13, bussplitter_1_d14, H_p10, H_p11, H_p20, L_p1,
       L_p12, L_p13, L_p14, L_p24, nCE_HIGH, nCE_LOW, nOE, not_1_out, not_4_out, nWE;

  not not_1 (not_1_out, CS);
  not not_2 (nWE, WE);
  not not_3 (nOE, OE);
  not not_4 (not_4_out, Address[0]);
  and and_1 (and_1_out, Address[0], Single_byte);
  and and_2 (and_2_out, Single_byte, not_4_out);
  or or_1 (nCE_LOW, and_1_out, not_1_out);
  or or_2 (nCE_HIGH, and_2_out, not_1_out);
  // A623308A H: pin names not known; wires that end beside it: Address[13], Address[8], Address[7], Address[6], Address[5], Address[4], Address[3], Address[2], Address[1], H_p10, H_p11, 1'b1, nWE, Address[9], Address[10], Address[12], nOE, Address[11], nCE_HIGH, H_p20
  // A623308A L: pin names not known; wires that end beside it: L_p1, 1'b0, Address[13], Address[8], Address[7], Address[6], Address[5], Address[4], Address[3], Address[2], Address[1], L_p12, L_p13, L_p14, 1'b0, 1'b1, nWE, Address[9], Address[10], Address[12], nOE, Address[11], nCE_LOW, L_p24
  BusSplitter #(.Bits(16)) bussplitter_1 (
    .D(Data), .OE(nOE), .D0(L_p12), .D1(L_p13), .D2(L_p14), .D3(bussplitter_1_d3), .D4(bussplitter_1_d4),
    .D5(bussplitter_1_d5), .D6(bussplitter_1_d6), .D7(L_p24), .D8(H_p10), .D9(H_p11), .D10(L_p1),
    .D11(bussplitter_1_d11), .D12(bussplitter_1_d12), .D13(bussplitter_1_d13), .D14(bussplitter_1_d14),
    .D15(H_p20));

  // Notes on the sheet:
  //   Address: lowest 15 bits from address bus
  //   Data: I/O port for data
  //   Low byte
  //   High byte
  //   8K Words RAM
endmodule
