// Digital circuit Memory selector.dig as structural Verilog
module Memory_selector (
  input  [7:0] MSB,
  output Upper,
  output Lower,
  output Unmapped
);

  wire nand_1_out;

  nand nand_1 (nand_1_out, MSB[3], MSB[2], MSB[1], MSB[0], MSB[4], MSB[5], MSB[6], MSB[7]);
  nor nor_1 (Lower, MSB[3], MSB[2], MSB[1], MSB[0], MSB[4], MSB[5], MSB[6], MSB[7]);
  not not_1 (Upper, nand_1_out);
  nor nor_2 (Unmapped, Upper, Lower);

  // Notes on the sheet:
  //   MSB: Most significant byte of address
  //   Upper: Upper 16 MB of memory address space
  //   In this part all ROMs and I/O are mapped
  //   Lower: The installed RAM is here
  //   Unmapped: Intermediate address space,
  //   no actual device is available via these addresses
  //   Can be used only as virtual addresses when
  //   there is a MMU.
  //   If hit, should cause esception / interrupt triggering
  //   Memory Selector
endmodule
