// Digital circuit GPR_selector.dig as structural Verilog
module GPR_selector (
  input  [15:0] _0,
  input  [15:0] _1,
  input  [15:0] _2,
  input  [15:0] _3,
  input  [15:0] _4,
  input  [15:0] _5,
  input  [15:0] _6,
  input  [15:0] _7,
  input  [2:0] Addr,
  output [15:0] Out
);

  _74151 _74151_1 (
    .pin1(_3[0]), .pin2(_2[0]), .pin3(_1[0]), .pin4(_0[0]), .pin5(Out[0]), .pin7(1'b0), .pin8(1'b0),
    .pin9(Addr[2]), .pin10(Addr[1]), .pin11(Addr[0]), .pin12(_7[0]), .pin13(_6[0]), .pin14(_5[0]),
    .pin15(_4[0]), .pin16(1'b1));  // open: pin6
  _74151 _74151_2 (
    .pin1(_3[2]), .pin2(_2[2]), .pin3(_1[2]), .pin4(_0[2]), .pin5(Out[2]), .pin7(1'b0), .pin8(1'b0),
    .pin9(Addr[2]), .pin10(Addr[1]), .pin11(Addr[0]), .pin12(_7[2]), .pin13(_6[2]), .pin14(_5[2]),
    .pin15(_4[2]), .pin16(1'b1));  // open: pin6
  _74151 _74151_3 (
    .pin1(_3[4]), .pin2(_2[4]), .pin3(_1[4]), .pin4(_0[4]), .pin5(Out[4]), .pin7(1'b0), .pin8(1'b0),
    .pin9(Addr[2]), .pin10(Addr[1]), .pin11(Addr[0]), .pin12(_7[4]), .pin13(_6[4]), .pin14(_5[4]),
    .pin15(_4[4]), .pin16(1'b1));  // open: pin6
  _74151 _74151_4 (
    .pin1(_3[6]), .pin2(_2[6]), .pin3(_1[6]), .pin4(_0[6]), .pin5(Out[6]), .pin7(1'b0), .pin8(1'b0),
    .pin9(Addr[2]), .pin10(Addr[1]), .pin11(Addr[0]), .pin12(_7[6]), .pin13(_6[6]), .pin14(_5[6]),
    .pin15(_4[6]), .pin16(1'b1));  // open: pin6
  _74151 _74151_5 (
    .pin1(_3[8]), .pin2(_2[8]), .pin3(_1[8]), .pin4(_0[8]), .pin5(Out[8]), .pin7(1'b0), .pin8(1'b0),
    .pin9(Addr[2]), .pin10(Addr[1]), .pin11(Addr[0]), .pin12(_7[8]), .pin13(_6[8]), .pin14(_5[8]),
    .pin15(_4[8]), .pin16(1'b1));  // open: pin6
  _74151 _74151_6 (
    .pin1(_3[10]), .pin2(_2[10]), .pin3(_1[10]), .pin4(_0[10]), .pin5(Out[10]), .pin7(1'b0), .pin8(1'b0),
    .pin9(Addr[2]), .pin10(Addr[1]), .pin11(Addr[0]), .pin12(_7[10]), .pin13(_6[10]), .pin14(_5[10]),
    .pin15(_4[10]), .pin16(1'b1));  // open: pin6
  _74151 _74151_7 (
    .pin1(_3[12]), .pin2(_2[12]), .pin3(_1[12]), .pin4(_0[12]), .pin5(Out[12]), .pin7(1'b0), .pin8(1'b0),
    .pin9(Addr[2]), .pin10(Addr[1]), .pin11(Addr[0]), .pin12(_7[12]), .pin13(_6[12]), .pin14(_5[12]),
    .pin15(_4[12]), .pin16(1'b1));  // open: pin6
  _74151 _74151_8 (
    .pin1(_3[14]), .pin2(_2[14]), .pin3(_1[14]), .pin4(_0[14]), .pin5(Out[14]), .pin7(1'b0), .pin8(1'b0),
    .pin9(Addr[2]), .pin10(Addr[1]), .pin11(Addr[0]), .pin12(_7[14]), .pin13(_6[14]), .pin14(_5[14]),
    .pin15(_4[14]), .pin16(1'b1));  // open: pin6
  _74151 _74151_9 (
    .pin1(_3[1]), .pin2(_2[1]), .pin3(_1[1]), .pin4(_0[1]), .pin5(Out[1]), .pin7(1'b0), .pin8(1'b0),
    .pin9(Addr[2]), .pin10(Addr[1]), .pin11(Addr[0]), .pin12(_7[1]), .pin13(_6[1]), .pin14(_5[1]),
    .pin15(_4[1]), .pin16(1'b1));  // open: pin6
  _74151 _74151_10 (
    .pin1(_3[3]), .pin2(_2[3]), .pin3(_1[3]), .pin4(_0[3]), .pin5(Out[3]), .pin7(1'b0), .pin8(1'b0),
    .pin9(Addr[2]), .pin10(Addr[1]), .pin11(Addr[0]), .pin12(_7[3]), .pin13(_6[3]), .pin14(_5[3]),
    .pin15(_4[3]), .pin16(1'b1));  // open: pin6
  _74151 _74151_11 (
    .pin1(_3[5]), .pin2(_2[5]), .pin3(_1[5]), .pin4(_0[5]), .pin5(Out[5]), .pin7(1'b0), .pin8(1'b0),
    .pin9(Addr[2]), .pin10(Addr[1]), .pin11(Addr[0]), .pin12(_7[5]), .pin13(_6[5]), .pin14(_5[5]),
    .pin15(_4[5]), .pin16(1'b1));  // open: pin6
  _74151 _74151_12 (
    .pin1(_3[7]), .pin2(_2[7]), .pin3(_1[7]), .pin4(_0[7]), .pin5(Out[7]), .pin7(1'b0), .pin8(1'b0),
    .pin9(Addr[2]), .pin10(Addr[1]), .pin11(Addr[0]), .pin12(_7[7]), .pin13(_6[7]), .pin14(_5[7]),
    .pin15(_4[7]), .pin16(1'b1));  // open: pin6
  _74151 _74151_13 (
    .pin1(_3[9]), .pin2(_2[9]), .pin3(_1[9]), .pin4(_0[9]), .pin5(Out[9]), .pin7(1'b0), .pin8(1'b0),
    .pin9(Addr[2]), .pin10(Addr[1]), .pin11(Addr[0]), .pin12(_7[9]), .pin13(_6[9]), .pin14(_5[9]),
    .pin15(_4[9]), .pin16(1'b1));  // open: pin6
  _74151 _74151_14 (
    .pin1(_3[11]), .pin2(_2[11]), .pin3(_1[11]), .pin4(_0[11]), .pin5(Out[11]), .pin7(1'b0), .pin8(1'b0),
    .pin9(Addr[2]), .pin10(Addr[1]), .pin11(Addr[0]), .pin12(_7[11]), .pin13(_6[11]), .pin14(_5[11]),
    .pin15(_4[11]), .pin16(1'b1));  // open: pin6
  _74151 _74151_15 (
    .pin1(_3[13]), .pin2(_2[13]), .pin3(_1[13]), .pin4(_0[13]), .pin5(Out[13]), .pin7(1'b0), .pin8(1'b0),
    .pin9(Addr[2]), .pin10(Addr[1]), .pin11(Addr[0]), .pin12(_7[13]), .pin13(_6[13]), .pin14(_5[13]),
    .pin15(_4[13]), .pin16(1'b1));  // open: pin6
  _74151 _74151_16 (
    .pin1(_3[15]), .pin2(_2[15]), .pin3(_1[15]), .pin4(_0[15]), .pin5(Out[15]), .pin7(1'b0), .pin8(1'b0),
    .pin9(Addr[2]), .pin10(Addr[1]), .pin11(Addr[0]), .pin12(_7[15]), .pin13(_6[15]), .pin14(_5[15]),
    .pin15(_4[15]), .pin16(1'b1));  // open: pin6

  // Notes on the sheet:
  //   16-bit 8to1 mux
endmodule
