// Digital circuit Register file.dig as structural Verilog
module Register_file (
  input  nr,
  input  [15:0] D_in,
  input  Clk,
  input  L1,
  input  [2:0] Dest,
  input  [2:0] Src1,
  input  [2:0] Src2,
  input  Src1_eq_Dest,
  input  E1,
  input  Src2_ind,
  input  ALU_instr,
  input  nCMP,
  output [15:0] Src1_out,
  output [15:0] Src2_out,
  output [63:0] R0_3,
  output [63:0] R4_7,
  output [15:0] Src1_to_bus,
  output [7:0] LA1_i,
  output [7:0] EA1_i,
  output [7:0] S1_i,
  output [7:0] S2_i,
  output Reg_write
);

  wire _7400_1_pin3, _7400_2_pin6, _7400_2_pin11, _74238_1_pin4, _74238_3_pin7, _74238_3_pin9,
       _74238_3_pin10, _74238_3_pin11, _74238_3_pin12, _74238_3_pin13, _74238_3_pin14, _74238_3_pin15;
  wire [2:0] _74157_1_pin12;

  _7400 _7400_1 (
    .pin1(Clk), .pin2(L1), .pin3(_7400_1_pin3), .pin4(1'b0), .pin5(1'b0), .pin7(1'b0), .pin9(1'b0),
    .pin10(1'b0), .pin11(Reg_write), .pin12(_7400_1_pin3), .pin13(_7400_1_pin3), .pin14(1'b1));  // open: pin6, pin8
  _74157 _74157_1 (
    .pin1(Src1_eq_Dest), .pin2(Src1[0]), .pin3(Dest[0]), .pin4(_74157_1_pin12[0]), .pin5(Src1[2]),
    .pin6(Dest[2]), .pin7(_74157_1_pin12[2]), .pin8(1'b0), .pin10(1'b0), .pin11(1'b0),
    .pin12(_74157_1_pin12[1]), .pin13(Dest[1]), .pin14(Src1[1]), .pin15(1'b0), .pin16(1'b1));  // open: pin9
  _74238 _74238_1 (
    .pin1(_74157_1_pin12[0]), .pin2(_74157_1_pin12[1]), .pin3(_74157_1_pin12[2]), .pin4(_74238_1_pin4),
    .pin5(1'b0), .pin6(nr), .pin7(EA1_i[7]), .pin8(1'b0), .pin9(EA1_i[6]), .pin10(EA1_i[5]),
    .pin11(EA1_i[4]), .pin12(EA1_i[3]), .pin13(EA1_i[2]), .pin14(EA1_i[1]), .pin15(EA1_i[0]), .pin16(1'b1));
  _74238 _74238_2 (
    .pin1(Dest[0]), .pin2(Dest[1]), .pin3(Dest[2]), .pin4(nCMP), .pin5(1'b0), .pin6(L1), .pin7(LA1_i[7]),
    .pin8(1'b0), .pin9(LA1_i[6]), .pin10(LA1_i[5]), .pin11(LA1_i[4]), .pin12(LA1_i[3]), .pin13(LA1_i[2]),
    .pin14(LA1_i[1]), .pin15(LA1_i[0]), .pin16(1'b1));
  _74238 _74238_3 (
    .pin1(Dest[0]), .pin2(Dest[1]), .pin3(Dest[2]), .pin4(nCMP), .pin5(1'b0), .pin6(Reg_write),
    .pin7(_74238_3_pin7), .pin8(1'b0), .pin9(_74238_3_pin9), .pin10(_74238_3_pin10), .pin11(_74238_3_pin11),
    .pin12(_74238_3_pin12), .pin13(_74238_3_pin13), .pin14(_74238_3_pin14), .pin15(_74238_3_pin15),
    .pin16(1'b1));
  _7400 _7400_2 (
    .pin1(E1), .pin2(E1), .pin3(_74238_1_pin4), .pin4(Src2_ind), .pin5(Src2_ind), .pin6(_7400_2_pin6),
    .pin7(1'b0), .pin9(1'b0), .pin10(1'b0), .pin11(_7400_2_pin11), .pin12(_74238_1_pin4), .pin13(ALU_instr),
    .pin14(1'b1));  // open: pin8
  _74238 _74238_4 (
    .pin1(_74157_1_pin12[0]), .pin2(_74157_1_pin12[1]), .pin3(_74157_1_pin12[2]), .pin4(1'b0),
    .pin5(_7400_2_pin11), .pin6(nr), .pin7(S1_i[7]), .pin8(1'b0), .pin9(S1_i[6]), .pin10(S1_i[5]),
    .pin11(S1_i[4]), .pin12(S1_i[3]), .pin13(S1_i[2]), .pin14(S1_i[1]), .pin15(S1_i[0]), .pin16(1'b1));
  _74238 _74238_5 (
    .pin1(Src2[0]), .pin2(Src2[1]), .pin3(Src2[2]), .pin4(_7400_2_pin6), .pin5(_7400_2_pin11), .pin6(nr),
    .pin7(S2_i[7]), .pin8(1'b0), .pin9(S2_i[6]), .pin10(S2_i[5]), .pin11(S2_i[4]), .pin12(S2_i[3]),
    .pin13(S2_i[2]), .pin14(S2_i[1]), .pin15(S2_i[0]), .pin16(1'b1));
  Register GPR0 (.nR(nr), .D_in(D_in), .Clk(_74238_3_pin15), .D_out(R0_3[15:0]));
  Register GPR1 (.nR(nr), .D_in(D_in), .Clk(_74238_3_pin14), .D_out(R0_3[31:16]));
  Register GPR2 (.nR(nr), .D_in(D_in), .Clk(_74238_3_pin13), .D_out(R0_3[47:32]));
  Register GPR3 (.nR(nr), .D_in(D_in), .Clk(_74238_3_pin12), .D_out(R0_3[63:48]));
  Register GPR4 (.nR(nr), .D_in(D_in), .Clk(_74238_3_pin11), .D_out(R4_7[15:0]));
  Register GPR5 (.nR(nr), .D_in(D_in), .Clk(_74238_3_pin10), .D_out(R4_7[31:16]));
  Register GPR6 (.nR(nr), .D_in(D_in), .Clk(_74238_3_pin9), .D_out(R4_7[47:32]));
  Register GPR7 (.nR(nr), .D_in(D_in), .Clk(_74238_3_pin7), .D_out(R4_7[63:48]));
  LED led_1 (.in(LA1_i[0]));
  LED led_2 (.in(LA1_i[1]));
  LED led_3 (.in(LA1_i[2]));
  LED led_4 (.in(LA1_i[3]));
  LED led_5 (.in(LA1_i[4]));
  LED led_6 (.in(LA1_i[5]));
  LED led_7 (.in(LA1_i[6]));
  LED led_8 (.in(LA1_i[7]));
  LED led_9 (.in(R0_3[15]));
  LED led_10 (.in(R0_3[14]));
  LED led_11 (.in(R0_3[13]));
  LED led_12 (.in(R0_3[12]));
  LED led_13 (.in(R0_3[31]));
  LED led_14 (.in(R0_3[30]));
  LED led_15 (.in(R0_3[29]));
  LED led_16 (.in(R0_3[28]));
  LED led_17 (.in(R0_3[47]));
  LED led_18 (.in(R0_3[46]));
  LED led_19 (.in(R0_3[45]));
  LED led_20 (.in(R0_3[44]));
  LED led_21 (.in(R0_3[63]));
  LED led_22 (.in(R0_3[62]));
  LED led_23 (.in(R0_3[61]));
  LED led_24 (.in(R0_3[60]));
  LED led_25 (.in(R4_7[15]));
  LED led_26 (.in(R4_7[14]));
  LED led_27 (.in(R4_7[13]));
  LED led_28 (.in(R4_7[12]));
  LED led_29 (.in(R4_7[31]));
  LED led_30 (.in(R4_7[30]));
  LED led_31 (.in(R4_7[29]));
  LED led_32 (.in(R4_7[28]));
  LED led_33 (.in(R4_7[47]));
  LED led_34 (.in(R4_7[46]));
  LED led_35 (.in(R4_7[45]));
  LED led_36 (.in(R4_7[44]));
  LED led_37 (.in(R4_7[63]));
  LED led_38 (.in(R4_7[62]));
  LED led_39 (.in(R4_7[61]));
  LED led_40 (.in(R4_7[60]));
  LED led_41 (.in(R0_3[11]));
  LED led_42 (.in(R0_3[10]));
  LED led_43 (.in(R0_3[9]));
  LED led_44 (.in(R0_3[8]));
  LED led_45 (.in(R0_3[27]));
  LED led_46 (.in(R0_3[26]));
  LED led_47 (.in(R0_3[25]));
  LED led_48 (.in(R0_3[24]));
  LED led_49 (.in(R0_3[43]));
  LED led_50 (.in(R0_3[42]));
  LED led_51 (.in(R0_3[41]));
  LED led_52 (.in(R0_3[40]));
  LED led_53 (.in(R0_3[59]));
  LED led_54 (.in(R0_3[58]));
  LED led_55 (.in(R0_3[57]));
  LED led_56 (.in(R0_3[56]));
  LED led_57 (.in(R4_7[11]));
  LED led_58 (.in(R4_7[10]));
  LED led_59 (.in(R4_7[9]));
  LED led_60 (.in(R4_7[8]));
  LED led_61 (.in(R4_7[27]));
  LED led_62 (.in(R4_7[26]));
  LED led_63 (.in(R4_7[25]));
  LED led_64 (.in(R4_7[24]));
  LED led_65 (.in(R4_7[43]));
  LED led_66 (.in(R4_7[42]));
  LED led_67 (.in(R4_7[41]));
  LED led_68 (.in(R4_7[40]));
  LED led_69 (.in(R4_7[59]));
  LED led_70 (.in(R4_7[58]));
  LED led_71 (.in(R4_7[57]));
  LED led_72 (.in(R4_7[56]));
  LED led_73 (.in(R0_3[7]));
  LED led_74 (.in(R0_3[6]));
  LED led_75 (.in(R0_3[5]));
  LED led_76 (.in(R0_3[4]));
  LED led_77 (.in(R0_3[23]));
  LED led_78 (.in(R0_3[22]));
  LED led_79 (.in(R0_3[21]));
  LED led_80 (.in(R0_3[20]));
  LED led_81 (.in(R0_3[39]));
  LED led_82 (.in(R0_3[38]));
  LED led_83 (.in(R0_3[37]));
  LED led_84 (.in(R0_3[36]));
  LED led_85 (.in(R0_3[55]));
  LED led_86 (.in(R0_3[54]));
  LED led_87 (.in(R0_3[53]));
  LED led_88 (.in(R0_3[52]));
  LED led_89 (.in(R4_7[7]));
  LED led_90 (.in(R4_7[6]));
  LED led_91 (.in(R4_7[5]));
  LED led_92 (.in(R4_7[4]));
  LED led_93 (.in(R4_7[23]));
  LED led_94 (.in(R4_7[22]));
  LED led_95 (.in(R4_7[21]));
  LED led_96 (.in(R4_7[20]));
  LED led_97 (.in(R4_7[39]));
  LED led_98 (.in(R4_7[38]));
  LED led_99 (.in(R4_7[37]));
  LED led_100 (.in(R4_7[36]));
  LED led_101 (.in(R4_7[55]));
  LED led_102 (.in(R4_7[54]));
  LED led_103 (.in(R4_7[53]));
  LED led_104 (.in(R4_7[52]));
  LED led_105 (.in(R0_3[3]));
  LED led_106 (.in(R0_3[2]));
  LED led_107 (.in(R0_3[1]));
  LED led_108 (.in(R0_3[0]));
  LED led_109 (.in(R0_3[19]));
  LED led_110 (.in(R0_3[18]));
  LED led_111 (.in(R0_3[17]));
  LED led_112 (.in(R0_3[16]));
  LED led_113 (.in(R0_3[35]));
  LED led_114 (.in(R0_3[34]));
  LED led_115 (.in(R0_3[33]));
  LED led_116 (.in(R0_3[32]));
  LED led_117 (.in(R0_3[51]));
  LED led_118 (.in(R0_3[50]));
  LED led_119 (.in(R0_3[49]));
  LED led_120 (.in(R0_3[48]));
  LED led_121 (.in(R4_7[3]));
  LED led_122 (.in(R4_7[2]));
  LED led_123 (.in(R4_7[1]));
  LED led_124 (.in(R4_7[0]));
  LED led_125 (.in(R4_7[19]));
  LED led_126 (.in(R4_7[18]));
  LED led_127 (.in(R4_7[17]));
  LED led_128 (.in(R4_7[16]));
  LED led_129 (.in(R4_7[35]));
  LED led_130 (.in(R4_7[34]));
  LED led_131 (.in(R4_7[33]));
  LED led_132 (.in(R4_7[32]));
  LED led_133 (.in(R4_7[51]));
  LED led_134 (.in(R4_7[50]));
  LED led_135 (.in(R4_7[49]));
  LED led_136 (.in(R4_7[48]));
  LED led_137 (.in(S1_i[0]));
  LED led_138 (.in(S1_i[1]));
  LED led_139 (.in(S1_i[2]));
  LED led_140 (.in(S1_i[3]));
  LED led_141 (.in(S1_i[4]));
  LED led_142 (.in(S1_i[5]));
  LED led_143 (.in(S1_i[6]));
  LED led_144 (.in(S1_i[7]));
  LED led_145 (.in(S2_i[0]));
  LED led_146 (.in(S2_i[1]));
  LED led_147 (.in(S2_i[2]));
  LED led_148 (.in(S2_i[3]));
  LED led_149 (.in(S2_i[4]));
  LED led_150 (.in(S2_i[5]));
  LED led_151 (.in(S2_i[6]));
  LED led_152 (.in(S2_i[7]));
  GPR_selector Src1_sel (
    ._0(R0_3[15:0]), ._1(R0_3[31:16]), ._2(R0_3[47:32]), ._3(R0_3[63:48]), ._4(R4_7[15:0]), ._5(R4_7[31:16]),
    ._6(R4_7[47:32]), ._7(R4_7[63:48]), .Addr(_74157_1_pin12), .Out(Src1_out));
  GPR_selector Src2_sel (
    ._0(R0_3[15:0]), ._1(R0_3[31:16]), ._2(R0_3[47:32]), ._3(R0_3[63:48]), ._4(R4_7[15:0]), ._5(R4_7[31:16]),
    ._6(R4_7[47:32]), ._7(R4_7[63:48]), .Addr(Src2), .Out(Src2_out));
  LED led_153 (.in(EA1_i[0]));
  LED led_154 (.in(EA1_i[1]));
  LED led_155 (.in(EA1_i[2]));
  LED led_156 (.in(EA1_i[3]));
  LED led_157 (.in(EA1_i[4]));
  LED led_158 (.in(EA1_i[5]));
  LED led_159 (.in(EA1_i[6]));
  LED led_160 (.in(EA1_i[7]));
  Bus_buffer E1_buffer (.nEnable(_74238_1_pin4), .Data_in(Src1_out), .Data_out(Src1_to_bus));

  // Other names for the same wires on the sheet: Src1_to_bus_t[7:0] = EA1_i; Dest_t[7:0] = LA1_i; Src1_t[7:0] = S1_i;
  //   Src2_t[7:0] = S2_i

  // Notes on the sheet:
  //   L1: Latch data to register
  //   Src1_eq_Dest: Instruction which uses A as source as well as destination,
  //   All instructions with immediate 8-bit values
  //   E1: Enable Src1 to Bus
  //   Src2_ind: For the purposes of display
  //   ALU_instr: For the purposes of display
  //   nCMP: Compare instr from ALU decoder, prevents write to register
  //   LA1_i: address of GPR to be written to
  //   EA1_i: Address of GPR to be enabled to bus
  //   S1_i: address of Src1
  //   S2_i: Address of Src2
  //   ~E1
endmodule
