// Digital circuit Register file_gates_muxes.dig as structural Verilog
module Register_file_gates_muxes (
  input  nr,
  input  [15:0] D_in,
  input  L1,
  input  [2:0] Dest,
  input  [2:0] Src1,
  input  [2:0] Src2,
  input  S1__eq_D,
  input  nCMP,
  output [15:0] Src1_out,
  output [15:0] Src2_out,
  output [63:0] R0_3,
  output [63:0] R4_7,
  output [15:0] Src1_to_bus
);

  wire and_1_out, and_2_out, demultiplexer_1_out_0, demultiplexer_1_out_1, demultiplexer_1_out_2,
       demultiplexer_1_out_3, demultiplexer_1_out_4, demultiplexer_1_out_5, demultiplexer_1_out_6,
       demultiplexer_1_out_7, not_1_out, not_2_out, not_3_out, not_4_out, not_5_out;
  wire [2:0] multiplexer_1_out;

  not not_1 (not_1_out, L1);
  not not_2 (not_2_out, nr);
  not not_3 (not_3_out, not_1_out);
  not not_4 (not_4_out, not_3_out);
  not not_5 (not_5_out, nCMP);
  and and_1 (and_1_out, not_4_out, L1);
  and and_2 (and_2_out, not_5_out, and_1_out);
  Demultiplexer #(.Selector_Bits(3)) demultiplexer_1 (
    .sel(Dest), .in(and_2_out), .out_0(demultiplexer_1_out_0), .out_1(demultiplexer_1_out_1),
    .out_2(demultiplexer_1_out_2), .out_3(demultiplexer_1_out_3), .out_4(demultiplexer_1_out_4),
    .out_5(demultiplexer_1_out_5), .out_6(demultiplexer_1_out_6), .out_7(demultiplexer_1_out_7));
  Multiplexer #(.Bits(3)) multiplexer_1 (.sel(S1__eq_D), .in_0(Dest), .in_1(Src1), .out(multiplexer_1_out));
  D_FF_AS #(.Bits(16)) r0 (
    .Set(1'b0), .D(D_in), .C(demultiplexer_1_out_0), .Clr(not_2_out), .Q(R0_3[15:0]));  // open: nQ
  D_FF_AS #(.Bits(16)) r1 (
    .Set(1'b0), .D(D_in), .C(demultiplexer_1_out_1), .Clr(not_2_out), .Q(R0_3[31:16]));  // open: nQ
  D_FF_AS #(.Bits(16)) r2 (
    .Set(1'b0), .D(D_in), .C(demultiplexer_1_out_2), .Clr(not_2_out), .Q(R0_3[47:32]));  // open: nQ
  D_FF_AS #(.Bits(16)) r3 (
    .Set(1'b0), .D(D_in), .C(demultiplexer_1_out_3), .Clr(not_2_out), .Q(R0_3[63:48]));  // open: nQ
  D_FF_AS #(.Bits(16)) r4 (
    .Set(1'b0), .D(D_in), .C(demultiplexer_1_out_4), .Clr(not_2_out), .Q(R4_7[15:0]));  // open: nQ
  D_FF_AS #(.Bits(16)) r5 (
    .Set(1'b0), .D(D_in), .C(demultiplexer_1_out_5), .Clr(not_2_out), .Q(R4_7[31:16]));  // open: nQ
  D_FF_AS #(.Bits(16)) r6 (
    .Set(1'b0), .D(D_in), .C(demultiplexer_1_out_6), .Clr(not_2_out), .Q(R4_7[47:32]));  // open: nQ
  D_FF_AS #(.Bits(16)) r7 (
    .Set(1'b0), .D(D_in), .C(demultiplexer_1_out_7), .Clr(not_2_out), .Q(R4_7[63:48]));  // open: nQ
  Multiplexer #(.Bits(16), .Selector_Bits(3)) multiplexer_2 (
    .sel(multiplexer_1_out), .in_0(R0_3[15:0]), .in_1(R0_3[31:16]), .in_2(R0_3[47:32]), .in_3(R0_3[63:48]),
    .in_4(R4_7[15:0]), .in_5(R4_7[31:16]), .in_6(R4_7[47:32]), .in_7(R4_7[63:48]), .out(Src1_out));
  Multiplexer #(.Selector_Bits(3), .Bits(16)) multiplexer_3 (
    .sel(Src2), .in_0(R0_3[15:0]), .in_1(R0_3[31:16]), .in_2(R0_3[47:32]), .in_3(R0_3[63:48]),
    .in_4(R4_7[15:0]), .in_5(R4_7[31:16]), .in_6(R4_7[47:32]), .in_7(R4_7[63:48]), .out(Src2_out));

  assign Src1_to_bus = Src1_out;

  // Notes on the sheet:
  //   L1: Latch data to register
  //   S1__eq_D: For all instructions except non-const ALU and MOVs
  //    should be 0
  //   nCMP: Compare instr from ALU decoder, prevents write to register
endmodule
