// Digital circuit Register file_no_display.dig as structural Verilog
module Register_file_no_display (
  input  nr,
  input  [15:0] D_in,
  input  L1,
  input  [2:0] Dest,
  input  [2:0] Src1,
  input  [2:0] Src2,
  input  S1__eq_D,
  input  nCMP,
  output [15:0] Src1_out,
  output [15:0] Src2_out,
  output [63:0] R0_3,
  output [63:0] R4_7,
  output [15:0] Src1_to_bus
);

  wire _74238_1_pin7, _74238_1_pin9, _74238_1_pin10, _74238_1_pin11, _74238_1_pin12, _74238_1_pin13,
       _74238_1_pin14, _74238_1_pin15, and_1_out, not_1_out, not_2_out, not_3_out;
  wire [2:0] _74157_1_pin12;

  _74157 _74157_1 (
    .pin1(S1__eq_D), .pin2(Dest[0]), .pin3(Src1[0]), .pin4(_74157_1_pin12[0]), .pin5(Dest[2]),
    .pin6(Src1[2]), .pin7(_74157_1_pin12[2]), .pin8(1'b0), .pin10(1'b0), .pin11(1'b0),
    .pin12(_74157_1_pin12[1]), .pin13(Src1[1]), .pin14(Dest[1]), .pin15(1'b0), .pin16(1'b1));  // open: pin9
  not not_1 (not_1_out, L1);
  not not_2 (not_2_out, not_1_out);
  not not_3 (not_3_out, not_2_out);
  and and_1 (and_1_out, not_3_out, L1);
  _74238 _74238_1 (
    .pin1(Dest[0]), .pin2(Dest[1]), .pin3(Dest[2]), .pin4(nCMP), .pin5(1'b0), .pin6(and_1_out),
    .pin7(_74238_1_pin7), .pin8(1'b0), .pin9(_74238_1_pin9), .pin10(_74238_1_pin10), .pin11(_74238_1_pin11),
    .pin12(_74238_1_pin12), .pin13(_74238_1_pin13), .pin14(_74238_1_pin14), .pin15(_74238_1_pin15),
    .pin16(1'b1));
  Register GPR0 (.nR(nr), .D_in(D_in), .Clk(_74238_1_pin15), .D_out(R0_3[15:0]));
  Register GPR1 (.nR(nr), .D_in(D_in), .Clk(_74238_1_pin14), .D_out(R0_3[31:16]));
  Register GPR2 (.nR(nr), .D_in(D_in), .Clk(_74238_1_pin13), .D_out(R0_3[47:32]));
  Register GPR3 (.nR(nr), .D_in(D_in), .Clk(_74238_1_pin12), .D_out(R0_3[63:48]));
  Register GPR4 (.nR(nr), .D_in(D_in), .Clk(_74238_1_pin11), .D_out(R4_7[15:0]));
  Register GPR5 (.nR(nr), .D_in(D_in), .Clk(_74238_1_pin10), .D_out(R4_7[31:16]));
  Register GPR6 (.nR(nr), .D_in(D_in), .Clk(_74238_1_pin9), .D_out(R4_7[47:32]));
  Register GPR7 (.nR(nr), .D_in(D_in), .Clk(_74238_1_pin7), .D_out(R4_7[63:48]));
  GPR_selector Src1_sel (
    ._0(R0_3[15:0]), ._1(R0_3[31:16]), ._2(R0_3[47:32]), ._3(R0_3[63:48]), ._4(R4_7[15:0]), ._5(R4_7[31:16]),
    ._6(R4_7[47:32]), ._7(R4_7[63:48]), .Addr(_74157_1_pin12), .Out(Src1_out));
  GPR_selector Src2_sel (
    ._0(R0_3[15:0]), ._1(R0_3[31:16]), ._2(R0_3[47:32]), ._3(R0_3[63:48]), ._4(R4_7[15:0]), ._5(R4_7[31:16]),
    ._6(R4_7[47:32]), ._7(R4_7[63:48]), .Addr(Src2), .Out(Src2_out));

  assign Src1_to_bus = Src1_out;

  // Notes on the sheet:
  //   L1: Latch data to register
  //   S1__eq_D: For all instructions except non-const ALU and MOVs
  //    should be 0
  //   nCMP: Compare instr from ALU decoder, prevents write to register
endmodule
