// Digital circuit indicator.dig as structural Verilog
module indicator (
  input  L1,
  input  [2:0] Dest,
  input  [2:0] Src1,
  input  [2:0] Src2,
  input  Src1_eq_Dest,
  input  E1,
  input  Src2_ind,
  input  ALU_instr,
  input  nCMP,
  input  nr
);

  wire _7400_1_pin6, _7400_1_pin11, _74238_1_pin4;
  wire [2:0] _74157_1_pin7;
  wire [7:0] Dest_t, Src1_t, Src1_to_bus, Src2_t;

  _74157 _74157_1 (
    .pin1(Src1_eq_Dest), .pin2(Src1[0]), .pin3(Dest[0]), .pin4(_74157_1_pin7[0]), .pin5(Src1[2]),
    .pin6(Dest[2]), .pin7(_74157_1_pin7[2]), .pin8(1'b0), .pin10(1'b0), .pin11(1'b0),
    .pin12(_74157_1_pin7[1]), .pin13(Dest[1]), .pin14(Src1[1]), .pin15(1'b0), .pin16(1'b1));  // open: pin9
  _74238 _74238_1 (
    .pin1(_74157_1_pin7[0]), .pin2(_74157_1_pin7[1]), .pin3(_74157_1_pin7[2]), .pin4(_74238_1_pin4),
    .pin5(1'b0), .pin6(nr), .pin7(Src1_to_bus[7]), .pin8(1'b0), .pin9(Src1_to_bus[6]),
    .pin10(Src1_to_bus[5]), .pin11(Src1_to_bus[4]), .pin12(Src1_to_bus[3]), .pin13(Src1_to_bus[2]),
    .pin14(Src1_to_bus[1]), .pin15(Src1_to_bus[0]), .pin16(1'b1));
  _74238 _74238_2 (
    .pin1(Dest[0]), .pin2(Dest[1]), .pin3(Dest[2]), .pin4(nCMP), .pin5(1'b0), .pin6(L1), .pin7(Dest_t[7]),
    .pin8(1'b0), .pin9(Dest_t[6]), .pin10(Dest_t[5]), .pin11(Dest_t[4]), .pin12(Dest_t[3]),
    .pin13(Dest_t[2]), .pin14(Dest_t[1]), .pin15(Dest_t[0]), .pin16(1'b1));
  _7400 _7400_1 (
    .pin1(E1), .pin2(E1), .pin3(_74238_1_pin4), .pin4(Src2_ind), .pin5(Src2_ind), .pin6(_7400_1_pin6),
    .pin7(1'b0), .pin9(1'b0), .pin10(1'b0), .pin11(_7400_1_pin11), .pin12(_74238_1_pin4), .pin13(ALU_instr),
    .pin14(1'b1));  // open: pin8
  _74238 _74238_3 (
    .pin1(_74157_1_pin7[0]), .pin2(_74157_1_pin7[1]), .pin3(_74157_1_pin7[2]), .pin4(1'b0),
    .pin5(_7400_1_pin11), .pin6(nr), .pin7(Src1_t[7]), .pin8(1'b0), .pin9(Src1_t[6]), .pin10(Src1_t[5]),
    .pin11(Src1_t[4]), .pin12(Src1_t[3]), .pin13(Src1_t[2]), .pin14(Src1_t[1]), .pin15(Src1_t[0]),
    .pin16(1'b1));
  _74238 _74238_4 (
    .pin1(Src2[0]), .pin2(Src2[1]), .pin3(Src2[2]), .pin4(_7400_1_pin6), .pin5(_7400_1_pin11), .pin6(nr),
    .pin7(Src2_t[7]), .pin8(1'b0), .pin9(Src2_t[6]), .pin10(Src2_t[5]), .pin11(Src2_t[4]), .pin12(Src2_t[3]),
    .pin13(Src2_t[2]), .pin14(Src2_t[1]), .pin15(Src2_t[0]), .pin16(1'b1));
  LED led_1 (.in(Dest_t[0]));
  LED led_2 (.in(Dest_t[1]));
  LED led_3 (.in(Dest_t[2]));
  LED led_4 (.in(Dest_t[3]));
  LED led_5 (.in(Dest_t[4]));
  LED led_6 (.in(Dest_t[5]));
  LED led_7 (.in(Dest_t[6]));
  LED led_8 (.in(Dest_t[7]));
  LED led_9 (.in(Src1_t[0]));
  LED led_10 (.in(Src2_t[0]));
  LED led_11 (.in(Src1_t[1]));
  LED led_12 (.in(Src2_t[1]));
  LED led_13 (.in(Src1_t[2]));
  LED led_14 (.in(Src2_t[2]));
  LED led_15 (.in(Src1_t[3]));
  LED led_16 (.in(Src2_t[3]));
  LED led_17 (.in(Src1_t[4]));
  LED led_18 (.in(Src2_t[4]));
  LED led_19 (.in(Src1_t[5]));
  LED led_20 (.in(Src2_t[5]));
  LED led_21 (.in(Src1_t[6]));
  LED led_22 (.in(Src2_t[6]));
  LED led_23 (.in(Src1_t[7]));
  LED led_24 (.in(Src2_t[7]));
  LED led_25 (.in(Src1_to_bus[0]));
  LED led_26 (.in(Src1_to_bus[1]));
  LED led_27 (.in(Src1_to_bus[2]));
  LED led_28 (.in(Src1_to_bus[3]));
  LED led_29 (.in(Src1_to_bus[4]));
  LED led_30 (.in(Src1_to_bus[5]));
  LED led_31 (.in(Src1_to_bus[6]));
  LED led_32 (.in(Src1_to_bus[7]));

  // Notes on the sheet:
  //   L1: Latch data to register
  //   Src1_eq_Dest: Instruction which uses A as source as well as destination,
  //   All instructions with immediate 8-bit values
  //   E1: Enable Src1 to Bus
  //   Src2_ind: For the purposes of display
  //   ALU_instr: For the purposes of display
  //   nCMP: Compare instr from ALU decoder, prevents write to register
  //   ~E1
endmodule
