// Digital circuit T B sel.dig as structural Verilog
module T_B_sel (
  input  [7:0] in,
  input  Flip,
  output top,
  output bottom
);

  wire and_1_out, nor_1_out;

  and and_1 (and_1_out, in[0], in[1], in[2], in[3], in[4], in[5], in[6], in[7]);
  nor nor_1 (nor_1_out, in[0], in[1], in[2], in[3], in[4], in[5], in[6], in[7]);
  xor xor_1 (top, Flip, and_1_out);
  xor xor_2 (bottom, Flip, nor_1_out);

  // Notes on the sheet:
  //   Flip: flips the ranges, used at startup for accessing ROM from 
  //   address 0x00000000
endmodule
